// Digital circuit C-SAFE.dig as structural Verilog
module C_SAFE (
  input  [7:0] in_1,
  input  FlagN,
  input  FlagV,
  input  FlagZ,
  input  FlagC,
  input  clk
);

  wire and_1_out, and_2_out, and_3_out, and_4_out, Clock2, Load_out, NotClock, or_1_out, or_2_out, uCJMP,
       uJMP, uJMPOP, uJSR, uNJMP, uPCINC, uRTS, uVJMP, uZJMP;
  wire [1:0] NEXTMUX;
  wire [7:0] IR;
  wire [15:0] add_1_s, add_2_s, CAR, CAR_Plus_Latch_q, CARstore, Next, PC, PC_plus_q, uControlLines,
       uNextAddr;

  Seven_Seg_Hex seven_seg_hex_1 (.d(CAR[15:12]), .dp(1'b0));
  Seven_Seg_Hex seven_seg_hex_2 (.d(uNextAddr[15:12]), .dp(1'b0));
  Seven_Seg_Hex seven_seg_hex_3 (.d(PC[15:12]), .dp(1'b0));
  Seven_Seg_Hex seven_seg_hex_4 (.d(CAR[7:4]), .dp(1'b0));
  Seven_Seg_Hex seven_seg_hex_5 (.d(CAR[11:8]), .dp(1'b0));
  Seven_Seg_Hex seven_seg_hex_6 (.d(uNextAddr[7:4]), .dp(1'b0));
  Seven_Seg_Hex seven_seg_hex_7 (.d(uNextAddr[11:8]), .dp(1'b0));
  Seven_Seg_Hex seven_seg_hex_8 (.d(PC[7:4]), .dp(1'b0));
  Seven_Seg_Hex seven_seg_hex_9 (.d(PC[11:8]), .dp(1'b0));
  LED led_1 (.in(NEXTMUX[1]));
  Seven_Seg_Hex seven_seg_hex_10 (.d(CAR[3:0]), .dp(1'b0));
  Seven_Seg_Hex seven_seg_hex_11 (.d(uNextAddr[3:0]), .dp(1'b0));
  Seven_Seg_Hex seven_seg_hex_12 (.d(PC[3:0]), .dp(1'b0));
  LED led_2 (.in(NEXTMUX[0]));
  Counter counter_1 (.en(1'b1), .C(clk), .clr(1'b0), .out(Clock2));  // open: ovf
  Seven_Seg_Hex seven_seg_hex_13 (.d(CARstore[11:8]), .dp(1'b0));
  Seven_Seg_Hex seven_seg_hex_14 (.d(CARstore[15:12]), .dp(1'b0));
  Seven_Seg_Hex seven_seg_hex_15 (.d(Next[11:8]), .dp(1'b0));
  Seven_Seg_Hex seven_seg_hex_16 (.d(Next[15:12]), .dp(1'b0));
  Seven_Seg_Hex seven_seg_hex_17 (.d(CARstore[3:0]), .dp(1'b0));
  Seven_Seg_Hex seven_seg_hex_18 (.d(CARstore[7:4]), .dp(1'b0));
  Seven_Seg_Hex seven_seg_hex_19 (.d(Next[3:0]), .dp(1'b0));
  Seven_Seg_Hex seven_seg_hex_20 (.d(Next[7:4]), .dp(1'b0));
  Seven_Seg_Hex seven_seg_hex_21 (.d(IR[3:0]), .dp(1'b0));
  Seven_Seg_Hex seven_seg_hex_22 (.d(IR[7:4]), .dp(1'b0));
  not not_1 (NotClock, clk);
  ROM #(.AddrBits(16), .Bits(41)) Microcode (
    .A(CAR), .sel(1'b1),
    .D({uControlLines, uCJMP, uZJMP, uVJMP, uNJMP, uPCINC, uJMPOP, uRTS, uJSR, uJMP, uNextAddr}));
  Register #(.Bits(16)) u_PC (.D(PC_plus_q), .C(clk), .en(uPCINC), .Q(PC));
  Register #(.Bits(16)) PC_plus (.D(add_1_s), .C(NotClock), .en(1'b1), .Q(PC_plus_q));
  Add #(.Bits(16)) add_1 (.a(PC), .b(16'h1), .c_i(1'b0), .s(add_1_s));  // open: c_o
  Register #(.Bits(16)) u_CAR (.D(Next), .C(clk), .en(1'b1), .Q(CAR));
  Add #(.Bits(16)) add_2 (.a(CAR), .b(16'h1), .c_i(1'b0), .s(add_2_s));  // open: c_o
  Register #(.Bits(8)) u_IR (.D(in_1), .C(Load_out), .en(1'b1), .Q(IR));
  Button Load (.out(Load_out));
  or or_1 (or_1_out, uJMP, uJSR);
  and and_1 (and_1_out, uNJMP, FlagN);
  and and_2 (and_2_out, uVJMP, FlagV);
  and and_3 (and_3_out, uZJMP, FlagZ);
  and and_4 (and_4_out, uCJMP, FlagC);
  Register #(.Bits(16)) CAR_Plus_Latch (.D(add_2_s), .C(NotClock), .en(1'b1), .Q(CAR_Plus_Latch_q));
  Register #(.Bits(16)) u_CARstore (.D(add_2_s), .C(NotClock), .en(uJSR), .Q(CARstore));
  or or_2 (or_2_out, or_1_out, and_1_out, and_2_out, and_3_out, and_4_out);
  or or_3 (NEXTMUX[1], or_2_out, uJMPOP);
  Multiplexer #(.Selector_Bits(2), .Bits(16)) multiplexer_1 (
    .sel(NEXTMUX), .in_0(CAR_Plus_Latch_q), .in_1(CARstore), .in_2(uNextAddr), .in_3({IR, {8{1'b0}}}),
    .out(Next));
  or or_4 (NEXTMUX[0], uJMPOP, uRTS);

  // Other names for the same wires on the sheet: Clock = clk

  // Notes on the sheet:
  //   CAR
  //   uNextAddr
  //   PC
  //   Next Mux
  //   CARstore
  //   Next
  //   IR
  //   contents of Microcode (hex, n*v repeats v):
  //   cccc020003,100000,80000,cccc040000
endmodule
