// Digital circuit CPU.dig as structural Verilog
module CPU (
  input  clk
);

  wire A_LD_CDATA, IR_LD_XDATA, MAR_LD_CADDR, MBR_LD_XDATA, MBR_OUT_CDATA, PC_INC, PC_OUT_MAR;
  wire [7:0] A, driver_2_out, IR, MBR, Program_d;
  wire [15:0] add_1_s, driver_1_out, MAR, PC;

  Seven_Seg_Hex seven_seg_hex_1 (.d(MAR[15:12]), .dp(1'b0));
  Seven_Seg_Hex seven_seg_hex_2 (.d(MAR[7:4]), .dp(1'b0));
  Seven_Seg_Hex seven_seg_hex_3 (.d(MAR[11:8]), .dp(1'b0));
  Seven_Seg_Hex seven_seg_hex_4 (.d(MAR[3:0]), .dp(1'b0));
  Seven_Seg_Hex seven_seg_hex_5 (.d(MBR[3:0]), .dp(1'b0));
  Seven_Seg_Hex seven_seg_hex_6 (.d(MBR[7:4]), .dp(1'b0));
  Register #(.Bits(16)) u_PC (.D(add_1_s), .C(clk), .en(PC_INC), .Q(PC));
  Seven_Seg_Hex seven_seg_hex_7 (.d(PC[11:8]), .dp(1'b0));
  Seven_Seg_Hex seven_seg_hex_8 (.d(PC[15:12]), .dp(1'b0));
  assign driver_1_out = MAR_LD_CADDR ? PC : 16'bz;  // Driver driver_1
  Add #(.Bits(16)) add_1 (.a(PC), .b(16'h1), .c_i(1'b0), .s(add_1_s));  // open: c_o
  Seven_Seg_Hex seven_seg_hex_9 (.d(PC[3:0]), .dp(1'b0));
  Seven_Seg_Hex seven_seg_hex_10 (.d(PC[7:4]), .dp(1'b0));
  Seven_Seg_Hex seven_seg_hex_11 (.d(IR[7:4]), .dp(1'b0));
  Register #(.Bits(16)) u_MAR (.D(driver_1_out), .C(clk), .en(MAR_LD_CADDR), .Q(MAR));
  Seven_Seg_Hex seven_seg_hex_12 (.d(IR[3:0]), .dp(1'b0));
  Seven_Seg_Hex seven_seg_hex_13 (.d(A[7:4]), .dp(1'b0));
  Seven_Seg_Hex seven_seg_hex_14 (.d(A[3:0]), .dp(1'b0));
  ROM #(.AddrBits(16), .Bits(8)) Program (.A(MAR), .sel(1'b1), .D(Program_d));
  Register #(.Bits(8)) u_MBR (.D(Program_d), .C(clk), .en(MBR_LD_XDATA), .Q(MBR));
  assign driver_2_out = MBR_OUT_CDATA ? MBR : 8'bz;  // Driver driver_2
  Register #(.Bits(8)) u_IR (.D(Program_d), .C(clk), .en(IR_LD_XDATA), .Q(IR));
  // Control_Unit control_unit_1: pin names not known; wires that end beside it: 1'b0, 1'b0, 1'b0, 1'b0, IR, clk, PC_OUT_MAR, MAR_LD_CADDR, IR_LD_XDATA, PC_INC, MBR_LD_XDATA, MBR_OUT_CDATA, A_LD_CDATA
  Register #(.Bits(8)) u_A (.D(driver_2_out), .C(clk), .en(A_LD_CDATA), .Q(A));
  assign driver_2_out = 1'b0 ? A : 8'bz;  // Driver driver_3

  // Other names for the same wires on the sheet: Clock = clk

  // Notes on the sheet:
  //   MAR
  //   MBR
  //   XADDR
  //   PC
  //   IR
  //   A
  //   contents of Program (hex, n*v repeats v):
  //   ff,ab
  //   XDATA Bus
  //   CDATA Bus
  //   CDATA
endmodule
