// Digital circuit RAM.dig as structural Verilog
module RAM (
  input  [3:0] Addr,
  input  Store,
  input  Output,
  input  [3:0] Data_In,
  input  [12:0] Addr_2,
  input  Read,
  input  Read_2,
  input  [7:0] Output_2,
  output [3:0] Data_Out
);

  wire a623308a_1_p10, a623308a_1_p11, a623308a_1_p12, a623308a_1_p15, a623308a_1_p19, a623308a_1_p22,
       bussplitter_1_d3, bussplitter_1_d4, bussplitter_1_d5, bussplitter_1_d6, Clock_out, Load_out;
  wire [7:0] bussplitter_1_d;

  // A623308A a623308a_1: pin names not known; wires that end beside it: Addr_2[12], Addr_2[7], Addr_2[6], Addr_2[5], Addr_2[4], Addr_2[3], Addr_2[2], Addr_2[1], Addr_2[0], a623308a_1_p10, a623308a_1_p11, a623308a_1_p12, 1'b0, 1'b1, a623308a_1_p15, Addr_2[8], Addr_2[9], Addr_2[11], a623308a_1_p19, Addr_2[10], 1'b0, a623308a_1_p22
  LED led_1 (.in(Addr_2[8]));
  LED led_2 (.in(Addr_2[10]));
  LED led_3 (.in(Addr_2[9]));
  LED led_4 (.in(Addr_2[12]));
  LED led_5 (.in(Addr_2[11]));
  LED led_6 (.in(a623308a_1_p11));
  LED led_7 (.in(a623308a_1_p12));
  LED led_8 (.in(a623308a_1_p10));
  not not_1 (a623308a_1_p15, Load_out);
  not not_2 (a623308a_1_p19, Read);
  BusSplitter #(.Bits(8)) bussplitter_1 (
    .D(bussplitter_1_d), .OE(Load_out), .D0(a623308a_1_p10), .D1(a623308a_1_p11), .D2(a623308a_1_p12),
    .D3(bussplitter_1_d3), .D4(bussplitter_1_d4), .D5(bussplitter_1_d5), .D6(bussplitter_1_d6),
    .D7(a623308a_1_p22));
  Button Load (.out(Load_out));
  Register #(.Bits(8)) register_1 (.D(bussplitter_1_d), .C(Load_out), .en(Read_2), .Q(Output_2));
  Button Clock (.out(Clock_out));
  RAMSinglePort #(.AddrBits(4), .Bits(4)) ramsingleport_1 (
    .A(Addr), .str(Store), .C(Clock_out), .ld(Output), .D(Data_Out));
  assign Data_Out = Store ? Data_In : 4'bz;  // Driver driver_1
endmodule
