// Digital circuit Register.dig as structural Verilog
module Register (
  input  [7:0] Din,
  input  Load,
  input  Out,
  input  Clk,
  output [7:0] Dout
);

  wire _7404_1_pin2, _7404_1_pin4, DRout0, DRout1, DRout2, DRout3, DRout4, DRout5, DRout6, DRout7;

  _7404 _7404_1 (
    .pin1(Load), .pin2(_7404_1_pin2), .pin3(Out), .pin4(_7404_1_pin4), .pin5(1'b0), .pin7(1'b0), .pin9(1'b0),
    .pin11(1'b0), .pin13(1'b0), .pin14(1'b1));  // open: pin6, pin8, pin10, pin12
  _74377 _74377_1 (
    .pin1(_7404_1_pin2), .pin2(DRout0), .pin3(Din[0]), .pin4(Din[1]), .pin5(DRout1), .pin6(DRout2),
    .pin7(Din[2]), .pin8(Din[3]), .pin9(DRout3), .pin10(1'b0), .pin11(Clk), .pin12(DRout4), .pin13(Din[4]),
    .pin14(Din[5]), .pin15(DRout5), .pin16(DRout6), .pin17(Din[6]), .pin18(Din[7]), .pin19(DRout7),
    .pin20(1'b1));
  _74244 _74244_1 (
    .pin1(_7404_1_pin4), .pin2(DRout0), .pin3(Dout[7]), .pin4(DRout1), .pin5(Dout[6]), .pin6(DRout2),
    .pin7(Dout[5]), .pin8(DRout3), .pin9(Dout[4]), .pin10(1'b0), .pin11(DRout4), .pin12(Dout[3]),
    .pin13(DRout5), .pin14(Dout[2]), .pin15(DRout6), .pin16(Dout[1]), .pin17(DRout7), .pin18(Dout[0]),
    .pin19(_7404_1_pin4), .pin20(1'b1));
endmodule
