// Digital circuit Latched ALU.dig as structural Verilog
module Latched_ALU (
  input  CLOCK,
  input  [7:0] A,
  input  [7:0] B,
  input  CIN,
  input  [3:0] OP,
  input  LDA,
  input  LDB,
  input  LDC,
  output V,
  output C,
  output [7:0] R,
  output N,
  output Z,
  output [7:0] lt_A_gt,
  output [7:0] lt_B_gt,
  output lt_C_gt
);

  wire _7432_1_pin3, _7432_1_pin6, _7432_1_pin8, _7432_1_pin11, _7432_2_pin3, _7432_2_pin6, _7432_2_pin11,
       A_pin11, ALU_p5, ALU_p7, ALU_p8, AND_pin8, B_pin11;
  wire [7:0] ALU_p6, MUX_3_pin3;

  Seven_Seg_Hex seven_seg_hex_1 (.d(lt_A_gt[3:0]), .dp(1'b0));
  Seven_Seg_Hex seven_seg_hex_2 (.d(lt_A_gt[7:4]), .dp(1'b0));
  LED led_1 (.in(A[7]));
  LED led_2 (.in(A[6]));
  LED led_3 (.in(A[5]));
  LED led_4 (.in(A[4]));
  Seven_Seg_Hex seven_seg_hex_3 (.d(R[3:0]), .dp(1'b0));
  Seven_Seg_Hex seven_seg_hex_4 (.d({N, R[6:4]}), .dp(1'b0));
  LED led_5 (.in(N));
  LED led_6 (.in(R[6]));
  LED led_7 (.in(R[5]));
  LED led_8 (.in(R[4]));
  LED led_9 (.in(A[3]));
  LED led_10 (.in(A[2]));
  LED led_11 (.in(A[1]));
  LED led_12 (.in(A[0]));
  LED led_13 (.in(R[3]));
  LED led_14 (.in(R[2]));
  LED led_15 (.in(R[1]));
  LED led_16 (.in(R[0]));
  LED led_17 (.in(V));
  Seven_Seg_Hex seven_seg_hex_5 (.d(lt_B_gt[3:0]), .dp(1'b0));
  Seven_Seg_Hex seven_seg_hex_6 (.d(lt_B_gt[7:4]), .dp(1'b0));
  LED led_18 (.in(B[7]));
  LED led_19 (.in(B[6]));
  LED led_20 (.in(B[5]));
  LED led_21 (.in(B[4]));
  LED led_22 (.in(N));
  LED led_23 (.in(Z));
  LED led_24 (.in(C));
  LED led_25 (.in(B[3]));
  LED led_26 (.in(B[2]));
  LED led_27 (.in(B[1]));
  LED led_28 (.in(B[0]));
  LED led_29 (.in(CIN));
  _74273 u_B (
    .pin1(1'b1), .pin2(lt_B_gt[0]), .pin3(B[0]), .pin4(B[1]), .pin5(lt_B_gt[1]), .pin6(lt_B_gt[2]),
    .pin7(B[2]), .pin8(B[3]), .pin9(lt_B_gt[3]), .pin10(1'b0), .pin11(B_pin11), .pin12(lt_B_gt[4]),
    .pin13(B[4]), .pin14(B[5]), .pin15(lt_B_gt[5]), .pin16(lt_B_gt[6]), .pin17(B[6]), .pin18(B[7]),
    .pin19(lt_B_gt[7]), .pin20(1'b1));
  Shifter Shifter (.D(lt_A_gt), .OP(OP[1]), .DIR(OP[0]), .CIN(CIN));  // open: Q, COUT
  // _74_ALU ALU: pin names not known; wires that end beside it: lt_A_gt, lt_B_gt, OP[2:0], CIN, ALU_p5, ALU_p6, ALU_p7, ALU_p8
  _74273 u_A (
    .pin1(1'b1), .pin2(lt_A_gt[0]), .pin3(A[0]), .pin4(A[1]), .pin5(lt_A_gt[1]), .pin6(lt_A_gt[2]),
    .pin7(A[2]), .pin8(A[3]), .pin9(lt_A_gt[3]), .pin10(1'b0), .pin11(A_pin11), .pin12(lt_A_gt[4]),
    .pin13(A[4]), .pin14(A[5]), .pin15(lt_A_gt[5]), .pin16(lt_A_gt[6]), .pin17(A[6]), .pin18(A[7]),
    .pin19(lt_A_gt[7]), .pin20(1'b1));
  _7408 AND (
    .pin1(CLOCK), .pin2(LDA), .pin3(A_pin11), .pin4(CLOCK), .pin5(LDB), .pin6(B_pin11), .pin7(1'b0),
    .pin8(AND_pin8), .pin9(CLOCK), .pin10(LDC), .pin12(1'b0), .pin13(1'b0), .pin14(1'b1));  // open: pin11
  _74157 MUX (
    .pin1(OP[3]), .pin2(ALU_p6[4]), .pin3(MUX_3_pin3[4]), .pin4(R[4]), .pin5(ALU_p6[5]),
    .pin6(MUX_3_pin3[5]), .pin7(R[5]), .pin8(1'b0), .pin9(R[6]), .pin10(MUX_3_pin3[6]), .pin11(ALU_p6[6]),
    .pin12(N), .pin13(MUX_3_pin3[7]), .pin14(ALU_p6[7]), .pin15(1'b0), .pin16(1'b1));
  _74157 MUX_2 (
    .pin1(OP[3]), .pin2(ALU_p8), .pin3(ALU_p5), .pin4(C), .pin5(ALU_p7), .pin6(1'b0), .pin7(V), .pin8(1'b0),
    .pin10(1'b0), .pin11(1'b0), .pin13(1'b0), .pin14(1'b0), .pin15(1'b0), .pin16(1'b1));  // open: pin9, pin12
  _74273 u_C (
    .pin1(1'b1), .pin2(lt_C_gt), .pin3(CIN), .pin4(1'b0), .pin7(1'b0), .pin8(1'b0), .pin10(1'b0),
    .pin11(AND_pin8), .pin13(1'b0), .pin14(1'b0), .pin17(1'b0), .pin18(1'b0), .pin20(1'b1));  // open: pin5, pin6, pin9, pin12, pin15, pin16, pin19
  _74157 MUX_3 (
    .pin1(OP[3]), .pin2(ALU_p6[0]), .pin3(MUX_3_pin3[0]), .pin4(R[0]), .pin5(ALU_p6[1]),
    .pin6(MUX_3_pin3[1]), .pin7(R[1]), .pin8(1'b0), .pin9(R[2]), .pin10(MUX_3_pin3[2]), .pin11(ALU_p6[2]),
    .pin12(R[3]), .pin13(MUX_3_pin3[3]), .pin14(ALU_p6[3]), .pin15(1'b0), .pin16(1'b1));
  _7432 _7432_1 (
    .pin1(R[0]), .pin2(R[1]), .pin3(_7432_1_pin3), .pin4(R[2]), .pin5(R[3]), .pin6(_7432_1_pin6),
    .pin7(1'b0), .pin8(_7432_1_pin8), .pin9(R[4]), .pin10(R[5]), .pin11(_7432_1_pin11), .pin12(R[6]),
    .pin13(N), .pin14(1'b1));
  _7432 _7432_2 (
    .pin1(_7432_1_pin3), .pin2(_7432_1_pin6), .pin3(_7432_2_pin3), .pin4(_7432_1_pin11), .pin5(_7432_1_pin8),
    .pin6(_7432_2_pin6), .pin7(1'b0), .pin9(1'b0), .pin10(1'b0), .pin11(_7432_2_pin11), .pin12(_7432_2_pin6),
    .pin13(_7432_2_pin3), .pin14(1'b1));  // open: pin8
  _7404 _7404_1 (
    .pin1(_7432_2_pin11), .pin2(Z), .pin3(1'b0), .pin5(1'b0), .pin7(1'b0), .pin9(1'b0), .pin11(1'b0),
    .pin13(1'b0), .pin14(1'b1));  // open: pin4, pin6, pin8, pin10, pin12

  assign R[7] = N;

  // Other names for the same wires on the sheet: AOUT0 = lt_A_gt[0]; AOUT1 = lt_A_gt[1]; AOUT2 = lt_A_gt[2];
  //   AOUT3 = lt_A_gt[3]; AOUT4 = lt_A_gt[4]; AOUT5 = lt_A_gt[5]; AOUT6 = lt_A_gt[6]; AOUT7 = lt_A_gt[7];
  //   BOUT0 = lt_B_gt[0]; BOUT1 = lt_B_gt[1]; BOUT2 = lt_B_gt[2]; BOUT3 = lt_B_gt[3]; BOUT4 = lt_B_gt[4];
  //   BOUT5 = lt_B_gt[5]; BOUT6 = lt_B_gt[6]; BOUT7 = lt_B_gt[7]; CFIN = C; COUT = lt_C_gt; OUT0 = R[0]; OUT1 = R[1];
  //   OUT2 = R[2]; OUT3 = R[3]; OUT4 = R[4]; OUT5 = R[5]; OUT6 = R[6]; NFIN = N; OUT7 = N; VFIN = V; ZFIN = Z

  // Notes on the sheet:
  //   A
  //   R
  //   B
  //   Registers
  //   Load Enables
  //   Output Selection
  //   R Low
  //   R High
  //   C
  //   Zero
endmodule

/* Test case AND:
CLOCK A    B    OP   CIN R    V N Z C  LDA LDB LDC
C     0x00 0x00 0x00 0   0    X 0 1 X  1   1   1
C     0x00 0x00 0x00 1   0    X 0 1 X  1   1   1 
C     0xBE 0xAC 0x00 0   0xAC X 1 0 X  1   1   1
C     0xBE 0xAC 0x00 1   0xAC X 1 0 X  1   1   1
*/

/* Test case NOT:
CLOCK A    B    OP     CIN R    V N Z C LDA LDB LDC
C     0x00 0x00 0b0010 0   0xFF X 1 0 X 1   1   1
C     0x00 0x00 0b0010 1   0xFF X 1 0 X 1   1   1 
C     0xBE 0xC5 0b0010 0   0x41 X 0 0 X 1   1   1
C     0xBE 0xAC 0b0010 1   0x41 X 0 0 X 1   1   1
*/

/* Test case ADD:
CLOCK A    B    OP    CIN R    V N Z C LDA LDB LDC
C     0x01 0x02 0b100 0   0x03 0 0 0 0 1   1   1
C     0xA0 0x12 0b100 0   0xB2 0 1 0 0 1   1   1
C     0xCC 0xDE 0b100 0   0xAA 0 1 0 1 1   1   1
C     0xCC 0xBB 0b100 0   0x87 0 1 0 1 1   1   1

# Two positives creating a negative
C     0x50 0x55 0b100 0   0xA5 1 1 0 0 1   1   1

# Two negatives create a positive
C     0xF0 0x80 0b100 0   0x70 1 0 0 1 1   1   1
*/

/* Test case INC:
CLOCK A    B    OP     CIN R    V N Z C LDA LDB LDC
C     0x01 0x02 0b0110 0   0x02 X 0 0 X 1   1   1
C     0x01 0x04 0b0110 0   0x02 X 0 0 X 1   1   1
C     0x01 0x02 0b0110 1   0x02 X 0 0 X 1   1   1
C     0x01 0x04 0b0110 1   0x02 X 0 0 X 1   1   1
C     0xCC 0x02 0b0110 0   0xCD X 1 0 X 1   1   1
C     0xFF 0x00 0b0110 0   0x00 X 0 1 X 1   1   1
*/

/* Test case RIGHT-SHIFT:
CLOCK  A          CIN OP          R          V N Z C LDA LDC
# Single bit, carry clear
C      0b00000001 0   0b1000      0b00000000 X 0 1 1 1   1
C      0b00000010 0   0b1000      0b00000001 X 0 0 0 1   1
C      0b00000100 0   0b1000      0b00000010 X 0 0 0 1   1
C      0b00001000 0   0b1000      0b00000100 X 0 0 0 1   1
C      0b00010000 0   0b1000      0b00001000 X 0 0 0 1   1
C      0b00100000 0   0b1000      0b00010000 X 0 0 0 1   1
C      0b01000000 0   0b1000      0b00100000 X 0 0 0 1   1
C      0b10000000 0   0b1000      0b01000000 X 0 0 0 1   1

# Single bit, carry set
C      0b00000001 1   0b1000      0b00000000 X 0 1 1 1   1
C      0b00000010 1   0b1000      0b00000001 X 0 0 0 1   1
C      0b00000100 1   0b1000      0b00000010 X 0 0 0 1   1
C      0b00001000 1   0b1000      0b00000100 X 0 0 0 1   1
C      0b00010000 1   0b1000      0b00001000 X 0 0 0 1   1
C      0b00100000 1   0b1000      0b00010000 X 0 0 0 1   1
C      0b01000000 1   0b1000      0b00100000 X 0 0 0 1   1
C      0b10000000 1   0b1000      0b01000000 X 0 0 0 1   1

# Multi-bit tests
C      0b00011001 0   0b1000      0b00001100 X 0 0 1 1   1
C      0b01100010 0   0b1000      0b00110001 X 0 0 0 1   1
C      0b00100100 0   0b1000      0b00010010 X 0 0 0 1   1
C      0b10001000 0   0b1000      0b01000100 X 0 0 0 1   1
C      0b00110000 1   0b1000      0b00011000 X 0 0 0 1   1
C      0b00100001 1   0b1000      0b00010000 X 0 0 1 1   1
C      0b01000111 1   0b1000      0b00100011 X 0 0 1 1   1
C      0b10110010 1   0b1000      0b01011001 X 0 0 0 1   1
*/

/* Test case RIGHT-ROT:
CLOCK A          CIN OP     R          V N Z C LDA LDC
# Single bit, carry clear
C     0b00000001 0   0b1010 0b00000000 X 0 1 1 1   1
C     0b00000010 0   0b1010 0b00000001 X 0 0 0 1   1
C     0b00000100 0   0b1010 0b00000010 X 0 0 0 1   1
C     0b00001000 0   0b1010 0b00000100 X 0 0 0 1   1
C     0b00010000 0   0b1010 0b00001000 X 0 0 0 1   1
C     0b00100000 0   0b1010 0b00010000 X 0 0 0 1   1
C     0b01000000 0   0b1010 0b00100000 X 0 0 0 1   1
C     0b10000000 0   0b1010 0b01000000 X 0 0 0 1   1

# Single bit, carry set
C     0b00000001 1   0b1010 0b10000000 X 1 0 1 1   1
C     0b00000010 1   0b1010 0b10000001 X 1 0 0 1   1
C     0b00000100 1   0b1010 0b10000010 X 1 0 0 1   1
C     0b00001000 1   0b1010 0b10000100 X 1 0 0 1   1
C     0b00010000 1   0b1010 0b10001000 X 1 0 0 1   1
C     0b00100000 1   0b1010 0b10010000 X 1 0 0 1   1
C     0b01000000 1   0b1010 0b10100000 X 1 0 0 1   1
C     0b10000000 1   0b1010 0b11000000 X 1 0 0 1   1

# Multi-bit tests
C     0b00011001 0   0b1010 0b00001100 X 0 0 1 1   1
C     0b01100010 0   0b1010 0b00110001 X 0 0 0 1   1
C     0b00100100 0   0b1010 0b00010010 X 0 0 0 1   1
C     0b10001000 0   0b1010 0b01000100 X 0 0 0 1   1
C     0b00110000 1   0b1010 0b10011000 X 1 0 0 1   1
C     0b00100001 1   0b1010 0b10010000 X 1 0 1 1   1
C     0b01000111 1   0b1010 0b10100011 X 1 0 1 1   1
C     0b10110010 1   0b1010 0b11011001 X 1 0 0 1   1
*/

/* Test case OR:
CLOCK A    B    OP     CIN R    V N Z C    LDA LDB LDC
C     0x00 0x00 0b0001 0   0    X 0 1 X    1   1   1
C     0x00 0x00 0b0001 1   0    X 0 1 X    1   1   1
C     0x2E 0xAC 0b0001 0   0xAE X 1 0 X    1   1   1
C     0x2E 0xAC 0b0001 1   0xAE X 1 0 X    1   1   1 
*/

/* Test case XOR:
CLOCK A    B    OP     CIN R    V N Z C LDA LDB LDC
C     0x00 0x00 0b0011 0   0    X 0 1 X 1   1   1
C     0x00 0x00 0b0011 1   0    X 0 1 X 1   1   1
C     0xBE 0xAC 0b0011 0   0x12 X 0 0 X 1   1   1
C     0xBE 0xAC 0b0011 1   0x12 X 0 0 X 1   1   1
*/

/* Test case DEC:
CLOCK A    B    OP     CIN R    V N Z C LDA LDB LDC
C     0xEE 0x02 0b0111 0   0xED X 1 0 X 1   1   1
C     0xEE 0x04 0b0111 0   0xED X 1 0 X 1   1   1    
C     0xEE 0x02 0b0111 1   0xED X 1 0 X 1   1   1    
C     0xEE 0x04 0b0111 1   0xED X 1 0 X 1   1   1    
C     0x00 0x00 0b0111 0   0xFF X 1 0 0 1   1   1    
*/

/* Test case LEFT-SHIFT:
CLOCK  A          CIN OP       R          V N Z C LDA LDC
# Single bit, carry clear
C      0b00000001 0   0b1001   0b00000010 X 0 0 0 1   1
C      0b00000010 0   0b1001   0b00000100 X 0 0 0 1   1
C      0b00000100 0   0b1001   0b00001000 X 0 0 0 1   1
C      0b00001000 0   0b1001   0b00010000 X 0 0 0 1   1
C      0b00010000 0   0b1001   0b00100000 X 0 0 0 1   1
C      0b00100000 0   0b1001   0b01000000 X 0 0 0 1   1
C      0b01000000 0   0b1001   0b10000000 X 1 0 0 1   1
C      0b10000000 0   0b1001   0b00000000 X 0 1 1 1   1

# Single bit, carry set
C      0b00000001 1   0b1001   0b00000010 X 0 0 0 1   1
C      0b00000010 1   0b1001   0b00000100 X 0 0 0 1   1
C      0b00000100 1   0b1001   0b00001000 X 0 0 0 1   1
C      0b00001000 1   0b1001   0b00010000 X 0 0 0 1   1
C      0b00010000 1   0b1001   0b00100000 X 0 0 0 1   1
C      0b00100000 1   0b1001   0b01000000 X 0 0 0 1   1
C      0b01000000 1   0b1001   0b10000000 X 1 0 0 1   1
C      0b10000000 1   0b1001   0b00000000 X 0 1 1 1   1

# Multi-bit tests
C      0b00011001 0   0b1001   0b00110010 X  0 0 0 1   1
C      0b01100010 0   0b1001   0b11000100 X  1 0 0 1   1
C      0b00100100 0   0b1001   0b01001000 X  0 0 0 1   1
C      0b10001000 0   0b1001   0b00010000 X  0 0 1 1   1
C      0b00110000 1   0b1001   0b01100000 X  0 0 0 1   1
C      0b00100001 1   0b1001   0b01000010 X  0 0 0 1   1
C      0b01000111 1   0b1001   0b10001110 X  1 0 0 1   1
C      0b10110010 1   0b1001   0b01100100 X  0 0 1 1   1
*/

/* Test case LEFT-ROT:
CLOCK A          CIN OP     R        C LDA LDC
# Single bit, carry clear
C     0b00000001 0   0b1011 0b00000010 0 1   1
C     0b00000010 0   0b1011 0b00000100 0 1   1
C     0b00000100 0   0b1011 0b00001000 0 1   1
C     0b00001000 0   0b1011 0b00010000 0 1   1
C     0b00010000 0   0b1011 0b00100000 0 1   1
C     0b00100000 0   0b1011 0b01000000 0 1   1
C     0b01000000 0   0b1011 0b10000000 0 1   1
C     0b10000000 0   0b1011 0b00000000 1 1   1

# Single bit, carry set
C     0b00000001 1   0b1011 0b00000011 0 1   1
C     0b00000010 1   0b1011 0b00000101 0 1   1
C     0b00000100 1   0b1011 0b00001001 0 1   1
C     0b00001000 1   0b1011 0b00010001 0 1   1
C     0b00010000 1   0b1011 0b00100001 0 1   1
C     0b00100000 1   0b1011 0b01000001 0 1   1
C     0b01000000 1   0b1011 0b10000001 0 1   1
C     0b10000000 1   0b1011 0b00000001 1 1   1

# Multi-bit tests
C     0b00011001 0   0b1011 0b00110010 0 1   1
C     0b01100010 0   0b1011 0b11000100 0 1   1
C     0b00100100 0   0b1011 0b01001000 0 1   1
C     0b10001000 0   0b1011 0b00010000 1 1   1
C     0b00110000 1   0b1011 0b01100001 0 1   1
C     0b00100001 1   0b1011 0b01000011 0 1   1
C     0b01000111 1   0b1011 0b10001111 0 1   1
C     0b10110010 1   0b1011 0b01100101 1 1   1
*/
