// Digital circuit ALU-SAFE-PRE-DITCHING-ARITH-LOG-FLAG-CALC.dig as structural Verilog
module ALU_SAFE_PRE_DITCHING_ARITH_LOG_FLAG_CALC (
  input  [7:0] A,
  input  [7:0] B,
  input  [2:0] OP,
  input  Nin,
  input  Vin,
  input  Zin,
  input  Cin,
  output [7:0] Out,
  output Nout,
  output Vout,
  output Zout,
  output Cout
);

  wire _3_Input_NANDs_pin6, _3_Input_NANDs_pin12, And0, And1, And2, And3, And4, And5, And6, And7, Bneg,
       Ccalc, Full_Adder_Low_pin14, Is_Arithmetic_pin3, Is_Arithmetic_pin6, Is_Arithmetic_pin8,
       Mux_High_B__1_pin4, Mux_High_B__1_pin7, Mux_High_B__1_pin9, Mux_High_B__1_pin12, Mux_Low_B__1_pin1,
       Mux_Low_B__1_pin4, Mux_Low_B__1_pin7, Mux_Low_B__1_pin9, Mux_Low_B__1_pin12, Not0, Not1, Not2, Not3,
       Not4, Not5, Not6, Not7, Not_2_pin11, Not_2_pin13, Not_pin11, Not_pin13, Not_Zero_pin19, NotA7,
       NotBneg, NotOut7, Ones_Comp_High__Xor_pin3, Ones_Comp_High__Xor_pin6, Ones_Comp_High__Xor_pin8,
       Ones_Comp_Low__Xor_pin2, Ones_Comp_Low__Xor_pin3, Ones_Comp_Low__Xor_pin6, Ones_Comp_Low__Xor_pin8,
       Ones_Comp_Low__Xor_pin11, OPadd, OPand, OPdec, OPinc, OPnot, OPor, OPsub, OPxor, Or0, Or1, Or2, Or3,
       Or4, Or5, Or6, Or7, Ors_pin3, Sum0, Sum1, Sum2, Sum3, Sum4, Sum5, Sum6, Sum7, Vcalc, XOr0, XOr1, XOr2,
       XOr3, XOr4, XOr5, XOr6, XOr7, Zcalc;

  Seven_Seg_Hex seven_seg_hex_1 (.d(A[7:4]), .dp(1'b0));
  LED led_1 (.in(A[7]));
  Seven_Seg_Hex seven_seg_hex_2 (.d(B[7:4]), .dp(1'b0));
  LED led_2 (.in(B[7]));
  LED led_3 (.in(Out[7]));
  Seven_Seg_Hex seven_seg_hex_3 (.d(A[3:0]), .dp(1'b0));
  LED led_4 (.in(A[6]));
  Seven_Seg_Hex seven_seg_hex_4 (.d(B[3:0]), .dp(1'b0));
  LED led_5 (.in(B[6]));
  Seven_Seg_Hex seven_seg_hex_5 (.d(Out[7:4]), .dp(1'b0));
  LED led_6 (.in(Out[6]));
  LED led_7 (.in(A[5]));
  LED led_8 (.in(B[5]));
  Seven_Seg_Hex seven_seg_hex_6 (.d(Out[3:0]), .dp(1'b0));
  LED led_9 (.in(Out[5]));
  LED led_10 (.in(A[4]));
  LED led_11 (.in(A[3]));
  LED led_12 (.in(B[4]));
  LED led_13 (.in(B[3]));
  LED led_14 (.in(Out[4]));
  LED led_15 (.in(Out[3]));
  LED led_16 (.in(A[2]));
  LED led_17 (.in(B[2]));
  LED led_18 (.in(Out[2]));
  LED led_19 (.in(A[1]));
  LED led_20 (.in(B[1]));
  LED N (.in(Nout));
  LED Z (.in(Zout));
  LED C (.in(Cout));
  LED V (.in(Vout));
  LED led_21 (.in(Out[1]));
  LED led_22 (.in(A[0]));
  LED led_23 (.in(B[0]));
  LED led_24 (.in(Out[0]));
  _74238 Op_Decoder (
    .pin1(OP[0]), .pin2(OP[1]), .pin3(OP[2]), .pin4(1'b0), .pin5(1'b0), .pin6(1'b1), .pin7(OPdec),
    .pin8(1'b0), .pin9(OPinc), .pin10(OPsub), .pin11(OPadd), .pin12(OPxor), .pin13(OPnot), .pin14(OPor),
    .pin15(OPand), .pin16(1'b1));
  _7408 And_Low (
    .pin1(A[0]), .pin2(B[0]), .pin3(And0), .pin4(A[1]), .pin5(B[1]), .pin6(And1), .pin7(1'b0), .pin8(And2),
    .pin9(A[2]), .pin10(B[2]), .pin11(And3), .pin12(A[3]), .pin13(B[3]), .pin14(1'b1));
  _7408 And_High (
    .pin1(A[4]), .pin2(B[4]), .pin3(And4), .pin4(A[5]), .pin5(B[5]), .pin6(And5), .pin7(1'b0), .pin8(And6),
    .pin9(A[6]), .pin10(B[6]), .pin11(And7), .pin12(A[7]), .pin13(B[7]), .pin14(1'b1));
  _74157 Mux_Low_B__1 (
    .pin1(Mux_Low_B__1_pin1), .pin2(B[0]), .pin3(1'b1), .pin4(Mux_Low_B__1_pin4), .pin5(B[1]), .pin6(1'b0),
    .pin7(Mux_Low_B__1_pin7), .pin8(1'b0), .pin9(Mux_Low_B__1_pin9), .pin10(1'b0), .pin11(B[2]),
    .pin12(Mux_Low_B__1_pin12), .pin13(1'b0), .pin14(B[3]), .pin15(1'b0), .pin16(1'b1));
  _74157 Mux_High_B__1 (
    .pin1(Mux_Low_B__1_pin1), .pin2(B[4]), .pin3(1'b0), .pin4(Mux_High_B__1_pin4), .pin5(B[5]), .pin6(1'b0),
    .pin7(Mux_High_B__1_pin7), .pin8(1'b0), .pin9(Mux_High_B__1_pin9), .pin10(1'b0), .pin11(B[7]),
    .pin12(Mux_High_B__1_pin12), .pin13(1'b0), .pin14(B[6]), .pin15(1'b0), .pin16(1'b1));
  _7432 Or_Low (
    .pin1(A[0]), .pin2(B[0]), .pin3(Or0), .pin4(A[1]), .pin5(B[1]), .pin6(Or1), .pin7(1'b0), .pin8(Or2),
    .pin9(A[2]), .pin10(B[2]), .pin11(Or3), .pin12(A[3]), .pin13(B[3]), .pin14(1'b1));
  _7432 Or_High (
    .pin1(A[4]), .pin2(B[4]), .pin3(Or4), .pin4(A[5]), .pin5(B[5]), .pin6(Or5), .pin7(1'b0), .pin8(Or6),
    .pin9(A[6]), .pin10(B[6]), .pin11(Or7), .pin12(A[7]), .pin13(B[7]), .pin14(1'b1));
  _7486 Ones_Comp_Low__Xor (
    .pin1(Mux_Low_B__1_pin4), .pin2(Ones_Comp_Low__Xor_pin2), .pin3(Ones_Comp_Low__Xor_pin3),
    .pin4(Mux_Low_B__1_pin7), .pin5(Ones_Comp_Low__Xor_pin2), .pin6(Ones_Comp_Low__Xor_pin6), .pin7(1'b0),
    .pin8(Ones_Comp_Low__Xor_pin8), .pin9(Mux_Low_B__1_pin9), .pin10(Ones_Comp_Low__Xor_pin2),
    .pin11(Ones_Comp_Low__Xor_pin11), .pin12(Mux_Low_B__1_pin12), .pin13(Ones_Comp_Low__Xor_pin2),
    .pin14(1'b1));
  _7486 Ones_Comp_High__Xor (
    .pin1(Mux_High_B__1_pin4), .pin2(Ones_Comp_Low__Xor_pin2), .pin3(Ones_Comp_High__Xor_pin3),
    .pin4(Mux_High_B__1_pin7), .pin5(Ones_Comp_Low__Xor_pin2), .pin6(Ones_Comp_High__Xor_pin6), .pin7(1'b0),
    .pin8(Ones_Comp_High__Xor_pin8), .pin9(Mux_High_B__1_pin9), .pin10(Ones_Comp_Low__Xor_pin2),
    .pin11(Bneg), .pin12(Mux_High_B__1_pin12), .pin13(Ones_Comp_Low__Xor_pin2), .pin14(1'b1));
  _7432 Ors (
    .pin1(Ones_Comp_Low__Xor_pin2), .pin2(Cin), .pin3(Ors_pin3), .pin4(OPsub), .pin5(OPdec),
    .pin6(Ones_Comp_Low__Xor_pin2), .pin7(1'b0), .pin8(Mux_Low_B__1_pin1), .pin9(OPdec), .pin10(OPinc),
    .pin12(1'b0), .pin13(1'b0), .pin14(1'b1));  // open: pin11
  _7486 Xor_Low (
    .pin1(A[0]), .pin2(B[0]), .pin3(XOr0), .pin4(A[1]), .pin5(B[1]), .pin6(XOr1), .pin7(1'b0), .pin8(XOr2),
    .pin9(A[2]), .pin10(B[2]), .pin11(XOr3), .pin12(A[3]), .pin13(B[3]), .pin14(1'b1));
  _7486 Xor_High (
    .pin1(A[4]), .pin2(B[4]), .pin3(XOr4), .pin4(A[5]), .pin5(B[5]), .pin6(XOr5), .pin7(1'b0), .pin8(XOr6),
    .pin9(A[6]), .pin10(B[6]), .pin11(XOr7), .pin12(A[7]), .pin13(B[7]), .pin14(1'b1));
  _7483 Full_Adder_Low (
    .pin1(A[3]), .pin2(Sum2), .pin3(A[2]), .pin4(Ones_Comp_Low__Xor_pin8), .pin5(1'b1), .pin6(Sum1),
    .pin7(Ones_Comp_Low__Xor_pin6), .pin8(A[1]), .pin9(Sum0), .pin10(A[0]), .pin11(Ones_Comp_Low__Xor_pin3),
    .pin12(1'b0), .pin13(Ors_pin3), .pin14(Full_Adder_Low_pin14), .pin15(Sum3),
    .pin16(Ones_Comp_Low__Xor_pin11));
  _7483 Full_Adder_High (
    .pin1(A[7]), .pin2(Sum6), .pin3(A[6]), .pin4(Ones_Comp_High__Xor_pin8), .pin5(1'b1), .pin6(Sum5),
    .pin7(Ones_Comp_High__Xor_pin6), .pin8(A[5]), .pin9(Sum4), .pin10(A[4]),
    .pin11(Ones_Comp_High__Xor_pin3), .pin12(1'b0), .pin13(Full_Adder_Low_pin14), .pin14(Ccalc),
    .pin15(Sum7), .pin16(Bneg));
  _7404 Not (
    .pin1(A[0]), .pin2(Not0), .pin3(A[1]), .pin4(Not1), .pin5(A[2]), .pin6(Not2), .pin7(1'b0), .pin8(Not3),
    .pin9(A[3]), .pin11(Not_pin11), .pin13(Not_pin13), .pin14(1'b1));  // open: pin10, pin12
  _7404 Not_2 (
    .pin1(A[4]), .pin2(Not4), .pin3(A[5]), .pin4(Not5), .pin5(A[6]), .pin6(Not6), .pin7(1'b0), .pin8(Not7),
    .pin9(A[7]), .pin11(Not_2_pin11), .pin13(Not_2_pin13), .pin14(1'b1));  // open: pin10, pin12
  // NotConnected on Not_pin13
  // NotConnected on Not_pin11
  // NotConnected on Not_2_pin13
  // NotConnected on Not_2_pin11
  _7410 _3_Input_NANDs (
    .pin1(A[7]), .pin2(Bneg), .pin3(NotA7), .pin4(NotBneg), .pin5(Out[7]), .pin6(_3_Input_NANDs_pin6),
    .pin7(1'b0), .pin9(1'b0), .pin10(1'b0), .pin11(1'b0), .pin12(_3_Input_NANDs_pin12), .pin13(NotOut7),
    .pin14(1'b1));  // open: pin8
  _74688 Not_Zero (
    .pin1(1'b0), .pin2(Out[0]), .pin3(1'b0), .pin4(Out[1]), .pin5(1'b0), .pin6(Out[2]), .pin7(1'b0),
    .pin8(Out[3]), .pin9(1'b0), .pin10(1'b0), .pin11(Out[4]), .pin12(1'b0), .pin13(Out[5]), .pin14(1'b0),
    .pin15(Out[6]), .pin16(1'b0), .pin17(Out[7]), .pin18(1'b0), .pin19(Not_Zero_pin19), .pin20(1'b1));
  _7404 Zero (
    .pin1(Not_Zero_pin19), .pin2(Zcalc), .pin3(1'b0), .pin5(1'b0), .pin7(1'b0), .pin9(1'b0), .pin11(1'b0),
    .pin13(1'b0), .pin14(1'b1));  // open: pin4, pin6, pin8, pin10, pin12
  _7400 _2_Input_NANDs (
    .pin1(A[7]), .pin2(A[7]), .pin3(NotA7), .pin4(Bneg), .pin5(Bneg), .pin6(NotBneg), .pin7(1'b0),
    .pin8(NotOut7), .pin9(Out[7]), .pin10(Out[7]), .pin11(Vcalc), .pin12(_3_Input_NANDs_pin6),
    .pin13(_3_Input_NANDs_pin12), .pin14(1'b1));
  _74151 Bit_3_Mux (
    .pin1(XOr3), .pin2(Not3), .pin3(Or3), .pin4(And3), .pin5(Out[3]), .pin7(1'b0), .pin8(1'b0), .pin9(OP[2]),
    .pin10(OP[1]), .pin11(OP[0]), .pin12(Sum3), .pin13(Sum3), .pin14(Sum3), .pin15(Sum3), .pin16(1'b1));  // open: pin6
  _74151 Bit_7_Mux (
    .pin1(XOr7), .pin2(Not7), .pin3(Or7), .pin4(And7), .pin5(Out[7]), .pin7(1'b0), .pin8(1'b0), .pin9(OP[2]),
    .pin10(OP[1]), .pin11(OP[0]), .pin12(Sum7), .pin13(Sum7), .pin14(Sum7), .pin15(Sum7), .pin16(1'b1));  // open: pin6
  _74151 Bit_2_Mux (
    .pin1(XOr2), .pin2(Not2), .pin3(Or2), .pin4(And2), .pin5(Out[2]), .pin7(1'b0), .pin8(1'b0), .pin9(OP[2]),
    .pin10(OP[1]), .pin11(OP[0]), .pin12(Sum2), .pin13(Sum2), .pin14(Sum2), .pin15(Sum2), .pin16(1'b1));  // open: pin6
  _74151 Bit_6_Mux (
    .pin1(XOr6), .pin2(Not6), .pin3(Or6), .pin4(And6), .pin5(Out[6]), .pin7(1'b0), .pin8(1'b0), .pin9(OP[2]),
    .pin10(OP[1]), .pin11(OP[0]), .pin12(Sum6), .pin13(Sum6), .pin14(Sum6), .pin15(Sum6), .pin16(1'b1));  // open: pin6
  _7432 Is_Arithmetic (
    .pin1(OPadd), .pin2(OPsub), .pin3(Is_Arithmetic_pin3), .pin4(OPinc), .pin5(OPdec),
    .pin6(Is_Arithmetic_pin6), .pin7(1'b0), .pin8(Is_Arithmetic_pin8), .pin9(Is_Arithmetic_pin6),
    .pin10(Is_Arithmetic_pin3), .pin12(1'b0), .pin13(1'b0), .pin14(1'b1));  // open: pin11
  _74157 Flag_Select__Mux (
    .pin1(Is_Arithmetic_pin8), .pin2(Out[7]), .pin3(Out[7]), .pin4(Nout), .pin5(Zcalc), .pin6(Zcalc),
    .pin7(Zout), .pin8(1'b0), .pin9(Cout), .pin10(Ccalc), .pin11(Cin), .pin12(Vout), .pin13(Vcalc),
    .pin14(Vin), .pin15(1'b0), .pin16(1'b1));
  _74151 Bit_1_Mux (
    .pin1(XOr1), .pin2(Not1), .pin3(Or1), .pin4(And1), .pin5(Out[1]), .pin7(1'b0), .pin8(1'b0), .pin9(OP[2]),
    .pin10(OP[1]), .pin11(OP[0]), .pin12(Sum1), .pin13(Sum1), .pin14(Sum1), .pin15(Sum1), .pin16(1'b1));  // open: pin6
  _74151 Bit_5_Mux (
    .pin1(XOr5), .pin2(Not5), .pin3(Or5), .pin4(And5), .pin5(Out[5]), .pin7(1'b0), .pin8(1'b0), .pin9(OP[2]),
    .pin10(OP[1]), .pin11(OP[0]), .pin12(Sum5), .pin13(Sum5), .pin14(Sum5), .pin15(Sum5), .pin16(1'b1));  // open: pin6
  _74151 Bit_0_Mux (
    .pin1(XOr0), .pin2(Not0), .pin3(Or0), .pin4(And0), .pin5(Out[0]), .pin7(1'b0), .pin8(1'b0), .pin9(OP[2]),
    .pin10(OP[1]), .pin11(OP[0]), .pin12(Sum0), .pin13(Sum0), .pin14(Sum0), .pin15(Sum0), .pin16(1'b1));  // open: pin6
  _74151 Bit_4_Mux (
    .pin1(XOr4), .pin2(Not4), .pin3(Or4), .pin4(And4), .pin5(Out[4]), .pin7(1'b0), .pin8(1'b0), .pin9(OP[2]),
    .pin10(OP[1]), .pin11(OP[0]), .pin12(Sum4), .pin13(Sum4), .pin14(Sum4), .pin15(Sum4), .pin16(1'b1));  // open: pin6

  // Other names for the same wires on the sheet: Z_in = Zin

  // Notes on the sheet:
  //   A: default 3
  //   B: default 2
  //   0 0 0 AND
  //   0 0 1 OR
  //   0 1 0 NOT
  //   0 1 1 XOR
  //   1 0 0 ADD
  //   1 0 1 SUB
  //   1 1 0 INC
  //   1 1 1 DEC
  //   Out
  //   In
  //   Op Decoding
  //   B/'1' for Inc/Dec
  //   Arithmetic Operations
  //   Logical Operations
  //   1: OPsub OR OpDec OR Cin => Cin Adder
  //   2: OPsub OR OpDec => 1's Comp
  //   3: OPinc OR OpDec => B or '1'
  //   Zero
  //   Overflow
  //   NOT ANeg AND NOT BNeg AND OutNeg
  //   OR
  //   ANet AND BNeg AND NOT OutNeg
  //   Need to account for add(inc)sub(dec) - tried using bit 7 after 1's comp ... don't know if that covers all?
  //   Flag Calculations
  //   Flag Output Selection
  //   Data Output Selection
endmodule
