// Digital circuit CPU.dig as structural Verilog
module CPU (
  input  RUN,
  input  [15:0] MCBREAKPOINT,
  input  [15:0] UCBREAKPOINT,
  input  FAST,
  input  SLOW,
  input  MCBSET,
  input  UCBSET
);

  wire A_LD_CDATA, A_OUT_CDATA, ALU_NOUT, ALU_VOUT, ALUA_LD_CDATA, ALUB_LD_CDATA, ALUC_LD, ALUC_OUT,
       ALUC_SRC_0, ALUC_SRC_1, ALUOP_0, ALUOP_1, ALUOP_2, ALUOP_3, ALUR_OUT_CDATA, ALUZ_OUT, and_1_out,
       and_2_out, and_3_out, and_4_out, and_5_out, and_6_out, and_7_out, and_8_out, and_9_out, and_10_out,
       and_11_out, and_12_out, and_13_out, and_15_out, and_16_out, BREAK, C, CDATA_LD_0, CDATA_LD_FF,
       CDATA_TO_CADDRH, CDATA_TO_CADDRL, Clck0, Clck1, clock_1_cout, comparator_1_gt, comparator_2_eq,
       comparator_3_eq, comparator_4_eq, comparator_5_eq, comparator_6_eq, comparator_7_eq, comparator_8_eq,
       comparator_9_eq, comparator_10_eq, comparator_11_eq, CS0, CS1, CS2, CS3, CUP_SRC_ALU, decoder_1_out_0,
       decoder_1_out_1, decoder_1_out_2, decoder_1_out_3, decoder_1_out_4, decoder_1_out_5, decoder_1_out_6,
       decoder_1_out_7, decoder_1_out_8, decoder_1_out_9, decoder_1_out_10, decoder_1_out_11,
       decoder_1_out_12, decoder_1_out_13, decoder_1_out_14, decoder_1_out_15, decoder_2_out_0,
       decoder_2_out_1, decoder_2_out_2, decoder_2_out_3, decoder_2_out_4, decoder_2_out_5, decoder_2_out_6,
       decoder_2_out_7, ERR, ERROR, HALT, HALTED, I, IR_LD_XDATA, IRQ, IRQ_out, KIRQ, lt_ALUC_gt,
       MARH_LD_CADDRH, MARL_LD_CADDRL, MBR_LD_CDATA, MBR_LD_XDATA, MBR_OUT_CDATA, MBR_OUT_XDATA,
       MEM_LD_XDATA, MEM_OUT_XDATA, multiplexer_1_out, multiplexer_3_out, multiplexer_4_out,
       multiplexer_5_out, multiplexer_6_out, multiplexer_7_out, N, nor_1_out, not_2_out, or_3_out, or_6_out,
       or_7_out, or_9_out, or_10_out, P_OUT_CDATA, P_SRC_0, P_SRC_1, P_SRC_2, PC_INC, PC_IRQ, PC_LD,
       PC_OUT_CADDR, PC_REL_CDATA, PC_RESET, PCH_LD_CDATA, PCH_OUT_CDATA, PCL_LD_CDATA, PCL_OUT_CDATA, PI_LD,
       PN_LD, PV_LD, PZ_LD, RESET, S_DEC, S_INC, S_LD_CDATA, S_OUT_CADDR, S_OUT_CDATA, STASHH_LD_CDATA,
       STASHH_OUT_CDATA, STASHL_LD_CDATA, STASHL_OUT_CDATA, STEP_out, switchdt_1_p3, TELNETIRQ, V,
       X_LD_CDATA, X_OUT_CDATA, Y_LD_CDATA, Y_OUT_CDATA, Z;
  wire [2:0] lt_uNEXTMUX_gt;
  wire [3:0] register_1_q, register_1_q_2, register_2_q, register_2_q_2;
  wire [4:0] multiplexer_8_out;
  wire [7:0] A, ALUR, CADDRH, CADDRL, CDATA, IR, keyboard_1_d, lt_ALUA_gt, lt_ALUB_gt, MARH, MARL, MBR,
       multiplexer_2_out, PCH, PCL, S, STASHH, STASHL, telnet_1_out, X, XDATA, Y;
  wire [15:0] DEMODE, DEOPCODE, lt_uCAR_gt, lt_uNEXTCAR_gt, lt_uParam_gt;
  wire [15:8] keyboard_1_d_2;

  Seven_Seg_Hex seven_seg_hex_1 (.d(MARH[3:0]), .dp(1'b0));
  Seven_Seg_Hex seven_seg_hex_2 (.d(MARH[7:4]), .dp(1'b0));
  Seven_Seg_Hex seven_seg_hex_3 (.d(A[7:4]), .dp(1'b0));
  Seven_Seg_Hex seven_seg_hex_4 (.d(MARL[3:0]), .dp(1'b0));
  Seven_Seg_Hex seven_seg_hex_5 (.d(MARL[7:4]), .dp(1'b0));
  Seven_Seg_Hex seven_seg_hex_6 (.d(A[3:0]), .dp(1'b0));
  Seven_Seg_Hex seven_seg_hex_7 (.d(X[7:4]), .dp(1'b0));
  and and_1 (and_1_out, CS3, MEM_LD_XDATA);
  Comparator #(.Bits(16)) comparator_1 (.a({MARH, MARL}), .b(16'h4007), .gt(comparator_1_gt));  // open: eq, lt
  Comparator #(.Bits(16)) comparator_2 (.a({MARH, MARL}), .b(16'h4002), .eq(comparator_2_eq));  // open: gt, lt
  Comparator #(.Bits(16)) comparator_3 (.a({MARH, MARL}), .b(16'h4003), .eq(comparator_3_eq));  // open: gt, lt
  Comparator #(.Bits(16)) comparator_4 (.a({MARH, MARL}), .b(16'h4004), .eq(comparator_4_eq));  // open: gt, lt
  Comparator #(.Bits(16)) comparator_5 (.a({MARH, MARL}), .b(16'h4005), .eq(comparator_5_eq));  // open: gt, lt
  Comparator #(.Bits(16)) comparator_6 (.a({MARH, MARL}), .b(16'h4006), .eq(comparator_6_eq));  // open: gt, lt
  Comparator #(.Bits(16)) comparator_7 (.a({MARH, MARL}), .b(16'h4007), .eq(comparator_7_eq));  // open: gt, lt
  Seven_Seg_Hex seven_seg_hex_8 (.d(MBR[7:4]), .dp(1'b0));
  Seven_Seg_Hex seven_seg_hex_9 (.d(X[3:0]), .dp(1'b0));
  Comparator #(.Bits(16)) comparator_8 (.a(MCBREAKPOINT), .b({PCH, PCL}), .eq(comparator_8_eq));  // open: gt, lt
  Comparator #(.Bits(16)) comparator_9 (.a(UCBREAKPOINT), .b(lt_uCAR_gt), .eq(comparator_9_eq));  // open: gt, lt
  and and_2 (and_2_out, CS1, comparator_1_gt);
  Button STEP (.out(STEP_out));
  Button u_RESET (.out(RESET));
  Button u_IRQ (.out(IRQ_out));
  or or_1 (IRQ, IRQ_out, KIRQ, TELNETIRQ);
  Seven_Seg_Hex seven_seg_hex_10 (.d(PCH[7:4]), .dp(1'b0));
  Seven_Seg_Hex seven_seg_hex_11 (.d(MBR[3:0]), .dp(1'b0));
  Seven_Seg_Hex seven_seg_hex_12 (.d(Y[3:0]), .dp(1'b0));
  Seven_Seg_Hex seven_seg_hex_13 (.d(Y[7:4]), .dp(1'b0));
  and and_3 (and_3_out, MCBSET, comparator_8_eq);
  and and_4 (and_4_out, UCBSET, comparator_9_eq);
  or or_2 (ERROR, ERR, and_1_out, CS2, and_2_out);
  and and_5 (and_5_out, comparator_2_eq, CS1, MEM_LD_XDATA);
  and and_6 (and_6_out, comparator_3_eq, CS1, MEM_OUT_XDATA);
  and and_7 (and_7_out, comparator_4_eq, CS1, MEM_OUT_XDATA);
  and and_8 (and_8_out, comparator_5_eq, CS1, MEM_LD_XDATA);
  and and_9 (and_9_out, comparator_6_eq, CS1, MEM_OUT_XDATA);
  and and_10 (and_10_out, comparator_7_eq, CS1, MEM_OUT_XDATA);
  or or_3 (or_3_out, HALT, ERROR, BREAK);
  // SwitchDT switchdt_1: pin names not known; wires that end beside it: FAST, SLOW, switchdt_1_p3
  Seven_Seg_Hex seven_seg_hex_14 (.d(PCL[7:4]), .dp(1'b0));
  Seven_Seg_Hex seven_seg_hex_15 (.d(PCH[3:0]), .dp(1'b0));
  assign XDATA = and_7_out ? {{7{1'b0}}, KIRQ} : 8'bz;  // Driver driver_1
  assign XDATA = and_10_out ? {{7{1'b0}}, TELNETIRQ} : 8'bz;  // Driver driver_2
  Seven_Seg_Hex seven_seg_hex_16 (.d(PCL[3:0]), .dp(1'b0));
  LED led_1 (.in(N));
  or or_4 (BREAK, and_3_out, and_4_out);
  Terminal terminal_1 (.D(XDATA), .C(Clck1), .en(and_5_out));
  Keyboard keyboard_1 (.C(Clck1), .en(and_6_out), .D({keyboard_1_d_2, keyboard_1_d}), .av(KIRQ));
  Telnet #(.port(6666)) telnet_1 (
    .in(XDATA), .C(Clck1), .wr(and_8_out), .rd(and_9_out), .out(telnet_1_out), .av(TELNETIRQ));
  Clock clock_1 (
    .RUN(RUN), .STEP(STEP_out), .HALT(or_3_out), .Cin(switchdt_1_p3), .HALTED(HALTED), .Cout(clock_1_cout));
  Seven_Seg_Hex seven_seg_hex_17 (.d(IR[3:0]), .dp(1'b0));
  Seven_Seg_Hex seven_seg_hex_18 (.d(IR[7:4]), .dp(1'b0));
  LED led_2 (.in(V));
  and and_11 (and_11_out, HALTED, RESET);
  Seven_Seg_Hex seven_seg_hex_19 (.d(STASHH[3:0]), .dp(1'b0));
  Seven_Seg_Hex seven_seg_hex_20 (.d(STASHH[7:4]), .dp(1'b0));
  LED led_3 (.in(Z));
  LED led_4 (.in(I));
  assign XDATA = and_6_out ? keyboard_1_d : 8'bz;  // Driver driver_3
  assign XDATA = and_9_out ? telnet_1_out : 8'bz;  // Driver driver_4
  or or_5 (Clck1, clock_1_cout, and_11_out);
  Seven_Seg_Hex seven_seg_hex_21 (.d(STASHL[7:4]), .dp(1'b0));
  LED led_5 (.in(C));
  Seven_Seg_Hex seven_seg_hex_22 (.d(S[7:4]), .dp(1'b0));
  Seven_Seg_Hex seven_seg_hex_23 (.d(STASHL[3:0]), .dp(1'b0));
  not not_1 (Clck0, Clck1);
  Seven_Seg_Hex seven_seg_hex_24 (.d(S[3:0]), .dp(1'b0));
  or or_6 (or_6_out, MEM_LD_XDATA, MEM_OUT_XDATA);
  Address_Decoder address_decoder_1 (.A({MARH, MARL}), .CS(or_6_out), .CS0(CS0), .CS1(CS1), .CS2(CS2), .CS3(CS3));
  Register #(.Bits(8)) MAR_H (.D(CADDRH), .C(Clck0), .en(MARH_LD_CADDRH), .Q(MARH));
  Register #(.Bits(8)) MAR_L (.D(CADDRL), .C(Clck0), .en(MARL_LD_CADDRL), .Q(MARL));
  Seven_Seg_Hex seven_seg_hex_25 (.d(DEMODE[11:8]), .dp(1'b0));
  Seven_Seg_Hex seven_seg_hex_26 (.d(DEMODE[15:12]), .dp(1'b0));
  Seven_Seg_Hex seven_seg_hex_27 (.d(lt_ALUA_gt[3:0]), .dp(1'b0));
  Seven_Seg_Hex seven_seg_hex_28 (.d(lt_ALUA_gt[7:4]), .dp(1'b0));
  Seven_Seg_Hex seven_seg_hex_29 (.d(DEMODE[3:0]), .dp(1'b0));
  Seven_Seg_Hex seven_seg_hex_30 (.d(DEMODE[7:4]), .dp(1'b0));
  Seven_Seg_Hex seven_seg_hex_31 (.d(lt_ALUB_gt[3:0]), .dp(1'b0));
  Seven_Seg_Hex seven_seg_hex_32 (.d(lt_ALUB_gt[7:4]), .dp(1'b0));
  assign CADDRH = CDATA_TO_CADDRH ? CDATA : 8'bz;  // Driver driver_5
  assign CADDRL = CDATA_TO_CADDRL ? CDATA : 8'bz;  // Driver driver_6
  nor nor_1 (nor_1_out, CDATA[0], CDATA[1], CDATA[2], CDATA[3], CDATA[4], CDATA[5], CDATA[6], CDATA[7]);
  not not_2 (not_2_out, MEM_LD_XDATA);
  Multiplexer #(.Selector_Bits(3)) multiplexer_1 (
    .sel({P_SRC_2, P_SRC_1, P_SRC_0}), .in_0(1'b0), .in_1(1'b1), .in_2(ALU_NOUT), .in_3(CDATA[7]),
    .in_4(CDATA[7]), .in_5(1'b0), .in_6(1'b0), .in_7(1'b0), .out(multiplexer_1_out));
  Seven_Seg_Hex seven_seg_hex_33 (.d(DEOPCODE[11:8]), .dp(1'b0));
  Seven_Seg_Hex seven_seg_hex_34 (.d(DEOPCODE[15:12]), .dp(1'b0));
  LED led_6 (.in(lt_ALUC_gt));
  and and_12 (and_12_out, MEM_LD_XDATA, Clck1);
  and and_13 (and_13_out, CS3, not_2_out);
  Seven_Seg_Hex seven_seg_hex_35 (.d(DEOPCODE[3:0]), .dp(1'b0));
  Seven_Seg_Hex seven_seg_hex_36 (.d(DEOPCODE[7:4]), .dp(1'b0));
  Seven_Seg_Hex seven_seg_hex_37 (.d(ALUR[3:0]), .dp(1'b0));
  Seven_Seg_Hex seven_seg_hex_38 (.d(ALUR[7:4]), .dp(1'b0));
  RAMSinglePortSel #(.AddrBits(14), .isProgramMemory("true"), .Bits(8)) RAM (
    .A({MARH[5:0], MARL}), .CS(CS0), .WE(and_12_out), .OE(MEM_OUT_XDATA), .D(XDATA));
  ROM #(.AddrBits(14), .Bits(8)) ROM (.A({MARH[5:0], MARL}), .sel(and_13_out), .D(XDATA));
  Multiplexer #(.Bits(8)) multiplexer_2 (.sel(MBR_LD_CDATA), .in_0(XDATA), .in_1(CDATA), .out(multiplexer_2_out));
  Register #(.Bits(8)) u_MBR (.D(multiplexer_2_out), .C(Clck1), .en(or_7_out), .Q(MBR));
  or or_7 (or_7_out, MBR_LD_CDATA, MBR_LD_XDATA);
  Multiplexer #(.Selector_Bits(3)) multiplexer_3 (
    .sel({P_SRC_2, P_SRC_1, P_SRC_0}), .in_0(1'b0), .in_1(1'b1), .in_2(ALU_VOUT), .in_3(1'b0),
    .in_4(CDATA[6]), .in_5(1'b0), .in_6(1'b0), .in_7(1'b0), .out(multiplexer_3_out));
  Multiplexer #(.Selector_Bits(3)) multiplexer_4 (
    .sel({P_SRC_2, P_SRC_1, P_SRC_0}), .in_0(1'b0), .in_1(1'b1), .in_2(ALUZ_OUT), .in_3(nor_1_out),
    .in_4(CDATA[1]), .in_5(1'b0), .in_6(1'b0), .in_7(1'b0), .out(multiplexer_4_out));
  Seven_Seg_Hex seven_seg_hex_39 (.d(lt_uCAR_gt[15:12]), .dp(1'b0));
  LED led_7 (.in(ALU_NOUT));
  Seven_Seg_Hex seven_seg_hex_40 (.d(lt_uCAR_gt[7:4]), .dp(1'b0));
  Seven_Seg_Hex seven_seg_hex_41 (.d(lt_uCAR_gt[11:8]), .dp(1'b0));
  LED led_8 (.in(ALU_VOUT));
  assign XDATA = MBR_OUT_XDATA ? MBR : 8'bz;  // Driver driver_7
  assign CDATA = MBR_OUT_CDATA ? MBR : 8'bz;  // Driver driver_8
  Seven_Seg_Hex seven_seg_hex_42 (.d(lt_uCAR_gt[3:0]), .dp(1'b0));
  LED led_9 (.in(ALUZ_OUT));
  LED led_10 (.in(ALUC_OUT));
  Multiplexer #(.Selector_Bits(2)) multiplexer_5 (
    .sel({ALUC_SRC_1, ALUC_SRC_0}), .in_0(1'b0), .in_1(1'b1), .in_2(C), .in_3(C), .out(multiplexer_5_out));
  Multiplexer #(.Selector_Bits(3)) multiplexer_6 (
    .sel({P_SRC_2, P_SRC_1, P_SRC_0}), .in_0(1'b0), .in_1(1'b1), .in_2(1'b0), .in_3(1'b0), .in_4(CDATA[2]),
    .in_5(1'b0), .in_6(1'b0), .in_7(1'b0), .out(multiplexer_6_out));
  Multiplexer #(.Selector_Bits(3)) multiplexer_7 (
    .sel({P_SRC_2, P_SRC_1, P_SRC_0}), .in_0(1'b0), .in_1(1'b1), .in_2(ALUC_OUT), .in_3(1'b0),
    .in_4(CDATA[0]), .in_5(1'b0), .in_6(1'b0), .in_7(1'b0), .out(multiplexer_7_out));
  Seven_Seg_Hex seven_seg_hex_43 (.d(lt_uNEXTCAR_gt[11:8]), .dp(1'b0));
  Seven_Seg_Hex seven_seg_hex_44 (.d(lt_uNEXTCAR_gt[15:12]), .dp(1'b0));
  Seven_Seg_Hex seven_seg_hex_45 (.d(lt_uNEXTCAR_gt[3:0]), .dp(1'b0));
  Seven_Seg_Hex seven_seg_hex_46 (.d(lt_uNEXTCAR_gt[7:4]), .dp(1'b0));
  Decoder #(.Selector_Bits(4)) decoder_1 (
    .sel({ALUOP_3, ALUOP_2, ALUOP_1, ALUOP_0}), .out_0(decoder_1_out_0), .out_1(decoder_1_out_1),
    .out_2(decoder_1_out_2), .out_3(decoder_1_out_3), .out_4(decoder_1_out_4), .out_5(decoder_1_out_5),
    .out_6(decoder_1_out_6), .out_7(decoder_1_out_7), .out_8(decoder_1_out_8), .out_9(decoder_1_out_9),
    .out_10(decoder_1_out_10), .out_11(decoder_1_out_11), .out_12(decoder_1_out_12),
    .out_13(decoder_1_out_13), .out_14(decoder_1_out_14), .out_15(decoder_1_out_15));
  LED AND_14 (.in(decoder_1_out_0));
  LED OR_8 (.in(decoder_1_out_1));
  LED NOT_3 (.in(decoder_1_out_2));
  LED XOR (.in(decoder_1_out_3));
  LED ADD (.in(decoder_1_out_4));
  LED SUB (.in(decoder_1_out_5));
  LED INC (.in(decoder_1_out_6));
  LED DEC (.in(decoder_1_out_7));
  LED SHIFTR (.in(decoder_1_out_8));
  LED SHIFTL (.in(decoder_1_out_9));
  LED ROTR (.in(decoder_1_out_10));
  LED ROTL (.in(decoder_1_out_11));
  LED N_A (.in(decoder_1_out_12));
  LED N_A_2 (.in(decoder_1_out_13));
  LED N_A_3 (.in(decoder_1_out_14));
  LED N_A_4 (.in(decoder_1_out_15));
  Latched_ALU ALU (
    .Clock(Clck1), .A(CDATA), .B(CDATA), .Cin(multiplexer_5_out), .LDA(ALUA_LD_CDATA), .LDB(ALUB_LD_CDATA),
    .LDC(ALUC_LD), .OP({ALUOP_3, ALUOP_2, ALUOP_1, ALUOP_0}), .N(ALU_NOUT), .V(ALU_VOUT), .Z(ALUZ_OUT),
    .C(ALUC_OUT), .R(ALUR), .lt_A_gt(lt_ALUA_gt), .lt_B_gt(lt_ALUB_gt), .lt_C_gt(lt_ALUC_gt));
  Register PN (.D(multiplexer_1_out), .C(Clck1), .en(PN_LD), .Q(N));
  Register PV (.D(multiplexer_3_out), .C(Clck1), .en(PV_LD), .Q(V));
  Register PI (.D(multiplexer_6_out), .C(Clck1), .en(PI_LD), .Q(I));
  Register PZ (.D(multiplexer_4_out), .C(Clck1), .en(PZ_LD), .Q(Z));
  Register PC (.D(multiplexer_7_out), .C(Clck1), .en(PC_LD), .Q(C));
  Seven_Seg_Hex seven_seg_hex_47 (.d(lt_uParam_gt[15:12]), .dp(1'b0));
  Register #(.Bits(8)) u_IR (.D(XDATA), .C(Clck1), .en(IR_LD_XDATA), .Q(IR));
  Seven_Seg_Hex seven_seg_hex_48 (.d(lt_uParam_gt[7:4]), .dp(1'b0));
  Seven_Seg_Hex seven_seg_hex_49 (.d(lt_uParam_gt[11:8]), .dp(1'b0));
  Seven_Seg_Hex seven_seg_hex_50 (.d(lt_uParam_gt[3:0]), .dp(1'b0));
  Comparator #(.Bits(16)) comparator_10 (.a({MARH, MARL}), .b(16'h4001), .eq(comparator_10_eq));  // open: gt, lt
  Seven_Seg_Hex seven_seg_hex_51 (.d(register_1_q_2), .dp(1'b0));
  assign CDATA = ALUR_OUT_CDATA ? ALUR : 8'bz;  // Driver driver_9
  Decoder #(.Selector_Bits(3)) decoder_2 (
    .sel(lt_uNEXTMUX_gt), .out_0(decoder_2_out_0), .out_1(decoder_2_out_1), .out_2(decoder_2_out_2),
    .out_3(decoder_2_out_3), .out_4(decoder_2_out_4), .out_5(decoder_2_out_5), .out_6(decoder_2_out_6),
    .out_7(decoder_2_out_7));
  Seven_Seg_Hex seven_seg_hex_52 (.d(register_1_q), .dp(1'b0));
  Register #(.Bits(8)) register_1 (.D(XDATA), .C(Clck1), .en(and_15_out), .Q({register_1_q_2, register_1_q}));
  and and_15 (and_15_out, comparator_10_eq, CS1);
  Comparator #(.Bits(16)) comparator_11 (.a({MARH, MARL}), .b(16'h4000), .eq(comparator_11_eq));  // open: gt, lt
  or or_9 (or_9_out, S_LD_CDATA, S_INC, S_DEC);
  Multiplexer #(.Bits(5)) multiplexer_8 (
    .sel(CUP_SRC_ALU), .in_0({C, Z, I, V, N}), .in_1({ALUC_OUT, ALUZ_OUT, I, ALU_VOUT, ALU_NOUT}),
    .out(multiplexer_8_out));
  Seven_Seg_Hex seven_seg_hex_53 (.d(register_2_q), .dp(1'b0));
  Seven_Seg_Hex seven_seg_hex_54 (.d(register_2_q_2), .dp(1'b0));
  and and_16 (and_16_out, comparator_11_eq, CS1);
  CounterPreset #(.Bits(8)) u_S (
    .en(or_9_out), .C(Clck1), .dir(S_DEC), .in(CDATA), .ld(S_LD_CDATA), .clr(1'b0), .out(S));  // open: ovf
  Register u_STASHH (.C(Clck1), .D(CDATA), .OUT(STASHH_OUT_CDATA), .LD(STASHH_LD_CDATA), .Q(CDATA), .lt_Q_gt(STASHH));
  or or_10 (or_10_out, decoder_2_out_4, decoder_2_out_5, decoder_2_out_6, decoder_2_out_7);
  Register #(.Bits(8)) register_2 (.D(XDATA), .C(Clck1), .en(and_16_out), .Q({register_2_q_2, register_2_q}));
  // Control_Unit Control_Unit: pin names not known; wires that end beside it: DEMODE, DEOPCODE, multiplexer_8_out[0], multiplexer_8_out[1], multiplexer_8_out[2], multiplexer_8_out[3], multiplexer_8_out[4], RESET, IRQ, Clck1, lt_uCAR_gt, lt_uParam_gt, lt_uNEXTCAR_gt, lt_uNEXTMUX_gt, HALT, CDATA_LD_0, CDATA_LD_FF, CDATA_TO_CADDRL, CDATA_TO_CADDRH, MEM_LD_XDATA, MEM_OUT_XDATA, IR_LD_XDATA, MBR_LD_XDATA, MBR_OUT_XDATA, MBR_LD_CDATA
  LED plus_1 (.in(decoder_2_out_0));
  LED p0 (.in(decoder_2_out_1));
  LED p1 (.in(decoder_2_out_2));
  LED p2 (.in(decoder_2_out_3));
  LED uJMPs (.in(or_10_out));
  assign CADDRH = S_OUT_CADDR ? 8'h1 : 8'bz;  // Driver driver_10
  Instruction_Decoder Instruction_Decoder (.OPCODE(IR), .MODEADDR(DEMODE), .OPCODEADDR(DEOPCODE));
  assign CADDRL = S_OUT_CADDR ? S : 8'bz;  // Driver driver_11
  Register u_STASHL (.C(Clck1), .D(CDATA), .OUT(STASHL_OUT_CDATA), .LD(STASHL_LD_CDATA), .Q(CDATA), .lt_Q_gt(STASHL));
  LED led_11 (.in(HALTED));
  LED led_12 (.in(ERROR));
  LED led_13 (.in(BREAK));
  assign CDATA = S_OUT_CDATA ? S : 8'bz;  // Driver driver_12
  Seven_Seg_Hex seven_seg_hex_55 (.d(MCBREAKPOINT[11:8]), .dp(1'b0));
  Seven_Seg_Hex seven_seg_hex_56 (.d(MCBREAKPOINT[15:12]), .dp(1'b0));
  Seven_Seg_Hex seven_seg_hex_57 (.d(UCBREAKPOINT[11:8]), .dp(1'b0));
  Seven_Seg_Hex seven_seg_hex_58 (.d(UCBREAKPOINT[15:12]), .dp(1'b0));
  Register u_A (.C(Clck1), .D(CDATA), .OUT(A_OUT_CDATA), .LD(A_LD_CDATA), .Q(CDATA), .lt_Q_gt(A));
  Seven_Seg_Hex seven_seg_hex_59 (.d(MCBREAKPOINT[3:0]), .dp(1'b0));
  Seven_Seg_Hex seven_seg_hex_60 (.d(MCBREAKPOINT[7:4]), .dp(1'b0));
  Seven_Seg_Hex seven_seg_hex_61 (.d(UCBREAKPOINT[3:0]), .dp(1'b0));
  Seven_Seg_Hex seven_seg_hex_62 (.d(UCBREAKPOINT[7:4]), .dp(1'b0));
  // PC PC_2: pin names not known; wires that end beside it: PCH_LD_CDATA, PCL_LD_CDATA, PC_INC, PC_REL_CDATA, CDATA, Clck1, PC_RESET, PC_IRQ, PCH, PCL
  Register u_X (.C(Clck1), .D(CDATA), .OUT(X_OUT_CDATA), .LD(X_LD_CDATA), .Q(CDATA), .lt_Q_gt(X));
  assign CDATA = P_OUT_CDATA ? {N, V, 3'b000, I, Z, C} : 8'bz;  // Driver driver_13
  assign CDATA = PCH_OUT_CDATA ? PCH : 8'bz;  // Driver driver_14
  assign CADDRH = PC_OUT_CADDR ? PCH : 8'bz;  // Driver driver_15
  Register u_Y (.C(Clck1), .D(CDATA), .OUT(Y_OUT_CDATA), .LD(Y_LD_CDATA), .Q(CDATA), .lt_Q_gt(Y));
  assign CADDRL = PC_OUT_CADDR ? PCL : 8'bz;  // Driver driver_16
  assign CDATA = PCL_OUT_CDATA ? PCL : 8'bz;  // Driver driver_17
  assign CDATA = CDATA_LD_0 ? {8{1'b0}} : 8'bz;  // Driver driver_18
  assign CDATA = CDATA_LD_FF ? {8{1'b1}} : 8'bz;  // Driver driver_19

  // Other names for the same wires on the sheet: XADDR[15:0] = {MARH, MARL}

  // Notes on the sheet:
  //   MCBREAKPOINT: default 65535
  //   UCBREAKPOINT: default 65535
  //   FAST: Hz: 500
  //   SLOW: Hz: 50
  //   CPU
  //   MAR
  //   A
  //   Breakpoints
  //   Error Conditions
  //   Memory Mapped IO
  //   Terminal
  //   Keyboard
  //   Telnet
  //   Clock
  //   MBR
  //   X
  //   Y
  //   PC
  //   P
  //   N
  //   IR
  //   V
  //   I
  //   STASH
  //   Z
  //   STASHL
  //   C
  //   ROM/RAM Interfacing
  //   S
  //   XADDR Bus
  //   CADDRH Bus
  //   CADDRL Bus
  //   Bank Selection
  //   Status Flags Processing
  //   P load source
  //   0 0 0 reset
  //   0 0 1 set
  //   0 1 0 ALU
  //   0 1 1 Processed CDATA
  //   1 0 0 Raw CDATA
  //   1 x x N/A
  //   RAW bit order: NV-BDIZC
  //   Instruction Decoder
  //   (p1) Decoded Mode
  //   ALU
  //   ALUA
  //   ALUB
  //   ROM/RAM Banks
  //   ALUC
  //   (p2) Decoded OpCode
  //   XDATA Bus
  //   CDATA Bus
  //   ALUOUT
  //   contents of ROM (hex, n*v repeats v):
  //   a9,42,16379*0,2
  //   ALU operation
  //   0 0 0 0 AND
  //   0 0 0 1 OR
  //   0 0 1 0 NOT
  //   0 0 1 1 XOR
  //   0 1 0 0 ADD
  //   0 1 0 1 SUB
  //   0 1 1 0 INC
  //   0 1 1 1 DEC
  //   1 0  0 0 SHIFT-R
  //   1 0 0 1 SHIFT-L
  //   1 0 1 0 ROT-R
  //   1 0 1 1 ROT-L
  //   ALUC Load Source
  //   0 0   0
  //   0 1   1
  //   1 0   P
  //   1 1    P
  //   Control Unit
  //   uCAR
  //   uNext CAR
  //   OP
  //   uParam
  //   S (Stack Pointer)
  //   In/out CDATA out CADDR
  //   NextMux
  //   POSTH
  //   POSTL
  //   HALTED
  //   ERROR
  //   BREAKPOINT
  //   General Purpose Registers
  //   MC Breakpoint
  //   UC Breakpoint
  //   PC - In/out CDATA out CADDR
  //   Used for initialisation/reset
endmodule
