// Digital circuit Clock.dig as structural Verilog
module Clock (
  input  RUN,
  input  STEP,
  input  HALT,
  input  Cin,
  output HALTED,
  output Cout
);

  wire and_2_out, not_1_out, RUNNING;

  not not_1 (not_1_out, HALT);
  not not_2 (HALTED, RUNNING);
  and and_1 (RUNNING, not_1_out, RUN);
  and and_2 (and_2_out, Cin, RUNNING);
  or or_1 (Cout, STEP, and_2_out);
endmodule
