// Digital circuit Control Unit.dig as structural Verilog
module Control_Unit (
  input  [15:0] MODEADDR,
  input  [15:0] OPCODEADDR,
  input  N,
  input  V,
  input  B,
  input  I,
  input  Z,
  input  C,
  input  RESET,
  input  IRQ,
  input  CLOCK,
  output CDATA_LD_0,
  output CDATA_LD_FF,
  output CDATA_TO_CADDRL,
  output CD_TO_CADDRH,
  output MEM_LD_XDATA,
  output MEM_OUT_XDATA,
  output IR_LD_XDATA,
  output MBR_LD_XDATA,
  output MBR_OUT_XDATA,
  output MBR_LD_CDATA,
  output MBR_OUT_CDATA,
  output MARL_LD_CADDRL,
  output MARH_LD_CADDRH,
  output PC_INC,
  output PC_REL_CDATA,
  output PCL_LD_CDATA,
  output PCL_OUT_CDATA,
  output PCH_LD_CDATA,
  output PCH_OUT_CDATA,
  output PC_OUT_CADDR,
  output STASHL_LD_CDATA,
  output STASHL_OUT_CDATA,
  output STASHH_LD_CDATA,
  output STASHH_OUT_CDATA,
  output A_LD_CDATA,
  output A_OUT_CDATA,
  output X_LD_CDATA,
  output X_OUT_CDATA,
  output Y_LD_CDATA,
  output Y_OUT_CDATA,
  output PN_LD,
  output PV_LD,
  output PI_LD,
  output PZ_LD,
  output PC_LD,
  output P_SRC_0,
  output P_SRC_1,
  output P_SRC_2,
  output P_OUT_CDATA,
  output ALUA_LD_CDATA,
  output ALUB_LD_CDATA,
  output ALUC_LD,
  output ALUR_OUT_CDATA,
  output ALUC_SRC_0,
  output ALUC_SRC_1,
  output ALUOP_0,
  output ALUOP_1,
  output ALUOP_2,
  output ALUOP_3,
  output S_INC,
  output S_DEC,
  output S_LD_CDATA,
  output S_OUT_CDATA,
  output S_OUT_CADDR,
  output CUP_SRC_ALU,
  output CPU_RESET,
  output CPU_HALT,
  output CPU_IRQ,
  output CPU_ERR,
  output [15:0] lt_CAR_gt,
  output [15:0] lt_UPARAM_gt,
  output [15:0] lt_CARNEXT_gt,
  output [2:0] lt_CARNEXTSRC_gt,
  output PB_LD
);

  wire and_1_out, and_2_out, and_3_out, and_4_out, and_5_out, and_6_out, decoder_1_out_0, decoder_1_out_1,
       decoder_1_out_2, decoder_1_out_3, decoder_1_out_4, decoder_1_out_5, decoder_1_out_6, decoder_1_out_7,
       not_1_out, not_2_out, uCJMP, uIRQINIT, uJMP, uJMPINV, uNJMP, uP0, uP0INIT, uP1, uP2, uVJMP, uZJMP,
       xor_1_out, xor_2_out, xor_3_out, xor_4_out;
  wire [15:0] CAR_Adder_s, IRQ_uCode_q, multiplexer_2_out, p0__Fetch_q;
  wire [15:6] uCode_5_d;

  Seven_Seg_Hex seven_seg_hex_1 (.d(lt_CAR_gt[15:12]), .dp(1'b0));
  Seven_Seg_Hex seven_seg_hex_2 (.d(lt_CAR_gt[7:4]), .dp(1'b0));
  Seven_Seg_Hex seven_seg_hex_3 (.d(lt_CAR_gt[11:8]), .dp(1'b0));
  Seven_Seg_Hex seven_seg_hex_4 (.d(lt_CAR_gt[3:0]), .dp(1'b0));
  Seven_Seg_Hex seven_seg_hex_5 (.d(lt_CARNEXT_gt[11:8]), .dp(1'b0));
  Seven_Seg_Hex seven_seg_hex_6 (.d(lt_CARNEXT_gt[15:12]), .dp(1'b0));
  Seven_Seg_Hex seven_seg_hex_7 (.d(lt_CARNEXT_gt[3:0]), .dp(1'b0));
  Seven_Seg_Hex seven_seg_hex_8 (.d(lt_CARNEXT_gt[7:4]), .dp(1'b0));
  Seven_Seg_Hex seven_seg_hex_9 (.d(lt_UPARAM_gt[15:12]), .dp(1'b0));
  Seven_Seg_Hex seven_seg_hex_10 (.d(lt_UPARAM_gt[7:4]), .dp(1'b0));
  Seven_Seg_Hex seven_seg_hex_11 (.d(lt_UPARAM_gt[11:8]), .dp(1'b0));
  Seven_Seg_Hex seven_seg_hex_12 (.d(lt_UPARAM_gt[3:0]), .dp(1'b0));
  Decoder #(.Selector_Bits(3)) decoder_1 (
    .sel(lt_CARNEXTSRC_gt), .out_0(decoder_1_out_0), .out_1(decoder_1_out_1), .out_2(decoder_1_out_2),
    .out_3(decoder_1_out_3), .out_4(decoder_1_out_4), .out_5(decoder_1_out_5), .out_6(decoder_1_out_6),
    .out_7(decoder_1_out_7));
  LED plus_1 (.in(decoder_1_out_0));
  LED p0 (.in(decoder_1_out_1));
  LED p1 (.in(decoder_1_out_2));
  LED p2 (.in(decoder_1_out_3));
  LED uJMPs (.in(decoder_1_out_4));
  LED u_IRQ (.in(decoder_1_out_5));
  LED N_A (.in(decoder_1_out_6));
  LED N_A_2 (.in(decoder_1_out_7));
  Comparator #(.Bits(16)) Error_Detection (.a(lt_CAR_gt), .b({16{1'b1}}), .eq(CPU_ERR));  // open: gt, lt
  ROM #(.AddrBits(16), .Bits(16)) uCode0 (.A(lt_CAR_gt), .sel(1'b1), .D(lt_UPARAM_gt));
  ROM #(.AddrBits(16), .Bits(16)) uCode1 (
    .A(lt_CAR_gt), .sel(1'b1),
    .D({MEM_LD_XDATA, CD_TO_CADDRH, CDATA_TO_CADDRL, CDATA_LD_FF, CDATA_LD_0, uJMPINV, uCJMP, uZJMP, uVJMP, uNJMP, uJMP, uP2, uP1, uP0, uIRQINIT, uP0INIT}));
  ROM #(.AddrBits(16), .Bits(16)) uCode2 (
    .A(lt_CAR_gt), .sel(1'b1),
    .D({STASHL_LD_CDATA, PC_OUT_CADDR, PCH_OUT_CDATA, PCH_LD_CDATA, PCL_OUT_CDATA, PCL_LD_CDATA, PC_REL_CDATA, PC_INC, MARH_LD_CADDRH, MARL_LD_CADDRL, MBR_OUT_CDATA, MBR_LD_CDATA, MBR_OUT_XDATA, MBR_LD_XDATA, IR_LD_XDATA, MEM_OUT_XDATA}));
  ROM #(.AddrBits(16), .Bits(16)) uCode3 (
    .A(lt_CAR_gt), .sel(1'b1),
    .D({P_SRC_1, P_SRC_0, PC_LD, PZ_LD, PI_LD, PV_LD, PN_LD, Y_OUT_CDATA, Y_LD_CDATA, X_OUT_CDATA, X_LD_CDATA, A_OUT_CDATA, A_LD_CDATA, STASHH_OUT_CDATA, STASHH_LD_CDATA, STASHL_OUT_CDATA}));
  ROM #(.AddrBits(16), .Bits(16)) uCode4 (
    .A(lt_CAR_gt), .sel(1'b1),
    .D({S_OUT_CDATA, S_LD_CDATA, S_DEC, S_INC, ALUOP_3, ALUOP_2, ALUOP_1, ALUOP_0, ALUC_SRC_1, ALUC_SRC_0, ALUR_OUT_CDATA, ALUC_LD, ALUB_LD_CDATA, ALUA_LD_CDATA, P_OUT_CDATA, P_SRC_2}));
  ROM #(.AddrBits(16), .Bits(16)) uCode_5 (
    .A(lt_CAR_gt), .sel(1'b1), .D({uCode_5_d, PB_LD, CPU_IRQ, CPU_HALT, CPU_RESET, CUP_SRC_ALU, S_OUT_CADDR}));
  and and_1 (and_1_out, not_1_out, IRQ, uP0);
  not not_1 (not_1_out, I);
  Register #(.Bits(16)) CAR (.D(lt_CARNEXT_gt), .C(CLOCK), .en(1'b1), .Q(lt_CAR_gt));
  Add #(.Bits(16)) CAR_Adder (.a(lt_CAR_gt), .b(16'h1), .c_i(1'b0), .s(CAR_Adder_s));  // open: c_o
  or or_1 (lt_CARNEXTSRC_gt[2], and_1_out, uJMP, and_2_out, and_3_out, and_4_out, and_5_out);
  and and_2 (and_2_out, uZJMP, xor_1_out);
  xor xor_1 (xor_1_out, Z, uJMPINV);
  Register #(.Bits(16)) p0__Fetch (.D(lt_UPARAM_gt), .C(CLOCK), .en(uP0INIT), .Q(p0__Fetch_q));
  Register #(.Bits(16)) IRQ_uCode (.D(lt_UPARAM_gt), .C(CLOCK), .en(uIRQINIT), .Q(IRQ_uCode_q));
  and and_3 (and_3_out, uNJMP, xor_2_out);
  xor xor_2 (xor_2_out, N, uJMPINV);
  and and_4 (and_4_out, uVJMP, xor_3_out);
  xor xor_3 (xor_3_out, V, uJMPINV);
  Multiplexer #(.Bits(16)) multiplexer_1 (
    .sel(RESET), .in_0(multiplexer_2_out), .in_1({16{1'b0}}), .out(lt_CARNEXT_gt));
  Multiplexer #(.Selector_Bits(3), .Bits(16)) multiplexer_2 (
    .sel(lt_CARNEXTSRC_gt), .in_0(CAR_Adder_s), .in_1(p0__Fetch_q), .in_2(MODEADDR), .in_3(OPCODEADDR),
    .in_4(lt_UPARAM_gt), .in_5(IRQ_uCode_q), .in_6({16{1'b0}}), .in_7({16{1'b0}}), .out(multiplexer_2_out));
  or or_2 (lt_CARNEXTSRC_gt[1], uP1, uP2);
  and and_5 (and_5_out, uCJMP, xor_4_out);
  xor xor_4 (xor_4_out, C, uJMPINV);
  or or_3 (lt_CARNEXTSRC_gt[0], uP0, uP2, and_6_out);
  and and_6 (and_6_out, not_2_out, IRQ, uP0);
  not not_2 (not_2_out, I);

  // Other names for the same wires on the sheet: CARNEXTSRC[2:0] = lt_CARNEXTSRC_gt; CDATA_TO_CADDRH = CD_TO_CADDRH;
  //   CAR[15:0] = lt_CAR_gt; CARNEXT[15:0] = lt_CARNEXT_gt; UPARAM[15:0] = lt_UPARAM_gt

  // Notes on the sheet:
  //   MODEADDR: default 169
  //   OPCODEADDR: default 169
  //   CAR
  //   CARNEXT
  //   UPARAM
  //   Debug
  //   CARNEXTSRC
  //   contents of uCode0 (hex, n*v repeats v):
  //   6000000,18000000,6000000,30000000,c0000000
  //   contents of uCode1 (hex, n*v repeats v):
  //   6000000,18000000,6000000,30000000,c0000000
  //   contents of uCode2 (hex, n*v repeats v):
  //   6000000,18000000,6000000,30000000,c0000000
  //   contents of uCode3 (hex, n*v repeats v):
  //   6000000,18000000,6000000,30000000,c0000000
  //   contents of uCode4 (hex, n*v repeats v):
  //   6000000,18000000,6000000,30000000,c0000000
  //   contents of uCode_5 (hex, n*v repeats v):
  //   6000000,18000000,6000000,30000000,c0000000
  //   Next Mux
  //   0 0 0 +1
  //   0 0 1 p0
  //   0 1 0 p1
  //   0 1 1 p2
  //   1 0 0 uJMPs
  //   1 0 1 IRQ
  //   1 1 x N/A
endmodule
