// Digital circuit Latched ALU.dig as structural Verilog
module Latched_ALU (
  input  Clock,
  input  [7:0] A,
  input  [7:0] B,
  input  Cin,
  input  LDA,
  input  LDB,
  input  LDC,
  input  [3:0] OP,
  output N,
  output V,
  output Z,
  output C,
  output [7:0] R,
  output [7:0] lt_A_gt,
  output [7:0] lt_B_gt,
  output lt_C_gt
);

  wire ALU_nout, ALU_vout, shifter_1_cout;
  wire [7:0] ALU_out, shifter_1_q;

  Register #(.Bits(8)) u_A (.D(A), .C(Clock), .en(LDA), .Q(lt_A_gt));
  Register #(.Bits(8)) u_B (.D(B), .C(Clock), .en(LDB), .Q(lt_B_gt));
  Register u_C (.D(Cin), .C(Clock), .en(LDC), .Q(lt_C_gt));
  Shifter shifter_1 (.D(lt_A_gt), .OP(OP[1]), .DIR(OP[0]), .Cin(lt_C_gt), .Q(shifter_1_q), .COUT(shifter_1_cout));
  ALU ALU (
    .A(lt_A_gt), .B(lt_B_gt), .OP(OP[2:0]), .Cin(lt_C_gt), .Out(ALU_out), .Nout(ALU_nout), .Vout(ALU_vout));  // open: Zout, Cout
  Multiplexer #(.Bits(8)) multiplexer_1 (.sel(OP[3]), .in_0(ALU_out), .in_1(shifter_1_q), .out({N, R[6:0]}));
  Comparator #(.Bits(8)) comparator_1 (.a({N, R[6:0]}), .b({8{1'b0}}), .eq(Z));  // open: gt, lt
  Multiplexer multiplexer_2 (.sel(OP[3]), .in_0(ALU_nout), .in_1(1'b0), .out(V));
  Multiplexer multiplexer_3 (.sel(OP[3]), .in_0(ALU_vout), .in_1(shifter_1_cout), .out(C));

  assign R[7] = N;

  // Notes on the sheet:
  //   ALU operation
  //   0 0 0 0 AND
  //   0 0 0 1 OR
  //   0 0 1 0 NOT
  //   0 0 1 1 XOR
  //   0 1 0 0 ADD
  //   0 1 0 1 SUB
  //   0 1 1 0 INC
  //   0 1 1 1 DEC
  //   1 0  0 0 SHIFT-R
  //   1 0 0 1 SHIFT-L
  //   1 0 1 0 ROT-R
  //   1 0 1 1 ROT-L
endmodule
