// Digital circuit Memory.dig as structural Verilog
module Memory (
  input  MEM_LD_XDATA,
  input  MEM_OUT_XDATA,
  input  [15:0] XADDR,
  input  Clock,
  output [7:0] XDATA
);

  wire and_1_out, and_2_out, and_3_out, not_1_out, or_1_out;

  and and_1 (and_1_out, XADDR[15], MEM_OUT_XDATA);
  or or_1 (or_1_out, MEM_LD_XDATA, MEM_OUT_XDATA);
  not not_1 (not_1_out, XADDR[15]);
  ROM #(.AddrBits(14), .Bits(8)) ROM (.A(XADDR[13:0]), .sel(and_1_out), .D(XDATA));
  and and_2 (and_2_out, or_1_out, not_1_out);
  and and_3 (and_3_out, MEM_LD_XDATA, Clock);
  RAMSinglePortSel #(.AddrBits(14), .isProgramMemory("true"), .Bits(8)) RAM (
    .A(XADDR[13:0]), .CS(and_2_out), .WE(and_3_out), .OE(MEM_OUT_XDATA), .D(XDATA));

  // Notes on the sheet:
  //   High bit 
  //     set => ROM
  //     unset => RAM
  //   contents of ROM (hex, n*v repeats v):
  //   a9,42
  //   XDATA Bus
endmodule
