// Digital circuit PC.dig as structural Verilog
module PC (
);

  wire Clock, or_1_out, or_2_out, PC_INC, PC_LD_ADD, PC_OUT_CADDR, PCADDL_c_o, PCH_LD_CDATA, PCH_OUT_CDATA,
       PCL_LD_CDATA, PCL_OUT_CDATA;
  wire [7:0] CADDRH, CADDRL, CDATA, multiplexer_1_out, multiplexer_2_out, multiplexer_3_out, PCADDH_s,
       PCADDL_s, PCH, PCL;

  Multiplexer #(.Bits(8)) multiplexer_1 (.sel(PC_LD_ADD), .in_0(CDATA), .in_1(PCADDH_s), .out(multiplexer_1_out));
  assign CDATA = PCH_OUT_CDATA ? PCH : 8'bz;  // Driver driver_1
  or or_1 (or_1_out, PC_LD_ADD, PCH_LD_CDATA);
  Add #(.Bits(8)) PCADDH (.a(PCH), .b({8{1'b0}}), .c_i(PCADDL_c_o), .s(PCADDH_s));  // open: c_o
  Register #(.Bits(8)) u_PCH (.D(multiplexer_1_out), .C(Clock), .en(or_1_out), .Q(PCH));
  assign CADDRH = PC_OUT_CADDR ? PCH : 8'bz;  // Driver driver_2
  Multiplexer #(.Bits(8)) multiplexer_2 (.sel(PC_LD_ADD), .in_0(CDATA), .in_1(PCADDL_s), .out(multiplexer_2_out));
  Multiplexer #(.Bits(8)) multiplexer_3 (.sel(PC_INC), .in_0(CDATA), .in_1(8'h1), .out(multiplexer_3_out));
  Add #(.Bits(8)) PCADDL (.a(PCL), .b(multiplexer_3_out), .c_i(1'b0), .s(PCADDL_s), .c_o(PCADDL_c_o));
  assign CDATA = PCL_OUT_CDATA ? PCL : 8'bz;  // Driver driver_3
  or or_2 (or_2_out, PC_LD_ADD, PCL_LD_CDATA);
  Register #(.Bits(8)) u_PCL (.D(multiplexer_2_out), .C(Clock), .en(or_2_out), .Q(PCL));
  assign CADDRL = PC_OUT_CADDR ? PCL : 8'bz;  // Driver driver_4

  // Notes on the sheet:
  //   PC load source
  //   0 CDATA
  //   1 ADDER
  //   PC - In/out CDATA out CADDR
  //   PC Adder load source
  //   00 CADDR
  //   01 1 (INC)
endmodule
