// Digital circuit Register.dig as structural Verilog
module Register (
  input  C,
  input  [7:0] D,
  input  OUT,
  input  LD,
  output [7:0] Q,
  output [7:0] lt_Q_gt
);

  Register #(.Bits(8)) register_1 (.D(D), .C(C), .en(LD), .Q(lt_Q_gt));
  assign Q = OUT ? lt_Q_gt : 8'bz;  // Driver driver_1
endmodule
