// Digital circuit Shifter.dig as structural Verilog
module Shifter (
  input  [7:0] D,
  input  [1:0] OP,
  input  DIR,
  input  Cin,
  output [7:0] Q,
  output COUT
);

  wire and_1_out, and_2_out, and_3_out, and_4_out, and_5_out, and_6_out, and_7_out, and_8_out, and_9_out,
       and_10_out, and_11_out, and_12_out, and_13_out, and_14_out, and_15_out, and_16_out, and_17_out,
       and_18_out, and_19_out, and_20_out, R;

  and and_1 (and_1_out, D[6], DIR);
  or or_1 (Q[7], and_3_out, and_1_out);
  and and_2 (and_2_out, Cin, OP[0]);
  and and_3 (and_3_out, and_2_out, R);
  and and_4 (and_4_out, D[5], DIR);
  and and_5 (and_5_out, D[7], R);
  or or_2 (Q[6], and_5_out, and_4_out);
  and and_6 (and_6_out, D[4], DIR);
  not not_1 (R, DIR);
  and and_7 (and_7_out, D[6], R);
  or or_3 (Q[5], and_7_out, and_6_out);
  and and_8 (and_8_out, D[3], DIR);
  or or_4 (Q[4], and_9_out, and_8_out);
  and and_9 (and_9_out, D[5], R);
  and and_10 (and_10_out, D[2], DIR);
  or or_5 (Q[3], and_11_out, and_10_out);
  and and_11 (and_11_out, D[4], R);
  LED led_1 (.in(D[7]));
  LED led_2 (.in(D[6]));
  LED led_3 (.in(Q[7]));
  LED led_4 (.in(Q[6]));
  and and_12 (and_12_out, D[1], DIR);
  LED led_5 (.in(D[5]));
  LED led_6 (.in(D[4]));
  LED led_7 (.in(Q[5]));
  LED led_8 (.in(Q[4]));
  and and_13 (and_13_out, D[3], R);
  or or_6 (Q[2], and_13_out, and_12_out);
  LED led_9 (.in(D[3]));
  LED led_10 (.in(D[2]));
  LED led_11 (.in(Q[3]));
  LED led_12 (.in(Q[2]));
  and and_14 (and_14_out, D[0], DIR);
  LED led_13 (.in(D[1]));
  LED led_14 (.in(D[0]));
  LED led_15 (.in(Q[1]));
  LED led_16 (.in(Q[0]));
  and and_15 (and_15_out, D[2], R);
  or or_7 (Q[1], and_15_out, and_14_out);
  LED led_17 (.in(Cin));
  LED led_18 (.in(COUT));
  and and_16 (and_16_out, Cin, OP[0]);
  and and_17 (and_17_out, and_16_out, DIR);
  or or_8 (Q[0], and_18_out, and_17_out);
  and and_18 (and_18_out, D[1], R);
  and and_19 (and_19_out, D[7], DIR);
  or or_9 (COUT, and_20_out, and_19_out);
  and and_20 (and_20_out, D[0], R);
  // Pins of 1 and 2 bits meet at OP

  // Other names for the same wires on the sheet: L = DIR; ROT[1:0] = OP

  // Notes on the sheet:
  //   0 SHIFT
  //   1 ROT
  //   0 R
  //   1 L
endmodule
