// Digital circuit Stack Register.dig as structural Verilog
module Stack_Register (
  input  C,
  input  INC,
  input  DEC,
  input  [7:0] D,
  input  LD,
  input  OUT,
  output [7:0] QH,
  output [7:0] QL,
  output [7:0] lt_QL_gt
);

  wire or_1_out;
  wire [7:0] add_1_s, multiplexer_1_out, multiplexer_2_out;

  Multiplexer #(.Bits(8)) multiplexer_1 (.sel(LD), .in_0(add_1_s), .in_1(D), .out(multiplexer_1_out));
  or or_1 (or_1_out, INC, DEC, LD);
  assign QH = OUT ? 8'h1 : 8'bz;  // Driver driver_1
  Multiplexer #(.Bits(8)) multiplexer_2 (.sel(DEC), .in_0(8'h1), .in_1({8{1'b1}}), .out(multiplexer_2_out));
  Register #(.Bits(8)) S (.D(multiplexer_1_out), .C(C), .en(or_1_out), .Q(lt_QL_gt));
  Add #(.Bits(8)) add_1 (.a(multiplexer_2_out), .b(lt_QL_gt), .c_i(1'b0), .s(add_1_s));  // open: c_o
  assign QL = OUT ? lt_QL_gt : 8'bz;  // Driver driver_2
endmodule
