// Digital circuit Address Decoder.dig as structural Verilog
module Address_Decoder (
  input  [15:0] A,
  input  CS,
  output CS0,
  output CS1,
  output CS2,
  output CS3
);

  wire decoder_1_out_0, decoder_1_out_1, decoder_1_out_2, decoder_1_out_3;

  Decoder #(.Selector_Bits(2)) decoder_1 (
    .sel(A[15:14]), .out_0(decoder_1_out_0), .out_1(decoder_1_out_1), .out_2(decoder_1_out_2),
    .out_3(decoder_1_out_3));
  and and_1 (CS0, decoder_1_out_0, CS);
  and and_2 (CS1, decoder_1_out_1, CS);
  and and_3 (CS2, CS, decoder_1_out_2);
  and and_4 (CS3, CS, decoder_1_out_3);

  // Notes on the sheet:
  //   Banks
  //   0xC000...0xFFFF - Bank 3
  //   0x8000...0xBFFF - Bank 2
  //   0x4000...0x7FFF - Bank 1
  //   0x0000...0x3FFF - Bank 0
endmodule
