// Digital circuit io.dig as structural Verilog
module io (
  input  [15:0] ADDR,
  input  [7:0] IN,
  input  [7:0] RDY,
  input  RD,
  input  WR,
  input  CLK,
  output [7:0] OUT,
  output IRQ
);

  wire and_1_out, and_2_out, and_3_out, and_4_out, and_5_out, and_6_out, comparator_1_eq, comparator_2_eq,
       comparator_3_eq, comparator_4_eq, comparator_5_eq, comparator_6_eq, KRDY, TRDY;
  wire [7:0] keyboard_1_d, telnet_1_out;
  wire [15:8] keyboard_1_d_2;

  or or_1 (IRQ, TRDY, KRDY);
  Comparator #(.Bits(16)) comparator_1 (.a(ADDR), .b(16'h4002), .eq(comparator_1_eq));  // open: gt, lt
  Comparator #(.Bits(16)) comparator_2 (.a(ADDR), .b(16'h4003), .eq(comparator_2_eq));  // open: gt, lt
  Comparator #(.Bits(16)) comparator_3 (.a(ADDR), .b(16'h4004), .eq(comparator_3_eq));  // open: gt, lt
  Comparator #(.Bits(16)) comparator_4 (.a(ADDR), .b(16'h4005), .eq(comparator_4_eq));  // open: gt, lt
  Comparator #(.Bits(16)) comparator_5 (.a(ADDR), .b(16'h4006), .eq(comparator_5_eq));  // open: gt, lt
  Comparator #(.Bits(16)) comparator_6 (.a(ADDR), .b(16'h4007), .eq(comparator_6_eq));  // open: gt, lt
  and and_1 (and_1_out, comparator_1_eq, WR);
  and and_2 (and_2_out, comparator_2_eq, RD);
  and and_3 (and_3_out, comparator_3_eq, RD);
  and and_4 (and_4_out, comparator_4_eq, WR);
  and and_5 (and_5_out, comparator_5_eq, RD);
  and and_6 (and_6_out, comparator_6_eq, RD);
  Terminal terminal_1 (.D(IN), .C(CLK), .en(and_1_out));
  Keyboard keyboard_1 (.C(CLK), .en(and_2_out), .D({keyboard_1_d_2, keyboard_1_d}), .av(KRDY));
  assign RDY = and_3_out ? {{7{1'b0}}, KRDY} : 8'bz;  // Driver driver_1
  Telnet #(.port(6666)) telnet_1 (.in(IN), .C(CLK), .wr(and_4_out), .rd(and_5_out), .out(telnet_1_out), .av(TRDY));
  assign IN = and_6_out ? {{7{1'b0}}, TRDY} : 8'bz;  // Driver driver_2
  assign OUT = and_2_out ? keyboard_1_d : 8'bz;  // Driver driver_3
  assign OUT = and_5_out ? telnet_1_out : 8'bz;  // Driver driver_4

  // Other names for the same wires on the sheet: Clck1 = CLK

  // Notes on the sheet:
  //   ADDR
  //   0x4002 Write to terminal
  //   0x4003 Read From keyboard
  //   0x4004 Keyboard has input waiting 
  //   0x4005 Read from telnet
  //   0x4006 Write to telnet
  //   0x4007 Telnet has input waiting
  //   Terminal
  //   Keyboard
  //   Telnet
endmodule
