// Digital circuit CPU-SAFE.dig as structural Verilog
module CPU_SAFE (
  input  clk,
  input  RUN
);

  wire A_LD_CDATA, A_OUT_CDATA, ALU_COUT, ALU_NOUT, ALU_VOUT, ALU_ZOUT, ALUA_LD_CDATA, ALUB_LD_CDATA,
       ALUOP_0, ALUOP_1, ALUOP_2, ALUP_LD_P, ALUP_q, ALUR_OUT_CDATA, and_1_out, and_2_out, and_3_out, C,
       CDATA_LD_0, CDATA_LD_FF, CDATA_TO_CADDRH, CDATA_TO_CADDRL, Clock, Clock2, clock_1_cout,
       demultiplexer_1_out_0, demultiplexer_1_out_1, demultiplexer_1_out_2, demultiplexer_1_out_3,
       demultiplexer_1_out_4, demultiplexer_1_out_5, demultiplexer_1_out_6, demultiplexer_1_out_7, HALT,
       HALTED, IR_LD_XDATA, MARH_LD_CADDRH, MARL_LD_CADDRL, MBR_LD_CDATA, MBR_LD_XDATA, MBR_OUT_CDATA,
       MBR_OUT_XDATA, MEM_LD_XDATA, MEM_OUT_XDATA, multiplexer_7_out, multiplexer_8_out, multiplexer_9_out,
       multiplexer_10_out, N, nor_1_out, not_2_out, or_1_out, or_2_out, or_4_out, or_5_out, or_6_out,
       or_7_out, P_SRC_0, P_SRC_1, PC_INC, PC_LD, PC_LD_ADD, PC_OUT_CADDR, PCADDL_c_o, PCH_LD_CDATA,
       PCH_OUT_CDATA, PCL_LD_CDATA, PCL_OUT_CDATA, PN_LD, PV_LD, PZ_LD, RESET, S_DEC, S_INC, S_LD_CDATA,
       S_OUT_CADDR, S_OUT_CDATA, STASHH_LD_CDATA, STASHH_OUT_CDATA, STASHL_LD_CDATA, STASHL_OUT_CDATA,
       STEP_out, V, X_LD_CDATA, X_OUT_CDATA, Y_LD_CDATA, Y_OUT_CDATA, Z;
  wire [2:0] lt_uNEXTMUX_gt;
  wire [7:0] A, add_1_s, ALUA, ALUB, ALUR, CADDRH, CADDRL, CDATA, IR, MARH, MARL, MBR, multiplexer_1_out,
       multiplexer_2_out, multiplexer_3_out, multiplexer_4_out, multiplexer_5_out, multiplexer_6_out,
       PCADDH_s, PCADDL_s, PCH, PCL, ROM_d, S, STASHH, STASHL, X, Y;
  wire [15:0] DEMODE, DEOPCODE, lt_uCAR_gt, lt_uNEXTCAR_gt, lt_uParam_gt;

  or or_1 (or_1_out, S_INC, S_DEC, S_LD_CDATA);
  assign CADDRH = S_OUT_CADDR ? 8'h1 : 8'bz;  // Driver driver_1
  Multiplexer #(.Bits(8)) multiplexer_1 (.sel(PC_LD_ADD), .in_0(CDATA), .in_1(PCADDH_s), .out(multiplexer_1_out));
  Seven_Seg_Hex seven_seg_hex_1 (.d(MARH[7:4]), .dp(1'b0));
  Seven_Seg_Hex seven_seg_hex_2 (.d(A[7:4]), .dp(1'b0));
  Multiplexer #(.Bits(8)) multiplexer_2 (.sel(S_LD_CDATA), .in_0(add_1_s), .in_1(CDATA), .out(multiplexer_2_out));
  Seven_Seg_Hex seven_seg_hex_3 (.d(MARL[7:4]), .dp(1'b0));
  Seven_Seg_Hex seven_seg_hex_4 (.d(MARH[3:0]), .dp(1'b0));
  Seven_Seg_Hex seven_seg_hex_5 (.d(A[3:0]), .dp(1'b0));
  LED led_1 (.in(HALTED));
  Multiplexer #(.Bits(8)) multiplexer_3 (.sel(S_DEC), .in_0(8'h1), .in_1({8{1'b1}}), .out(multiplexer_3_out));
  Register #(.Bits(8)) u_S (.D(multiplexer_2_out), .C(Clock), .en(or_1_out), .Q(S));
  assign CDATA = PCH_OUT_CDATA ? PCH : 8'bz;  // Driver driver_2
  or or_2 (or_2_out, PC_LD_ADD, PCH_LD_CDATA);
  Add #(.Bits(8)) PCADDH (.a(PCH), .b({8{1'b0}}), .c_i(PCADDL_c_o), .s(PCADDH_s));  // open: c_o
  Button STEP (.out(STEP_out));
  Button u_RESET (.out(RESET));
  Seven_Seg_Hex seven_seg_hex_6 (.d(MARL[3:0]), .dp(1'b0));
  Seven_Seg_Hex seven_seg_hex_7 (.d(X[3:0]), .dp(1'b0));
  Seven_Seg_Hex seven_seg_hex_8 (.d(X[7:4]), .dp(1'b0));
  Register #(.Bits(8)) u_PCH (.D(multiplexer_1_out), .C(Clock), .en(or_2_out), .Q(PCH));
  Seven_Seg_Hex seven_seg_hex_9 (.d(MBR[3:0]), .dp(1'b0));
  Seven_Seg_Hex seven_seg_hex_10 (.d(MBR[7:4]), .dp(1'b0));
  Seven_Seg_Hex seven_seg_hex_11 (.d(Y[3:0]), .dp(1'b0));
  Seven_Seg_Hex seven_seg_hex_12 (.d(Y[7:4]), .dp(1'b0));
  Add #(.Bits(8)) add_1 (.a(multiplexer_3_out), .b(S), .c_i(1'b0), .s(add_1_s));  // open: c_o
  assign CDATA = S_OUT_CDATA ? S : 8'bz;  // Driver driver_3
  assign CADDRL = S_OUT_CADDR ? S : 8'bz;  // Driver driver_4
  assign CADDRH = PC_OUT_CADDR ? PCH : 8'bz;  // Driver driver_5
  Clock clock_1 (.RUN(RUN), .STEP(STEP_out), .HALT(HALT), .Cin(clk), .HALTED(HALTED), .Cout(clock_1_cout));
  Seven_Seg_Hex seven_seg_hex_13 (.d(PCH[3:0]), .dp(1'b0));
  Seven_Seg_Hex seven_seg_hex_14 (.d(PCH[7:4]), .dp(1'b0));
  Seven_Seg_Hex seven_seg_hex_15 (.d(PCL[3:0]), .dp(1'b0));
  Seven_Seg_Hex seven_seg_hex_16 (.d(PCL[7:4]), .dp(1'b0));
  Seven_Seg_Hex seven_seg_hex_17 (.d(ALUA[3:0]), .dp(1'b0));
  Seven_Seg_Hex seven_seg_hex_18 (.d(ALUA[7:4]), .dp(1'b0));
  Multiplexer #(.Bits(8)) multiplexer_4 (.sel(PC_LD_ADD), .in_0(CDATA), .in_1(PCADDL_s), .out(multiplexer_4_out));
  Multiplexer #(.Bits(8)) multiplexer_5 (.sel(PC_INC), .in_0(CDATA), .in_1(8'h1), .out(multiplexer_5_out));
  or or_3 (Clock, clock_1_cout, RESET);
  Seven_Seg_Hex seven_seg_hex_19 (.d(IR[7:4]), .dp(1'b0));
  Seven_Seg_Hex seven_seg_hex_20 (.d(ALUB[7:4]), .dp(1'b0));
  LED led_2 (.in(N));
  Add #(.Bits(8)) PCADDL (.a(PCL), .b(multiplexer_5_out), .c_i(1'b0), .s(PCADDL_s), .c_o(PCADDL_c_o));
  Seven_Seg_Hex seven_seg_hex_21 (.d(IR[3:0]), .dp(1'b0));
  Seven_Seg_Hex seven_seg_hex_22 (.d(STASHL[7:4]), .dp(1'b0));
  Seven_Seg_Hex seven_seg_hex_23 (.d(ALUB[3:0]), .dp(1'b0));
  Seven_Seg_Hex seven_seg_hex_24 (.d(ALUR[7:4]), .dp(1'b0));
  LED led_3 (.in(V));
  LED led_4 (.in(Z));
  assign CDATA = PCL_OUT_CDATA ? PCL : 8'bz;  // Driver driver_6
  or or_4 (or_4_out, PC_LD_ADD, PCL_LD_CDATA);
  not not_1 (Clock2, Clock);
  Seven_Seg_Hex seven_seg_hex_25 (.d(STASHL[3:0]), .dp(1'b0));
  Seven_Seg_Hex seven_seg_hex_26 (.d(ALUR[3:0]), .dp(1'b0));
  LED led_5 (.in(C));
  Register #(.Bits(8)) u_PCL (.D(multiplexer_4_out), .C(Clock), .en(or_4_out), .Q(PCL));
  Seven_Seg_Hex seven_seg_hex_27 (.d(STASHH[3:0]), .dp(1'b0));
  Seven_Seg_Hex seven_seg_hex_28 (.d(STASHH[7:4]), .dp(1'b0));
  assign CADDRL = PC_OUT_CADDR ? PCL : 8'bz;  // Driver driver_7
  Seven_Seg_Hex seven_seg_hex_29 (.d(S[3:0]), .dp(1'b0));
  Seven_Seg_Hex seven_seg_hex_30 (.d(S[7:4]), .dp(1'b0));
  Register #(.Bits(8)) MAR_H (.D(CADDRH), .C(Clock), .en(MARH_LD_CADDRH), .Q(MARH));
  Register #(.Bits(8)) MAR_L (.D(CADDRL), .C(Clock), .en(MARL_LD_CADDRL), .Q(MARL));
  Seven_Seg_Hex seven_seg_hex_31 (.d(DEMODE[11:8]), .dp(1'b0));
  Seven_Seg_Hex seven_seg_hex_32 (.d(DEMODE[15:12]), .dp(1'b0));
  Seven_Seg_Hex seven_seg_hex_33 (.d(DEMODE[3:0]), .dp(1'b0));
  Seven_Seg_Hex seven_seg_hex_34 (.d(DEMODE[7:4]), .dp(1'b0));
  assign CADDRH = CDATA_TO_CADDRH ? CDATA : 8'bz;  // Driver driver_8
  assign CADDRL = CDATA_TO_CADDRL ? CDATA : 8'bz;  // Driver driver_9
  Seven_Seg_Hex seven_seg_hex_35 (.d(DEOPCODE[11:8]), .dp(1'b0));
  Seven_Seg_Hex seven_seg_hex_36 (.d(DEOPCODE[15:12]), .dp(1'b0));
  nor nor_1 (nor_1_out, CDATA[0], CDATA[1], CDATA[2], CDATA[3], CDATA[4], CDATA[5], CDATA[6], CDATA[7]);
  Seven_Seg_Hex seven_seg_hex_37 (.d(DEOPCODE[3:0]), .dp(1'b0));
  Seven_Seg_Hex seven_seg_hex_38 (.d(DEOPCODE[7:4]), .dp(1'b0));
  and and_1 (and_1_out, MARH[7], MEM_OUT_XDATA);
  Multiplexer #(.Bits(8)) multiplexer_6 (.sel(MBR_LD_CDATA), .in_0(ROM_d), .in_1(CDATA), .out(multiplexer_6_out));
  Register #(.Bits(8)) u_MBR (.D(multiplexer_6_out), .C(Clock), .en(or_5_out), .Q(MBR));
  or or_5 (or_5_out, MBR_LD_CDATA, MBR_LD_XDATA);
  Multiplexer #(.Selector_Bits(2)) multiplexer_7 (
    .sel({P_SRC_1, P_SRC_0}), .in_0(1'b0), .in_1(1'b1), .in_2(ALU_ZOUT), .in_3(nor_1_out),
    .out(multiplexer_7_out));
  Seven_Seg_Hex seven_seg_hex_39 (.d(lt_uCAR_gt[15:12]), .dp(1'b0));
  not not_2 (not_2_out, MARH[7]);
  ROM #(.AddrBits(14), .Bits(8)) ROM (.A({MARH[5:0], MARL}), .sel(and_1_out), .D(ROM_d));
  Multiplexer #(.Selector_Bits(2)) multiplexer_8 (
    .sel({P_SRC_1, P_SRC_0}), .in_0(1'b0), .in_1(1'b1), .in_2(ALU_VOUT), .in_3(1'b0), .out(multiplexer_8_out));
  Seven_Seg_Hex seven_seg_hex_40 (.d(lt_uCAR_gt[7:4]), .dp(1'b0));
  Seven_Seg_Hex seven_seg_hex_41 (.d(lt_uCAR_gt[11:8]), .dp(1'b0));
  or or_6 (or_6_out, MEM_LD_XDATA, MEM_OUT_XDATA);
  assign ROM_d = MBR_OUT_XDATA ? MBR : 8'bz;  // Driver driver_10
  assign CDATA = MBR_OUT_CDATA ? MBR : 8'bz;  // Driver driver_11
  Seven_Seg_Hex seven_seg_hex_42 (.d(lt_uCAR_gt[3:0]), .dp(1'b0));
  Register #(.Bits(8)) u_ALUB (.D(CDATA), .C(Clock), .en(ALUB_LD_CDATA), .Q(ALUB));
  Multiplexer #(.Selector_Bits(2)) multiplexer_9 (
    .sel({P_SRC_1, P_SRC_0}), .in_0(1'b0), .in_1(1'b1), .in_2(ALU_NOUT), .in_3(CDATA[7]),
    .out(multiplexer_9_out));
  Multiplexer #(.Selector_Bits(2)) multiplexer_10 (
    .sel({P_SRC_1, P_SRC_0}), .in_0(1'b0), .in_1(1'b1), .in_2(ALU_COUT), .in_3(1'b0), .out(multiplexer_10_out));
  Seven_Seg_Hex seven_seg_hex_43 (.d(lt_uNEXTCAR_gt[11:8]), .dp(1'b0));
  Seven_Seg_Hex seven_seg_hex_44 (.d(lt_uNEXTCAR_gt[15:12]), .dp(1'b0));
  and and_2 (and_2_out, or_6_out, not_2_out);
  and and_3 (and_3_out, MEM_LD_XDATA, Clock);
  Seven_Seg_Hex seven_seg_hex_45 (.d(lt_uNEXTCAR_gt[3:0]), .dp(1'b0));
  Seven_Seg_Hex seven_seg_hex_46 (.d(lt_uNEXTCAR_gt[7:4]), .dp(1'b0));
  Register PN (.D(multiplexer_9_out), .C(Clock), .en(PN_LD), .Q(N));
  Register PV (.D(multiplexer_8_out), .C(Clock), .en(PV_LD), .Q(V));
  Register PZ (.D(multiplexer_7_out), .C(Clock), .en(PZ_LD), .Q(Z));
  Register PC (.D(multiplexer_10_out), .C(Clock), .en(PC_LD), .Q(C));
  Seven_Seg_Hex seven_seg_hex_47 (.d(lt_uParam_gt[15:12]), .dp(1'b0));
  Register #(.Bits(8)) u_IR (.D(ROM_d), .C(Clock), .en(IR_LD_XDATA), .Q(IR));
  Register #(.Bits(8)) u_ALUA (.D(CDATA), .C(Clock), .en(ALUA_LD_CDATA), .Q(ALUA));
  Register ALUP (.D(C), .C(Clock), .en(ALUP_LD_P), .Q(ALUP_q));
  Seven_Seg_Hex seven_seg_hex_48 (.d(lt_uParam_gt[7:4]), .dp(1'b0));
  Seven_Seg_Hex seven_seg_hex_49 (.d(lt_uParam_gt[11:8]), .dp(1'b0));
  RAMSinglePortSel #(.AddrBits(14), .isProgramMemory("true"), .Bits(8)) RAM (
    .A({MARH[5:0], MARL}), .CS(and_2_out), .WE(and_3_out), .OE(MEM_OUT_XDATA), .D(ROM_d));
  Seven_Seg_Hex seven_seg_hex_50 (.d(lt_uParam_gt[3:0]), .dp(1'b0));
  ALU alu_1 (
    .A(ALUA), .B(ALUB), .OP({ALUOP_2, ALUOP_1, ALUOP_0}), .CIN(ALUP_q), .OUT(ALUR), .NOUT(ALU_NOUT),
    .VOUT(ALU_VOUT), .ZOUT(ALU_ZOUT), .COUT(ALU_COUT));
  Instruction_Decoder instruction_decoder_1 (.OPCODE(IR), .MODEADDR(DEMODE), .OPCODEADDR(DEOPCODE));
  Demultiplexer #(.Selector_Bits(3)) demultiplexer_1 (
    .sel(lt_uNEXTMUX_gt), .in(1'b1), .out_0(demultiplexer_1_out_0), .out_1(demultiplexer_1_out_1),
    .out_2(demultiplexer_1_out_2), .out_3(demultiplexer_1_out_3), .out_4(demultiplexer_1_out_4),
    .out_5(demultiplexer_1_out_5), .out_6(demultiplexer_1_out_6), .out_7(demultiplexer_1_out_7));
  assign CDATA = ALUR_OUT_CDATA ? ALUR : 8'bz;  // Driver driver_12
  or or_7 (or_7_out, demultiplexer_1_out_4, demultiplexer_1_out_5, demultiplexer_1_out_6, demultiplexer_1_out_7);
  Register u_STASHH (.C(Clock), .D(CDATA), .OUT(STASHH_OUT_CDATA), .LD(STASHH_LD_CDATA), .Q(CDATA), .lt_Q_gt(STASHH));
  LED plus_1 (.in(demultiplexer_1_out_0));
  LED p0 (.in(demultiplexer_1_out_1));
  LED p1 (.in(demultiplexer_1_out_2));
  LED p2 (.in(demultiplexer_1_out_3));
  LED uJMPs (.in(or_7_out));
  Register u_STASHL (.C(Clock), .D(CDATA), .OUT(STASHL_OUT_CDATA), .LD(STASHL_LD_CDATA), .Q(CDATA), .lt_Q_gt(STASHL));
  Control_Unit control_unit_1 (
    .DEMODEin(DEMODE), .DEOPCODEin(DEOPCODE), .Nin(N), .Vin(V), .Zin(Z), .Cin(C), .RESET(RESET),
    .ClockIn(Clock), .lt_uCAR_gt(lt_uCAR_gt), .lt_uParam_gt(lt_uParam_gt), .lt_uNEXTCAR_gt(lt_uNEXTCAR_gt),
    .lt_uNEXTMUX_gt(lt_uNEXTMUX_gt), .HALT(HALT), .CDATA_LD_0(CDATA_LD_0), .CDATA_LD_FF(CDATA_LD_FF),
    .CDATA_TO_CADDRL(CDATA_TO_CADDRL), .CD_TO_CADDRH(CDATA_TO_CADDRH), .MEM_LD_XDATA(MEM_LD_XDATA),
    .MEM_OUT_XDATA(MEM_OUT_XDATA), .IR_LD_XDATA(IR_LD_XDATA), .MBR_LD_XDATA(MBR_LD_XDATA),
    .MBR_OUT_XDATA(MBR_OUT_XDATA), .MBR_LD_CDATA(MBR_LD_CDATA), .MBR_OUT_CDATA(MBR_OUT_CDATA),
    .MARL_LD_CADDRL(MARL_LD_CADDRL), .MARH_LD_CADDRH(MARH_LD_CADDRH), .PC_INC(PC_INC),
    .PC_ADD_CDATA(PC_LD_ADD), .PCL_LD_CDATA(PCL_LD_CDATA), .PCL_OUT_CDATA(PCL_OUT_CDATA),
    .PCH_LD_CDATA(PCH_LD_CDATA), .PCH_OUT_CDATA(PCH_OUT_CDATA), .PC_OUT_CADDR(PC_OUT_CADDR),
    .STASHL_LD_CDATA(STASHL_LD_CDATA), .STASHL_OUT_CDATA(STASHL_OUT_CDATA),
    .STASHH_LD_CDATA(STASHH_LD_CDATA), .STASHH_OUT_CDATA(STASHH_OUT_CDATA), .A_LD_CDATA(A_LD_CDATA),
    .A_OUT_CDATA(A_OUT_CDATA), .X_LD_CDATA(X_LD_CDATA), .X_OUT_CDATA(X_OUT_CDATA), .Y_LD_CDATA(Y_LD_CDATA),
    .Y_OUT_CDATA(Y_OUT_CDATA), .PN_LD(PN_LD), .PV_LD(PV_LD), .PZ_LD(PZ_LD), .PC_LD(PC_LD), .P_SRC_0(P_SRC_0),
    .P_SRC_1(P_SRC_1), .ALUA_LD_CDATA(ALUA_LD_CDATA), .ALUB_LD_CDATA(ALUB_LD_CDATA), .ALUC_LD(ALUP_LD_P),
    .ALUR_OUT_CDATA(ALUR_OUT_CDATA), .ALUOP_0(ALUOP_0), .ALUOP_1(ALUOP_1), .ALUOP_2(ALUOP_2), .S_INC(S_INC),
    .S_DEC(S_DEC), .S_LD_CDATA(S_LD_CDATA), .S_OUT_CDATA(S_OUT_CDATA), .S_OUT_CADDR(S_OUT_CADDR));  // open: ALUC_SRC_0, ALUC_SRC_1, CUP_SRC_ALU, ALUOP_3, PC_RESET, ERR
  Register u_A (.C(Clock), .D(CDATA), .OUT(A_OUT_CDATA), .LD(A_LD_CDATA), .Q(CDATA), .lt_Q_gt(A));
  Register u_X (.C(Clock), .D(CDATA), .OUT(X_OUT_CDATA), .LD(X_LD_CDATA), .Q(CDATA), .lt_Q_gt(X));
  Register u_Y (.C(Clock), .D(CDATA), .OUT(Y_OUT_CDATA), .LD(Y_LD_CDATA), .Q(CDATA), .lt_Q_gt(Y));
  assign CDATA = CDATA_LD_0 ? {8{1'b0}} : 8'bz;  // Driver driver_13
  assign CDATA = CDATA_LD_FF ? {8{1'b1}} : 8'bz;  // Driver driver_14

  // Notes on the sheet:
  //   clk: Hz: 100
  //   PC load source
  //   0 CDATA
  //   1 ADDER
  //   S (Stack) - In/out CDATA out CADDR
  //   PC - In/out CDATA out CADDR
  //   MAR
  //   A
  //   HALTED
  //   X
  //   MBR
  //   Y
  //   PC
  //   ALUA
  //   IR
  //   ALUB
  //   N
  //   V
  //   Z
  //   STASHL
  //   ALUOUT
  //   C
  //   XADDR Bus
  //   CADDRH Bus
  //   CADDRL Bus
  //   PC Adder load source
  //   00 CADDR
  //   01 1 (INC)
  //   STASH
  //   S
  //   High bit 
  //     set => ROM
  //     unset => RAM
  //   Instruction Decoder
  //   (p1) Decoded Mode
  //   P load source
  //   00 reset
  //   01 set
  //   10 ALU
  //   11 Processed CDATA
  //   (p2) Decoded OpCode
  //   XDATA Bus
  //   CDATA Bus
  //   contents of ROM (hex, n*v repeats v):
  //   a9,42
  //   Control Unit
  //   uCAR
  //   uNext CAR
  //   uParam
  //   NextMux
  //   ALU operation
  //   0 0 0 AND
  //   0 0 1 OR
  //   0 1 0 NOT
  //   0 1 1 XOR
  //   1 0 0 ADD
  //   1 0 1 SUB
  //   1 1 0 INC
  //   1 1 1 DEC
endmodule
