// Digital circuit tmp.dig as structural Verilog
module tmp (
  input  clk,
  input  RUN
);

  wire and_2_out, Clock, HALT, not_1_out, or_1_out, or_2_out, or_4_out, or_5_out, P0_Clock, PC_INC,
       PC_LD_ADD, PC_OUT_CADDR, PCADDL_2_c_o, PCADDL_3_c_o, PCADDL_c_o, PCH_LD_CDATA, PCH_OUT_CDATA,
       PCL_2_ovf, PCL_LD_CDATA, PCL_OUT_CDATA, RESET, RUNNING, STEP_out;
  wire [7:0] CADDRH, CADDRL, CDATA, multiplexer_1_out, multiplexer_2_out, multiplexer_3_out,
       multiplexer_4_out, multiplexer_5_out, multiplexer_6_out, PCADDH_2_s, PCADDH_3_s, PCADDH_s, PCADDL_2_s,
       PCADDL_3_s, PCADDL_s, PCH, PCL;
  wire [15:0] add_1_s, driver_11_out, PC;

  Multiplexer #(.Bits(8)) multiplexer_1 (.sel(PC_LD_ADD), .in_0(CDATA), .in_1(PCADDH_s), .out(multiplexer_1_out));
  assign CDATA = PCH_OUT_CDATA ? PCH : 8'bz;  // Driver driver_1
  or or_1 (or_1_out, PC_LD_ADD, PCH_LD_CDATA);
  Add #(.Bits(8)) PCADDH (.a(PCH), .b({8{1'b0}}), .c_i(PCADDL_c_o), .s(PCADDH_s));  // open: c_o
  Register #(.Bits(8)) u_PCH (.D(multiplexer_1_out), .C(Clock), .en(or_1_out), .Q(PCH));
  assign CADDRH = PC_OUT_CADDR ? PCH : 8'bz;  // Driver driver_2
  Multiplexer #(.Bits(8)) multiplexer_2 (.sel(PC_LD_ADD), .in_0(CDATA), .in_1(PCADDL_s), .out(multiplexer_2_out));
  Multiplexer #(.Bits(8)) multiplexer_3 (.sel(PC_INC), .in_0(CDATA), .in_1(8'h1), .out(multiplexer_3_out));
  Add #(.Bits(8)) PCADDL (.a(PCL), .b(multiplexer_3_out), .c_i(1'b0), .s(PCADDL_s), .c_o(PCADDL_c_o));
  assign CDATA = PCL_OUT_CDATA ? PCL : 8'bz;  // Driver driver_3
  or or_2 (or_2_out, PC_LD_ADD, PCL_LD_CDATA);
  CounterPreset #(.Bits(8)) PCH_2 (
    .en(PC_INC), .C(PCL_2_ovf), .dir(1'b0), .in(CDATA), .ld(PCH_LD_CDATA), .clr(1'b0), .out(PCH));  // open: ovf
  Register #(.Bits(8)) u_PCL (.D(multiplexer_2_out), .C(Clock), .en(or_2_out), .Q(PCL));
  assign CDATA = PCH_OUT_CDATA ? PCH : 8'bz;  // Driver driver_4
  assign CADDRL = PC_OUT_CADDR ? PCL : 8'bz;  // Driver driver_5
  assign CADDRH = PC_OUT_CADDR ? PCH : 8'bz;  // Driver driver_6
  CounterPreset #(.Bits(8)) PCL_2 (
    .en(PC_INC), .C(Clock), .dir(1'b0), .in(CDATA), .ld(PCL_LD_CDATA), .clr(1'b0), .out(PCL), .ovf(PCL_2_ovf));
  assign CADDRL = PC_OUT_CADDR ? PCL : 8'bz;  // Driver driver_7
  assign CDATA = PCL_OUT_CDATA ? PCL : 8'bz;  // Driver driver_8
  Register #(.Bits(8)) PCH_3 (.D(PCADDH_2_s), .C(P0_Clock), .en(PC_INC), .Q(PCH));
  Add #(.Bits(8)) PCADDH_2 (.a(PCH), .b({8{1'b0}}), .c_i(PCADDL_2_c_o), .s(PCADDH_2_s));  // open: c_o
  Driver #(.Bits(8)) driver_9 (.in(PCH), .en(PC_OUT_CADDR));  // open: out
  Register #(.Bits(8)) PCL_3 (.D(PCADDL_2_s), .C(P0_Clock), .en(PC_INC), .Q(PCL));
  Add #(.Bits(8)) PCADDL_2 (.a(PCL), .b(8'h1), .c_i(1'b0), .s(PCADDL_2_s), .c_o(PCADDL_2_c_o));
  Driver #(.Bits(8)) driver_10 (.in(PCL), .en(PC_OUT_CADDR));  // open: out
  Button u_RESET (.out(RESET));
  Button STEP (.out(STEP_out));
  not not_1 (not_1_out, HALT);
  and and_1 (RUNNING, not_1_out, RUN);
  and and_2 (and_2_out, clk, RUNNING);
  Register #(.Bits(16)) u_PC (.D(add_1_s), .C(P0_Clock), .en(PC_INC), .Q(PC));
  or or_3 (Clock, RESET, STEP_out, and_2_out);
  assign driver_11_out = PC_OUT_CADDR ? PC : 16'bz;  // Driver driver_11
  Multiplexer #(.Bits(8)) multiplexer_4 (.sel(PC_LD_ADD), .in_0(CDATA), .in_1(PCADDH_3_s), .out(multiplexer_4_out));
  Add #(.Bits(16)) add_1 (.a(PC), .b(16'h1), .c_i(1'b0), .s(add_1_s));  // open: c_o
  assign CDATA = PCH_OUT_CDATA ? PCH : 8'bz;  // Driver driver_12
  or or_4 (or_4_out, PC_LD_ADD, PCH_LD_CDATA);
  Add #(.Bits(8)) PCADDH_3 (.a(PCH), .b({8{1'b0}}), .c_i(PCADDL_3_c_o), .s(PCADDH_3_s));  // open: c_o
  Register #(.Bits(8)) PCH_4 (.D(multiplexer_4_out), .C(Clock), .en(or_4_out), .Q(PCH));
  assign CADDRH = PC_OUT_CADDR ? PCH : 8'bz;  // Driver driver_13
  Multiplexer #(.Bits(8)) multiplexer_5 (.sel(PC_LD_ADD), .in_0(CDATA), .in_1(PCADDL_3_s), .out(multiplexer_5_out));
  Multiplexer #(.Bits(8)) multiplexer_6 (.sel(PC_INC), .in_0(CDATA), .in_1(8'h1), .out(multiplexer_6_out));
  Add #(.Bits(8)) PCADDL_3 (.a(PCL), .b(multiplexer_6_out), .c_i(1'b0), .s(PCADDL_3_s), .c_o(PCADDL_3_c_o));
  assign CDATA = PCL_OUT_CDATA ? PCL : 8'bz;  // Driver driver_14
  or or_5 (or_5_out, PC_LD_ADD, PCL_LD_CDATA);
  Register #(.Bits(8)) PCL_4 (.D(multiplexer_5_out), .C(Clock), .en(or_5_out), .Q(PCL));
  assign CADDRL = PC_OUT_CADDR ? PCL : 8'bz;  // Driver driver_15

  // Notes on the sheet:
  //   clk: Hz: 100
  //   PC - In/out CDATA out CADDR
  //   PC load source
  //   0 CDATA
  //   1 ADDER
  //   PC Adder load source
  //   00 CADDR
  //   01 1 (INC)
endmodule
