// Digital circuit tmp.dig as structural Verilog
module tmp (
);

  wire P0_Clock, PC_INC, PC_OUT_CADDR, PCADDL_c_o;
  wire [7:0] PCADDH_s, PCADDL_s, PCH, PCL;
  wire [15:0] add_1_s, driver_3_out, PC;

  Register #(.Bits(8)) u_PCH (.D(PCADDH_s), .C(P0_Clock), .en(PC_INC), .Q(PCH));
  Add #(.Bits(8)) PCADDH (.a(PCH), .b({8{1'b0}}), .c_i(PCADDL_c_o), .s(PCADDH_s));  // open: c_o
  Driver #(.Bits(8)) driver_1 (.in(PCH), .en(PC_OUT_CADDR));  // open: out
  Register #(.Bits(8)) u_PCL (.D(PCADDL_s), .C(P0_Clock), .en(PC_INC), .Q(PCL));
  Add #(.Bits(8)) PCADDL (.a(PCL), .b(8'h1), .c_i(1'b0), .s(PCADDL_s), .c_o(PCADDL_c_o));
  Driver #(.Bits(8)) driver_2 (.in(PCL), .en(PC_OUT_CADDR));  // open: out
  Register #(.Bits(16)) u_PC (.D(add_1_s), .C(P0_Clock), .en(PC_INC), .Q(PC));
  assign driver_3_out = PC_OUT_CADDR ? PC : 16'bz;  // Driver driver_3
  Add #(.Bits(16)) add_1 (.a(PC), .b(16'h1), .c_i(1'b0), .s(add_1_s));  // open: c_o
endmodule
