// Digital circuit Shifter.dig as structural Verilog
module Shifter (
  input  [7:0] D,
  input  OP,
  input  DIR,
  input  CIN,
  output [7:0] Q,
  output COUT
);

  wire AND_3_pin6, AND_3_pin8, AND_4_pin3, AND_4_pin6, AND_4_pin8, AND_4_pin11, AND_pin3, AND_pin5, AND_pin6,
       AND_pin8, AND_pin11, OR_3_pin9, OR_3_pin10, OR_3_pin12, OR_3_pin13, OR_pin9, OR_pin10, OR_pin12,
       OR_pin13, R;

  _7408 AND (
    .pin1(DIR), .pin2(D[6]), .pin3(AND_pin3), .pin4(R), .pin5(AND_pin5), .pin6(AND_pin6), .pin7(1'b0),
    .pin8(AND_pin8), .pin9(DIR), .pin10(D[5]), .pin11(AND_pin11), .pin12(R), .pin13(D[7]), .pin14(1'b1));
  _7432 OR (
    .pin1(AND_pin3), .pin2(AND_pin6), .pin3(Q[7]), .pin4(AND_pin8), .pin5(AND_pin11), .pin6(Q[6]),
    .pin7(1'b0), .pin8(Q[5]), .pin9(OR_pin9), .pin10(OR_pin10), .pin11(Q[4]), .pin12(OR_pin12),
    .pin13(OR_pin13), .pin14(1'b1));
  _7404 NOT (
    .pin1(DIR), .pin2(R), .pin3(1'b0), .pin5(1'b0), .pin7(1'b0), .pin9(1'b0), .pin11(1'b0), .pin13(1'b0),
    .pin14(1'b1));  // open: pin4, pin6, pin8, pin10, pin12
  _7408 AND_2 (
    .pin1(DIR), .pin2(D[4]), .pin3(OR_pin9), .pin4(R), .pin5(D[6]), .pin6(OR_pin10), .pin7(1'b0),
    .pin8(OR_pin12), .pin9(DIR), .pin10(D[3]), .pin11(OR_pin13), .pin12(R), .pin13(D[5]), .pin14(1'b1));
  _7408 AND_3 (
    .pin1(OP), .pin2(CIN), .pin3(AND_pin5), .pin4(DIR), .pin5(D[7]), .pin6(AND_3_pin6), .pin7(1'b0),
    .pin8(AND_3_pin8), .pin9(D[0]), .pin10(R), .pin12(1'b0), .pin13(1'b0), .pin14(1'b1));  // open: pin11
  LED led_1 (.in(D[7]));
  LED led_2 (.in(Q[7]));
  _7432 OR_2 (
    .pin1(AND_3_pin6), .pin2(AND_3_pin8), .pin3(COUT), .pin4(1'b0), .pin5(1'b0), .pin7(1'b0), .pin9(1'b0),
    .pin10(1'b0), .pin12(1'b0), .pin13(1'b0), .pin14(1'b1));  // open: pin6, pin8, pin11
  _7408 AND_4 (
    .pin1(DIR), .pin2(D[2]), .pin3(AND_4_pin3), .pin4(R), .pin5(D[4]), .pin6(AND_4_pin6), .pin7(1'b0),
    .pin8(AND_4_pin8), .pin9(DIR), .pin10(D[1]), .pin11(AND_4_pin11), .pin12(R), .pin13(D[3]), .pin14(1'b1));
  LED led_3 (.in(D[6]));
  LED led_4 (.in(D[5]));
  LED led_5 (.in(D[4]));
  LED led_6 (.in(D[3]));
  LED led_7 (.in(Q[6]));
  LED led_8 (.in(Q[5]));
  LED led_9 (.in(Q[4]));
  LED led_10 (.in(Q[3]));
  LED led_11 (.in(D[2]));
  LED led_12 (.in(D[1]));
  LED led_13 (.in(D[0]));
  LED led_14 (.in(Q[2]));
  LED led_15 (.in(Q[1]));
  LED led_16 (.in(Q[0]));
  LED led_17 (.in(CIN));
  LED led_18 (.in(COUT));
  _7432 OR_3 (
    .pin1(AND_4_pin3), .pin2(AND_4_pin6), .pin3(Q[3]), .pin4(AND_4_pin8), .pin5(AND_4_pin11), .pin6(Q[2]),
    .pin7(1'b0), .pin8(Q[1]), .pin9(OR_3_pin9), .pin10(OR_3_pin10), .pin11(Q[0]), .pin12(OR_3_pin12),
    .pin13(OR_3_pin13), .pin14(1'b1));
  _7408 AND_5 (
    .pin1(DIR), .pin2(D[0]), .pin3(OR_3_pin9), .pin4(R), .pin5(D[2]), .pin6(OR_3_pin10), .pin7(1'b0),
    .pin8(OR_3_pin12), .pin9(DIR), .pin10(AND_pin5), .pin11(OR_3_pin13), .pin12(R), .pin13(D[1]), .pin14(1'b1));

  // Other names for the same wires on the sheet: CINT = CIN; L = DIR; ROT = OP

  // Notes on the sheet:
  //   Q7->Q6
  //   ROT AND CIN
  //   Q7->Q4
  //   0 SHIFT
  //   1 ROT
  //   Q5->Q4
  //   0 R
  //   1 L
  //   Q3->Q2
  //   Q3->Q0
  //   Q1->Q0
endmodule

/* Test case LEFT-SHIFT:
D          CIN OP DIR Q          COUT
# Single bit, carry clear
0b00000001 0   0  1   0b00000010 0
0b00000010 0   0  1   0b00000100 0
0b00000100 0   0  1   0b00001000 0
0b00001000 0   0  1   0b00010000 0
0b00010000 0   0  1   0b00100000 0
0b00100000 0   0  1   0b01000000 0
0b01000000 0   0  1   0b10000000 0
0b10000000 0   0  1   0b00000000 1

# Single bit, carry set
0b00000001 1   0  1   0b00000010 0
0b00000010 1   0  1   0b00000100 0
0b00000100 1   0  1   0b00001000 0
0b00001000 1   0  1   0b00010000 0
0b00010000 1   0  1   0b00100000 0
0b00100000 1   0  1   0b01000000 0
0b01000000 1   0  1   0b10000000 0
0b10000000 1   0  1   0b00000000 1

# Multi-bit tests
0b00011001 0   0  1   0b00110010 0
0b01100010 0   0  1   0b11000100 0
0b00100100 0   0  1   0b01001000 0
0b10001000 0   0  1   0b00010000 1
0b00110000 1   0  1   0b01100000 0
0b00100001 1   0  1   0b01000010 0
0b01000111 1   0  1   0b10001110 0
0b10110010 1   0  1   0b01100100 1
*/

/* Test case LEFT-ROT:
D          CIN OP DIR Q          COUT
# Single bit, carry clear
0b00000001 0   1  1   0b00000010 0
0b00000010 0   1  1   0b00000100 0
0b00000100 0   1  1   0b00001000 0
0b00001000 0   1  1   0b00010000 0
0b00010000 0   1  1   0b00100000 0
0b00100000 0   1  1   0b01000000 0
0b01000000 0   1  1   0b10000000 0
0b10000000 0   1  1   0b00000000 1

# Single bit, carry set
0b00000001 1   1  1   0b00000011 0
0b00000010 1   1  1   0b00000101 0
0b00000100 1   1  1   0b00001001 0
0b00001000 1   1  1   0b00010001 0
0b00010000 1   1  1   0b00100001 0
0b00100000 1   1  1   0b01000001 0
0b01000000 1   1  1   0b10000001 0
0b10000000 1   1  1   0b00000001 1

# Multi-bit tests
0b00011001 0   1  1   0b00110010 0
0b01100010 0   1  1   0b11000100 0
0b00100100 0   1  1   0b01001000 0
0b10001000 0   1  1   0b00010000 1
0b00110000 1   1  1   0b01100001 0
0b00100001 1   1  1   0b01000011 0
0b01000111 1   1  1   0b10001111 0
0b10110010 1   1  1   0b01100101 1
*/

/* Test case RIGHT-SHIFT:
D          CIN OP DIR Q          COUT
# Single bit, carry clear
0b00000001 0   0  0   0b00000000 1
0b00000010 0   0  0   0b00000001 0
0b00000100 0   0  0   0b00000010 0
0b00001000 0   0  0   0b00000100 0
0b00010000 0   0  0   0b00001000 0
0b00100000 0   0  0   0b00010000 0
0b01000000 0   0  0   0b00100000 0
0b10000000 0   0  0   0b01000000 0

# Single bit, carry set
0b00000001 1   0  0   0b00000000 1
0b00000010 1   0  0   0b00000001 0
0b00000100 1   0  0   0b00000010 0
0b00001000 1   0  0   0b00000100 0
0b00010000 1   0  0   0b00001000 0
0b00100000 1   0  0   0b00010000 0
0b01000000 1   0  0   0b00100000 0
0b10000000 1   0  0   0b01000000 0

# Multi-bit tests
0b00011001 0   0  0   0b00001100 1
0b01100010 0   0  0   0b00110001 0
0b00100100 0   0  0   0b00010010 0
0b10001000 0   0  0   0b01000100 0
0b00110000 1   0  0   0b00011000 0
0b00100001 1   0  0   0b00010000 1
0b01000111 1   0  0   0b00100011 1
0b10110010 1   0  0   0b01011001 0
*/

/* Test case RIGHT-ROT:
D          CIN OP DIR Q          COUT
# Single bit, carry clear
0b00000001 0   1  0   0b00000000 1
0b00000010 0   1  0   0b00000001 0
0b00000100 0   1  0   0b00000010 0
0b00001000 0   1  0   0b00000100 0
0b00010000 0   1  0   0b00001000 0
0b00100000 0   1  0   0b00010000 0
0b01000000 0   1  0   0b00100000 0
0b10000000 0   1  0   0b01000000 0

# Single bit, carry set
0b00000001 1   1  0   0b10000000 1
0b00000010 1   1  0   0b10000001 0
0b00000100 1   1  0   0b10000010 0
0b00001000 1   1  0   0b10000100 0
0b00010000 1   1  0   0b10001000 0
0b00100000 1   1  0   0b10010000 0
0b01000000 1   1  0   0b10100000 0
0b10000000 1   1  0   0b11000000 0

# Multi-bit tests
0b00011001 0   1  0   0b00001100 1
0b01100010 0   1  0   0b00110001 0
0b00100100 0   1  0   0b00010010 0
0b10001000 0   1  0   0b01000100 0
0b00110000 1   1  0   0b10011000 0
0b00100001 1   1  0   0b10010000 1
0b01000111 1   1  0   0b10100011 1
0b10110010 1   1  0   0b11011001 0
*/
