// Digital circuit CONTROL-SAFE.dig as structural Verilog
module CONTROL_SAFE (
  input  Nin,
  input  Vin,
  input  Zin,
  input  Cin,
  input  [7:0] IRin,
  input  ClockIn,
  output PC_OUT_CADDR,
  output MARH_LD_CADDRH,
  output IR_LD_XDATA,
  output PC_INC,
  output MBR_LD_XDATA,
  output MBR_OUT_CDATA,
  output A_LD_CDATA,
  output MEM_OUT_XDATA,
  output MEM_LD_XDATA,
  output MBR_OUT_XDATA,
  output MBR_LD_CDATA,
  output A_OUT_CDATA,
  output MARL_LD_CADDRL,
  output CDATA_TO_CADDRH,
  output CDATA_TO_CADDRL,
  output STASH_LD_CDATA,
  output STASH_OUT_CDATA,
  output PCL_LD_CADDRL,
  output PCH_LD_CADDR,
  output ALUA_LD_CDATA,
  output ALUR_OUT_CDATA,
  output ALUOP_0,
  output ALUOP_1,
  output ALUOP_2,
  output ALUB_LD_CDATA,
  output X_LD_CDATA,
  output Y_LD_CDATA,
  output X_OUT_CDATA,
  output Y_OUT_CDATA
);

  wire and_1_out, and_2_out, and_3_out, and_4_out, or_1_out, or_3_out, uCJMP, uJMP, uJMPINV, uJMPOP, uJSR,
       uNJMP, uPCINC, uRTS, uVJMP, uZJMP, xor_1_out, xor_2_out, xor_3_out, xor_4_out;
  wire [1:0] NextMux;
  wire [15:0] add_1_s, CAR, CARstore, Next, uNextAddr;
  wire [55:55] Microcode_d;

  Seven_Seg_Hex seven_seg_hex_1 (.d(CAR[11:8]), .dp(1'b0));
  Seven_Seg_Hex seven_seg_hex_2 (.d(CAR[15:12]), .dp(1'b0));
  Seven_Seg_Hex seven_seg_hex_3 (.d(uNextAddr[11:8]), .dp(1'b0));
  Seven_Seg_Hex seven_seg_hex_4 (.d(uNextAddr[15:12]), .dp(1'b0));
  Seven_Seg_Hex seven_seg_hex_5 (.d(CAR[3:0]), .dp(1'b0));
  Seven_Seg_Hex seven_seg_hex_6 (.d(CAR[7:4]), .dp(1'b0));
  Seven_Seg_Hex seven_seg_hex_7 (.d(uNextAddr[3:0]), .dp(1'b0));
  Seven_Seg_Hex seven_seg_hex_8 (.d(uNextAddr[7:4]), .dp(1'b0));
  Seven_Seg_Hex seven_seg_hex_9 (.d(CARstore[15:12]), .dp(1'b0));
  Seven_Seg_Hex seven_seg_hex_10 (.d(Next[15:12]), .dp(1'b0));
  Seven_Seg_Hex seven_seg_hex_11 (.d(CARstore[7:4]), .dp(1'b0));
  Seven_Seg_Hex seven_seg_hex_12 (.d(CARstore[11:8]), .dp(1'b0));
  Seven_Seg_Hex seven_seg_hex_13 (.d(Next[7:4]), .dp(1'b0));
  Seven_Seg_Hex seven_seg_hex_14 (.d(Next[11:8]), .dp(1'b0));
  Seven_Seg_Hex seven_seg_hex_15 (.d(CARstore[3:0]), .dp(1'b0));
  Seven_Seg_Hex seven_seg_hex_16 (.d(Next[3:0]), .dp(1'b0));
  LED led_1 (.in(NextMux[1]));
  LED led_2 (.in(NextMux[0]));
  ROM #(.AddrBits(16), .Bits(56)) Microcode (
    .A(CAR), .sel(1'b1),
    .D({Microcode_d[55], uJMPINV, Y_OUT_CDATA, Y_LD_CDATA, X_OUT_CDATA, X_LD_CDATA, ALUB_LD_CDATA, ALUOP_2, ALUOP_1, ALUOP_0, ALUR_OUT_CDATA, ALUA_LD_CDATA, PCH_LD_CADDR, PCL_LD_CADDRL, STASH_OUT_CDATA, STASH_LD_CDATA, CDATA_TO_CADDRL, CDATA_TO_CADDRH, MARL_LD_CADDRL, A_OUT_CDATA, MBR_LD_CDATA, MBR_OUT_XDATA, MEM_LD_XDATA, MEM_OUT_XDATA, A_LD_CDATA, MBR_OUT_CDATA, MBR_LD_XDATA, PC_INC, IR_LD_XDATA, MARH_LD_CADDRH, PC_OUT_CADDR, uCJMP, uZJMP, uVJMP, uNJMP, uPCINC, uJMPOP, uRTS, uJSR, uJMP, uNextAddr}));
  Register #(.Bits(16)) u_CAR (.D(Next), .C(ClockIn), .en(1'b1), .Q(CAR));
  Add #(.Bits(16)) add_1 (.a(CAR), .b(16'h1), .c_i(1'b0), .s(add_1_s));  // open: c_o
  Register #(.Bits(16)) CAR_RTS (.D(add_1_s), .C(ClockIn), .en(uJSR), .Q(CARstore));
  or or_1 (or_1_out, uJMP, uJSR);
  and and_1 (and_1_out, uZJMP, xor_1_out);
  xor xor_1 (xor_1_out, Zin, uJMPINV);
  or or_2 (NextMux[1], or_3_out, uJMPOP);
  or or_3 (or_3_out, or_1_out, and_1_out, and_2_out, and_3_out, and_4_out);
  and and_2 (and_2_out, uNJMP, xor_2_out);
  xor xor_2 (xor_2_out, Nin, uJMPINV);
  Multiplexer #(.Selector_Bits(2), .Bits(16)) multiplexer_1 (
    .sel(NextMux), .in_0(add_1_s), .in_1(CARstore), .in_2(uNextAddr), .in_3({4'b0001, IRin, 4'b0000}),
    .out(Next));
  and and_3 (and_3_out, uVJMP, xor_3_out);
  xor xor_3 (xor_3_out, Vin, uJMPINV);
  or or_4 (NextMux[0], uJMPOP, uRTS);
  and and_4 (and_4_out, uCJMP, xor_4_out);
  xor xor_4 (xor_4_out, Cin, uJMPINV);

  // Other names for the same wires on the sheet: PCH_LD_CADDRH = PCH_LD_CADDR; Clock = ClockIn

  // Notes on the sheet:
  //   IRin: default 169
  //   CAR
  //   uNextAddr
  //   CAR RTS
  //   Next
  //   NextMux
  //   contents of Microcode (hex, n*v repeats v):
  //   6000000,18000000,6000000,30000000,c0000000
endmodule
