# Fritzing sketch alu board power to z (saved by Fritzing 0.9.10b)
perfboards: 1

parts:
  A_Reg = IC, DIP package, 20 pins [chip_label=74HC377]  # not connected
  J9 = male pin header, 2 pins [form="♂ (male)"]  # not connected
  Not = 74HC04_HEX_INVERTER [package=dil14]
  Not_2 = 74HC04_HEX_INVERTER [package=dil14]
  Carry_In = DIP - 14 pins [chip_label=74HC00 package="DIP (Dual Inline) [THT]"]
  Mux_0-1 = IC, DIP package, 16 pins [chip_label=74HC153]
  Mux_4-5 = IC, DIP package, 16 pins [chip_label=74HC153]
  Mux_2-3 = IC, DIP package, 16 pins [chip_label=74HC153]
  Mux_6-7 = IC, DIP package, 16 pins [chip_label=74HC153]
  Adder_Low = IC, DIP package, 16 pins [chip_label=74HC283]  # not connected
  Adder_High = IC, DIP package, 16 pins [chip_label=74HC283]
  B_Reg = IC, DIP package, 20 pins [chip_label=74HC377]
  J18 = shrouded pin header, 8 pins [form="♂ (shrouded male)"]  # not connected
  J22 = shrouded pin header, 8 pins [form="♂ (shrouded male)"]  # not connected
  J25 = shrouded pin header, 8 pins [form="♂ (shrouded male)"]
  J26 = shrouded pin header, 8 pins [form="♂ (shrouded male)"]  # not connected
  C1 = Ceramic Capacitor [capacitance=100nF voltage=35V package="100 mil [THT, multilayer]"]
  C2 = Ceramic Capacitor [capacitance=100nF voltage=35V package="100 mil [THT, multilayer]"]
  C3 = Ceramic Capacitor [capacitance=100nF voltage=35V package="100 mil [THT, multilayer]"]
  C4 = Ceramic Capacitor [capacitance=100nF voltage=35V package="100 mil [THT, multilayer]"]
  C5 = Ceramic Capacitor [capacitance=100nF voltage=35V package="100 mil [THT, multilayer]"]
  C6 = Ceramic Capacitor [capacitance=100nF voltage=35V package="100 mil [THT, multilayer]"]
  C7 = Ceramic Capacitor [capacitance=100nF voltage=35V package="100 mil [THT, multilayer]"]
  C8 = Ceramic Capacitor [capacitance=100nF voltage=35V package="100 mil [THT, multilayer]"]
  C9 = Ceramic Capacitor [capacitance=100nF voltage=35V package="100 mil [THT, multilayer]"]  # not connected
  C10 = Ceramic Capacitor [capacitance=100nF voltage=35V package="100 mil [THT, multilayer]"]  # not connected
  C14 = Ceramic Capacitor [capacitance=100nF voltage=35V package="100 mil [THT, multilayer]"]  # not connected
  C15 = Ceramic Capacitor [capacitance=100nF voltage=35V package="100 mil [THT, multilayer]"]  # not connected
  C16 = Electrolytic Capacitor [capacitance=1µF voltage=35V package="100 mil [THT, electrolytic]"]
  J19 = shrouded pin header, 8 pins [form="♂ (shrouded male)"]  # not connected
  Out_Buffer = DIP - 20 pins [chip_label=74HC244 package="DIP (Dual Inline) [THT]"]  # not connected
  J30 = shrouded pin header, 8 pins [form="♂ (shrouded male)"]  # not connected
  J31 = shrouded pin header, 8 pins [form="♂ (shrouded male)"]  # not connected

nets:
  N1: Not.1A, J25.pin2
  N2: Not.1Y, B_Reg.pin1
  N3: Not.GND, C3.1, C16.+
  VCC: Not.VCC, Not_2.VCC, Mux_0-1.pin3, Mux_0-1.pin4, Mux_0-1.pin13, Mux_0-1.pin16, Mux_4-5.pin3, Mux_4-5.pin13, Mux_4-5.pin16, Mux_2-3.pin3, Mux_2-3.pin13, Mux_2-3.pin16, Mux_6-7.pin3, Mux_6-7.pin13, Mux_6-7.pin16, B_Reg.pin20, C1.0, C2.0, C3.0, C4.0, C5.0, C6.0, C7.0, C16.-
  N4: Not_2.GND, B_Reg.pin10, C1.1, C2.1
  N5: Carry_In.1A, Carry_In.1B
  N6: Mux_0-1.pin1, Mux_0-1.pin8, Mux_0-1.pin12, Mux_0-1.pin15, Mux_4-5.pin1, Mux_4-5.pin4, Mux_4-5.pin8, Mux_4-5.pin12, Mux_4-5.pin15, Mux_2-3.pin1, Mux_2-3.pin4, Mux_2-3.pin8, Mux_2-3.pin12, Mux_2-3.pin15, Mux_6-7.pin1, Mux_6-7.pin4, Mux_6-7.pin8, Mux_6-7.pin12, Mux_6-7.pin15, C4.1, C5.1, C6.1, C7.1
  N7: Mux_0-1.pin2, Mux_4-5.pin2, Mux_2-3.pin2, Mux_6-7.pin2, J25.pin1
  N8: Mux_0-1.pin14, Mux_4-5.pin14, Mux_2-3.pin14, Mux_6-7.pin14, J25.pin8
  N9: Adder_High.pin8, C8.1
  N10: B_Reg.pin11, J25.pin4

custom parts:
  DIP - 14 pins: A DIP stand-in part for whatever IC you want. With 14 pins on a 300mil dual inline package (DIP) footprint.
  DIP - 20 pins: A DIP stand-in part for whatever IC you want. With 20 pins on a 300mil dual inline package (DIP) footprint.
