# Fritzing sketch alu board power (saved by Fritzing 0.9.10b)
perfboards: 1

parts:
  A_Reg = IC, DIP package, 20 pins [chip_label=74HC377]
  Or = 7CHC32 [package="DIP (Dual Inline) [THT]"]
  Or_2 = 7CHC32 [package="DIP (Dual Inline) [THT]"]
  J9 = male pin header, 2 pins [form="♂ (male)"]  # not connected
  Not = 74HC04_HEX_INVERTER [package=dil14]
  Not_2 = 74HC04_HEX_INVERTER [package=dil14]
  Not_3 = 74HC04_HEX_INVERTER [package=dil14]
  Carry_In = DIP - 14 pins [chip_label=74HC00 package="DIP (Dual Inline) [THT]"]
  Mux_0-1 = IC, DIP package, 16 pins [chip_label=74HC153]
  Mux_4-5 = IC, DIP package, 16 pins [chip_label=74HC153]
  Mux_2-3 = IC, DIP package, 16 pins [chip_label=74HC153]
  Mux_6-7 = IC, DIP package, 16 pins [chip_label=74HC153]
  Adder_Low = IC, DIP package, 16 pins [chip_label=74HC283]
  Adder_High = IC, DIP package, 16 pins [chip_label=74HC283]
  B_Reg = IC, DIP package, 20 pins [chip_label=74HC377]
  J18 = shrouded pin header, 8 pins [form="♂ (shrouded male)"]  # not connected
  J22 = shrouded pin header, 8 pins [form="♂ (shrouded male)"]  # not connected
  J25 = shrouded pin header, 8 pins [form="♂ (shrouded male)"]
  J26 = shrouded pin header, 8 pins [form="♂ (shrouded male)"]  # not connected
  J27 = shrouded pin header, 8 pins [form="♂ (shrouded male)"]  # not connected
  C1 = Ceramic Capacitor [capacitance=100nF voltage=35V package="100 mil [THT, multilayer]"]
  C2 = Ceramic Capacitor [capacitance=100nF voltage=35V package="100 mil [THT, multilayer]"]
  C3 = Ceramic Capacitor [capacitance=100nF voltage=35V package="100 mil [THT, multilayer]"]
  C4 = Ceramic Capacitor [capacitance=100nF voltage=35V package="100 mil [THT, multilayer]"]
  C5 = Ceramic Capacitor [capacitance=100nF voltage=35V package="100 mil [THT, multilayer]"]
  C6 = Ceramic Capacitor [capacitance=100nF voltage=35V package="100 mil [THT, multilayer]"]
  C7 = Ceramic Capacitor [capacitance=100nF voltage=35V package="100 mil [THT, multilayer]"]
  C8 = Ceramic Capacitor [capacitance=100nF voltage=35V package="100 mil [THT, multilayer]"]
  C9 = Ceramic Capacitor [capacitance=100nF voltage=35V package="100 mil [THT, multilayer]"]
  C10 = Ceramic Capacitor [capacitance=100nF voltage=35V package="100 mil [THT, multilayer]"]
  C11 = Ceramic Capacitor [capacitance=100nF voltage=35V package="100 mil [THT, multilayer]"]
  C12 = Ceramic Capacitor [capacitance=100nF voltage=35V package="100 mil [THT, multilayer]"]
  C13 = Ceramic Capacitor [capacitance=100nF voltage=35V package="100 mil [THT, multilayer]"]
  C14 = Ceramic Capacitor [capacitance=100nF voltage=35V package="100 mil [THT, multilayer]"]
  C15 = Ceramic Capacitor [capacitance=100nF voltage=35V package="100 mil [THT, multilayer]"]
  C16 = Electrolytic Capacitor [capacitance=1µF voltage=35V package="100 mil [THT, electrolytic]"]
  J19 = shrouded pin header, 8 pins [form="♂ (shrouded male)"]  # not connected
  Out_Buffer = DIP - 20 pins [chip_label=74HC244 package="DIP (Dual Inline) [THT]"]

nets:
  N1: A_Reg.pin1, Not.1Y
  N2: A_Reg.pin10, Adder_High.pin8, C8.1, C9.1
  N3: A_Reg.pin11, B_Reg.pin11, J25.pin4
  N4: A_Reg.pin20, Adder_Low.pin16, Adder_High.pin16, C7.0, C8.0, C9.0
  GND: Or.GND, Or.3A, Or.3B, Or_2.GND, C11.1, C12.1, C15.1, Out_Buffer.GND
  N5: Or.4Y, Not.2A
  VCC: Or.VCC, Or_2.VCC, Not.VCC, Carry_In.VCC, C10.0, C11.0, C12.0, C13.0, C14.0, C15.0, Out_Buffer.VCC
  N6: Not.1A, J25.pin7
  N7: Not.3A, J25.pin3
  N8: Not.3Y, Out_Buffer.~1OE, Out_Buffer.~2OE
  GND_2: Not.GND, Not.4A, Not.5A, Not.6A, Carry_In.GND, C13.1, C14.1
  N9: Not_2.1A, J25.pin2
  N10: Not_2.1Y, B_Reg.pin1
  N11: Not_2.GND, C3.1, C16.+
  VCC_2: Not_2.VCC, Not_3.VCC, Mux_0-1.pin3, Mux_0-1.pin4, Mux_0-1.pin13, Mux_0-1.pin16, Mux_4-5.pin3, Mux_4-5.pin16, Mux_2-3.pin3, Mux_2-3.pin13, Mux_2-3.pin16, Mux_6-7.pin3, Mux_6-7.pin16, B_Reg.pin20, C1.0, C2.0, C3.0, C6.0, C16.-
  N12: Not_3.2A, Not_3.3A, Not_3.GND, C1.1
  N13: Carry_In.1A, Mux_0-1.pin2, Mux_4-5.pin2, Mux_2-3.pin2, Mux_6-7.pin2, J25.pin1
  N14: Carry_In.2B, J25.pin6
  N15: Mux_0-1.pin1, Mux_0-1.pin8, Mux_0-1.pin12, Mux_0-1.pin15, Mux_4-5.pin1, Mux_4-5.pin4, Mux_4-5.pin8, Mux_4-5.pin12, Mux_4-5.pin15, Mux_2-3.pin1, Mux_2-3.pin4, Mux_2-3.pin8, Mux_2-3.pin12, Mux_2-3.pin15, Mux_6-7.pin1, Mux_6-7.pin4, Mux_6-7.pin8, Mux_6-7.pin12, Mux_6-7.pin15, Adder_Low.pin8, C4.1, C5.1, C6.1, C7.1, C10.1
  N16: Mux_0-1.pin14, Mux_4-5.pin14, Mux_2-3.pin14, Mux_6-7.pin14, J25.pin8
  N17: Mux_4-5.pin13, C5.0
  N18: Mux_6-7.pin13, C4.0
  N19: B_Reg.pin10, C2.1

custom parts:
  7CHC32: A DIP stand-in part for whatever IC you want. With 14 pins on a 300mil dual inline package (DIP) footprint.
  DIP - 14 pins: A DIP stand-in part for whatever IC you want. With 14 pins on a 300mil dual inline package (DIP) footprint.
  DIP - 20 pins: A DIP stand-in part for whatever IC you want. With 20 pins on a 300mil dual inline package (DIP) footprint.
