# Fritzing sketch alu board (saved by Fritzing 0.9.10b)
perfboards: 1

parts:
  A_Reg = IC, DIP package, 20 pins [chip_label=74HC377]
  Or = 7CHC32 [package="DIP (Dual Inline) [THT]"]
  Or_2 = 7CHC32 [package="DIP (Dual Inline) [THT]"]
  J9 = male pin header, 2 pins [form="♂ (male)"]  # not connected
  Not = 74HC04_HEX_INVERTER [package=dil14]
  Not_2 = 74HC04_HEX_INVERTER [package=dil14]
  Not_3 = 74HC04_HEX_INVERTER [package=dil14]
  Out_Buffer = DIP - 20 pins [chip_label=74HC244 package="DIP (Dual Inline) [THT]"]  # not connected
  Carry_In = DIP - 14 pins [chip_label=74HC00 package="DIP (Dual Inline) [THT]"]
  Mux_0-1 = IC, DIP package, 16 pins [chip_label=74HC153]
  Mux_4-5 = IC, DIP package, 16 pins [chip_label=74HC153]
  Mux_2-3 = IC, DIP package, 16 pins [chip_label=74HC153]
  Mux_6-7 = IC, DIP package, 16 pins [chip_label=74HC153]
  Adder_Low = IC, DIP package, 16 pins [chip_label=74HC283]
  Adder_High = IC, DIP package, 16 pins [chip_label=74HC283]
  B_Reg = IC, DIP package, 20 pins [chip_label=74HC377]
  J18 = shrouded pin header, 8 pins [form="♂ (shrouded male)"]  # not connected
  J19 = shrouded pin header, 8 pins [form="♂ (shrouded male)"]
  J22 = shrouded pin header, 8 pins [form="♂ (shrouded male)"]  # not connected
  J25 = shrouded pin header, 8 pins [form="♂ (shrouded male)"]  # not connected
  J26 = shrouded pin header, 8 pins [form="♂ (shrouded male)"]  # not connected
  J27 = shrouded pin header, 8 pins [form="♂ (shrouded male)"]  # not connected
  C1 = Ceramic Capacitor [capacitance=100nF voltage=35V package="100 mil [THT, multilayer]"]
  C2 = Ceramic Capacitor [capacitance=100nF voltage=35V package="100 mil [THT, multilayer]"]
  C3 = Ceramic Capacitor [capacitance=100nF voltage=35V package="100 mil [THT, multilayer]"]
  C4 = Ceramic Capacitor [capacitance=100nF voltage=35V package="100 mil [THT, multilayer]"]
  C5 = Ceramic Capacitor [capacitance=100nF voltage=35V package="100 mil [THT, multilayer]"]
  C6 = Ceramic Capacitor [capacitance=100nF voltage=35V package="100 mil [THT, multilayer]"]
  C7 = Ceramic Capacitor [capacitance=100nF voltage=35V package="100 mil [THT, multilayer]"]
  C8 = Ceramic Capacitor [capacitance=100nF voltage=35V package="100 mil [THT, multilayer]"]
  C9 = Ceramic Capacitor [capacitance=100nF voltage=35V package="100 mil [THT, multilayer]"]
  C10 = Ceramic Capacitor [capacitance=100nF voltage=35V package="100 mil [THT, multilayer]"]
  C11 = Ceramic Capacitor [capacitance=100nF voltage=35V package="100 mil [THT, multilayer]"]
  C12 = Ceramic Capacitor [capacitance=100nF voltage=35V package="100 mil [THT, multilayer]"]  # not connected
  C13 = Ceramic Capacitor [capacitance=100nF voltage=35V package="100 mil [THT, multilayer]"]
  C14 = Ceramic Capacitor [capacitance=100nF voltage=35V package="100 mil [THT, multilayer]"]
  C15 = Ceramic Capacitor [capacitance=100nF voltage=35V package="100 mil [THT, multilayer]"]
  C16 = Electrolytic Capacitor [capacitance=1µF voltage=35V package="100 mil [THT, electrolytic]"]

nets:
  N1: A_Reg.pin10, Adder_High.pin8, C8.1, C9.1
  N2: A_Reg.pin20, Adder_Low.pin16, Adder_High.pin16, C7.0, C8.0
  GND: Or.GND, Or_2.GND, Not.GND, Carry_In.GND, C11.1, C13.1, C14.1, C15.1
  N3: Or.4B, Adder_Low.pin4
  VCC: Or.VCC, Or_2.VCC, Not.VCC, Carry_In.VCC, C10.0, C11.0, C13.0, C14.0, C15.0
  N4: Not_2.1A, Mux_0-1.pin6, B_Reg.pin2
  N5: Not_2.1Y, Mux_0-1.pin5
  N6: Not_2.2A, Mux_0-1.pin10, B_Reg.pin5
  N7: Not_2.2Y, Mux_0-1.pin11
  N8: Not_2.3A, Mux_2-3.pin6, B_Reg.pin6
  N9: Not_2.GND, C3.1, C16.+
  VCC_2: Not_2.VCC, Not_3.VCC, Mux_0-1.pin3, Mux_0-1.pin4, Mux_0-1.pin13, Mux_0-1.pin16, Mux_4-5.pin3, Mux_4-5.pin16, Mux_2-3.pin3, Mux_2-3.pin13, Mux_2-3.pin16, Mux_6-7.pin3, Mux_6-7.pin16, B_Reg.pin20, C1.0, C2.0, C3.0, C6.0, C16.-
  N10: Not_3.1A, B_Reg.pin12
  N11: Not_3.GND, C1.1
  N12: Not_3.4A, B_Reg.pin15
  N13: Not_3.5A, B_Reg.pin16
  N14: Not_3.6A, B_Reg.pin19
  N15: Mux_0-1.pin1, Mux_0-1.pin8, Mux_0-1.pin12, Mux_0-1.pin15, Mux_4-5.pin4, Mux_4-5.pin8, Mux_4-5.pin12, Mux_2-3.pin4, Mux_2-3.pin8, Mux_2-3.pin12, Mux_6-7.pin4, Mux_6-7.pin8, Mux_6-7.pin12, Adder_Low.pin8, C4.1, C5.1, C6.1, C7.1, C10.1
  N16: Mux_0-1.pin7, Adder_Low.pin6
  N17: Mux_4-5.pin13, C5.0
  N18: Mux_2-3.pin10, B_Reg.pin9
  N19: Mux_6-7.pin13, C4.0
  N20: B_Reg.pin3, J19.pin4
  N21: B_Reg.pin4, J19.pin3
  N22: B_Reg.pin7, J19.pin2
  N23: B_Reg.pin8, J19.pin1
  N24: B_Reg.pin10, C2.1
  N25: B_Reg.pin13, J19.pin5
  N26: B_Reg.pin14, J19.pin6
  N27: B_Reg.pin17, J19.pin7
  N28: B_Reg.pin18, J19.pin8

custom parts:
  7CHC32: A DIP stand-in part for whatever IC you want. With 14 pins on a 300mil dual inline package (DIP) footprint.
  DIP - 20 pins: A DIP stand-in part for whatever IC you want. With 20 pins on a 300mil dual inline package (DIP) footprint.
  DIP - 14 pins: A DIP stand-in part for whatever IC you want. With 14 pins on a 300mil dual inline package (DIP) footprint.
