# Fritzing sketch carry board (saved by Fritzing 0.9.10b)
breadboards: 1
perfboards: 1

parts:
  IC1 = DIP - 14 pins [chip_label=74HC00 package="DIP (Dual Inline) [THT]"]
  J1 = male pin header, 2 pins [form="♂ (male)"]
  R1 = Resistor [tolerance=±5% power=0.25 resistance=220 package=THT]
  LED1 = LED - 5mm [color="Red (633nm)" current=0.030 package="5 mm [THT]"]
  R2 = Resistor [tolerance=±5% power=0.25 resistance=220 package=THT]
  LED2 = LED - 5mm [color="Red (633nm)" current=0.030 package="5 mm [THT]"]
  R3 = Resistor [tolerance=±5% power=0.25 resistance=220 package=THT]
  LED3 = LED - 5mm [color="Red (633nm)" current=0.030 package="5 mm [THT]"]
  J2 = male pin header, 2 pins [form="♂ (male)"]
  J3 = male pin header, 1 pin [form="♂ (male)"]  # not connected
  Q4 = MOSFET-NCHANNEL [package=to-92]
  Q5 = MOSFET-NCHANNEL [package=to-92]
  Q6 = MOSFET-NCHANNEL [package=to-92]

nets:
  N1: IC1.GND, J1.pin2, Q4.D, Q5.D, Q6.D
  N2: J1.pin1, LED3.anode
  N3: R1.Pin_0, Q6.G
  N4: R1.Pin_1, LED3.cathode
  N5: LED1.cathode, R2.Pin_1
  N6: LED1.anode, LED2.anode
  N7: R2.Pin_0, Q5.G
  N8: LED2.cathode, R3.Pin_1
  N9: R3.Pin_0, Q4.G
  N10: J2.pin1, Q6.S
  N11: J2.pin2, Q5.S

custom parts:
  DIP - 14 pins: A DIP stand-in part for whatever IC you want. With 14 pins on a 300mil dual inline package (DIP) footprint.
  MOSFET-NCHANNEL: Generic NMOS footprint
