// Digital circuit 74-ALU.dig as structural Verilog
module _74_ALU (
  input  [7:0] D,
  input  [1:0] OP,
  input  CIN,
  input  CLCK,
  input  LDA,
  input  LDB,
  input  OUT,
  output [7:0] Q,
  output COUT,
  output ZOUT
);

  wire A0, A1, A2, A3, A4, A5, A6, A7, A__FFs_pin11, ADD_pin9, B0, B1, B2, B3, B4, B5, B6, B7, B__FFs_pin11,
       BADD0, BADD1, BADD2, BADD3, BADD4, BADD5, BADD6, BADD7, CINAS, NOTB0, NOTB1, NOTB2, NOTB3, NOTB4,
       NOTB5, NOTB6, NOTB7, NOTTRIOUT, OR_2_pin3, OR_2_pin6, OR_2_pin8, OR_2_pin10, OR_2_pin11, OR_pin3,
       OR_pin6, OR_pin8, OR_pin11, OUT0, OUT1, OUT2, OUT3, OUT4, OUT5, OUT6, OUT7;

  Seven_Seg_Hex seven_seg_hex_1 (.d({A7, A6, A5, A4}), .dp(1'b0));
  LED led_1 (.in(A7));
  LED led_2 (.in(A6));
  LED led_3 (.in(A5));
  Seven_Seg_Hex seven_seg_hex_2 (.d({OUT7, OUT6, OUT5, OUT4}), .dp(1'b0));
  LED led_4 (.in(OUT7));
  LED led_5 (.in(OUT6));
  LED led_6 (.in(OUT5));
  Seven_Seg_Hex seven_seg_hex_3 (.d({A3, A2, A1, A0}), .dp(1'b0));
  LED led_7 (.in(A4));
  LED led_8 (.in(A3));
  LED led_9 (.in(A2));
  LED led_10 (.in(A1));
  Seven_Seg_Hex seven_seg_hex_4 (.d({OUT3, OUT2, OUT1, OUT0}), .dp(1'b0));
  LED led_11 (.in(OUT4));
  LED led_12 (.in(OUT3));
  LED led_13 (.in(OUT2));
  LED led_14 (.in(OUT1));
  LED led_15 (.in(A0));
  LED led_16 (.in(COUT));
  LED led_17 (.in(OUT0));
  Seven_Seg_Hex seven_seg_hex_5 (.d({B7, B6, B5, B4}), .dp(1'b0));
  LED led_18 (.in(B7));
  LED led_19 (.in(B6));
  LED led_20 (.in(B5));
  LED led_21 (.in(ZOUT));
  Seven_Seg_Hex seven_seg_hex_6 (.d({B3, B2, B1, B0}), .dp(1'b0));
  LED led_22 (.in(B4));
  LED led_23 (.in(B3));
  LED led_24 (.in(B2));
  LED led_25 (.in(B1));
  LED led_26 (.in(B0));
  LED led_27 (.in(CIN));
  _74273 A__FFs (
    .pin1(1'b1), .pin2(A0), .pin3(D[0]), .pin4(D[1]), .pin5(A1), .pin6(A2), .pin7(D[2]), .pin8(D[3]),
    .pin9(A3), .pin10(1'b0), .pin11(A__FFs_pin11), .pin12(A4), .pin13(D[4]), .pin14(D[5]), .pin15(A5),
    .pin16(A6), .pin17(D[6]), .pin18(D[7]), .pin19(A7), .pin20(1'b1));
  _74273 B__FFs (
    .pin1(1'b1), .pin2(B0), .pin3(D[0]), .pin4(D[1]), .pin5(B1), .pin6(B2), .pin7(D[2]), .pin8(D[3]),
    .pin9(B3), .pin10(1'b0), .pin11(B__FFs_pin11), .pin12(B4), .pin13(D[4]), .pin14(D[5]), .pin15(B5),
    .pin16(B6), .pin17(D[6]), .pin18(D[7]), .pin19(B7), .pin20(1'b1));
  _7408 AND (
    .pin1(CLCK), .pin2(LDA), .pin3(A__FFs_pin11), .pin4(CLCK), .pin5(LDB), .pin6(B__FFs_pin11), .pin7(1'b0),
    .pin9(1'b0), .pin10(1'b0), .pin12(1'b0), .pin13(1'b0), .pin14(1'b1));  // open: pin8, pin11
  _7404 NOT (
    .pin1(B0), .pin2(NOTB0), .pin3(B1), .pin4(NOTB1), .pin5(B2), .pin6(NOTB2), .pin7(1'b0), .pin8(NOTB3),
    .pin9(B3), .pin11(1'b0), .pin13(1'b0), .pin14(1'b1));  // open: pin10, pin12
  _7404 NOT_2 (
    .pin1(B4), .pin2(NOTB4), .pin3(B5), .pin4(NOTB5), .pin5(B6), .pin6(NOTB6), .pin7(1'b0), .pin8(NOTB7),
    .pin9(B7), .pin11(1'b0), .pin13(1'b0), .pin14(1'b1));  // open: pin10, pin12
  _7432 OR (
    .pin1(OUT0), .pin2(OUT1), .pin3(OR_pin3), .pin4(OUT2), .pin5(OUT3), .pin6(OR_pin6), .pin7(1'b0),
    .pin8(OR_pin8), .pin9(OUT4), .pin10(OUT5), .pin11(OR_pin11), .pin12(OUT6), .pin13(OUT7), .pin14(1'b1));
  _74153 MUX___0_1 (
    .pin1(1'b0), .pin2(OP[1]), .pin3(1'b1), .pin4(1'b1), .pin5(NOTB0), .pin6(B0), .pin7(BADD0), .pin8(1'b0),
    .pin9(BADD1), .pin10(B1), .pin11(NOTB1), .pin12(1'b0), .pin13(1'b1), .pin14(OP[0]), .pin15(1'b0),
    .pin16(1'b1));
  _74153 MUX___2_3 (
    .pin1(1'b0), .pin2(OP[1]), .pin3(1'b1), .pin4(1'b0), .pin5(NOTB2), .pin6(B2), .pin7(BADD2), .pin8(1'b0),
    .pin9(BADD3), .pin10(B3), .pin11(NOTB3), .pin12(1'b0), .pin13(1'b1), .pin14(OP[0]), .pin15(1'b0),
    .pin16(1'b1));
  _7432 OR_2 (
    .pin1(OR_pin3), .pin2(OR_pin6), .pin3(OR_2_pin3), .pin4(OR_pin11), .pin5(OR_pin8), .pin6(OR_2_pin6),
    .pin7(1'b0), .pin8(OR_2_pin8), .pin9(OP[1]), .pin10(OR_2_pin10), .pin11(OR_2_pin11), .pin12(OR_2_pin6),
    .pin13(OR_2_pin3), .pin14(1'b1));
  _74153 MUX___4_5 (
    .pin1(1'b0), .pin2(OP[1]), .pin3(1'b1), .pin4(1'b0), .pin5(NOTB4), .pin6(B4), .pin7(BADD4), .pin8(1'b0),
    .pin9(BADD5), .pin10(B5), .pin11(NOTB5), .pin12(1'b0), .pin13(1'b1), .pin14(OP[0]), .pin15(1'b0),
    .pin16(1'b1));
  _74153 MUX___6_7 (
    .pin1(1'b0), .pin2(OP[1]), .pin3(1'b1), .pin4(1'b0), .pin5(NOTB6), .pin6(B6), .pin7(BADD6), .pin8(1'b0),
    .pin9(BADD7), .pin10(B7), .pin11(NOTB7), .pin12(1'b0), .pin13(1'b1), .pin14(OP[0]), .pin15(1'b0),
    .pin16(1'b1));
  _7404 NOT_3 (
    .pin1(OR_2_pin11), .pin2(ZOUT), .pin3(CIN), .pin4(OR_2_pin10), .pin5(OR_2_pin8), .pin6(CINAS),
    .pin7(1'b0), .pin9(1'b0), .pin11(1'b0), .pin12(NOTTRIOUT), .pin13(OUT), .pin14(1'b1));  // open: pin8, pin10
  _74283 ADD (
    .pin1(OUT1), .pin2(BADD1), .pin3(A1), .pin4(OUT0), .pin5(A0), .pin6(BADD0), .pin7(CINAS), .pin8(1'b0),
    .pin9(ADD_pin9), .pin10(OUT3), .pin11(BADD3), .pin12(A3), .pin13(OUT2), .pin14(A2), .pin15(BADD2),
    .pin16(1'b1));
  _74283 ADD_2 (
    .pin1(OUT5), .pin2(BADD5), .pin3(A5), .pin4(OUT4), .pin5(A4), .pin6(BADD4), .pin7(ADD_pin9), .pin8(1'b0),
    .pin9(COUT), .pin10(OUT7), .pin11(BADD7), .pin12(A7), .pin13(OUT6), .pin14(A6), .pin15(BADD6),
    .pin16(1'b1));
  _74244 _74244_1 (
    .pin1(NOTTRIOUT), .pin2(OUT0), .pin3(Q[7]), .pin4(OUT1), .pin5(Q[6]), .pin6(OUT2), .pin7(Q[5]),
    .pin8(OUT3), .pin9(Q[4]), .pin10(1'b0), .pin11(OUT4), .pin12(Q[3]), .pin13(OUT5), .pin14(Q[2]),
    .pin15(OUT6), .pin16(Q[1]), .pin17(OUT7), .pin18(Q[0]), .pin19(NOTTRIOUT), .pin20(1'b1));

  // Other names for the same wires on the sheet: CINT = CIN; TRIOUT = OUT; TRIOUT0 = Q[0]; TRIOUT1 = Q[1];
  //   TRIOUT2 = Q[2]; TRIOUT3 = Q[3]; TRIOUT4 = Q[4]; TRIOUT5 = Q[5]; TRIOUT6 = Q[6]; TRIOUT7 = Q[7]

  // Notes on the sheet:
  //   D: default 3
  //   NOTES
  //   Follows the 6502 sub behaviour where CIN
  //   must be set for correct subtraction
  //   0 0 ADD
  //   0 1 SUB
  //   1 0 INC
  //   1 1 DEC
  //   Maybe better with two inputs - A/B?
  //   A
  //   Out
  //   B
  //   ZOUT, Apply carry in
endmodule

/* Test case ADD:
CLCK D    OUT LDA   LDB OP   CIN Q  COUT ZOUT 
C    0x21 1   1     0   0b00 0   x    x    x
C    0x32 1   0     1   0b00 0   0x53 0    0
C    0    1   1     0   0b00 0   x    x    x
C    0    1   0     1   0b00 0   0x0  0    1
C    0xDD 1   1     0   0b00 0   x    x    x
C    0xEE 1   0     1   0b00 0   x    1    0
*/

/* Test case INC:
CLCK D    OUT  LDA   LDB OP   CIN Q    COUT ZOUT
C    0x21 1    1     0   0b10 0   0x22 x    x
C    0x21 1    1     0   0b10 1   0x22 x    x
*/

/* Test case SUB:
CLCK D    OUT LDA   LDB OP   CIN  Q    COUT ZOUT
C    0x63 1   1     0   0b01  0   x    x    x
C    0x32 1   0     1   0b01  1   0x31 1    0
C    0    1   1     0   0b01  0   x    x    x
C    0    1   0     1   0b01  1   0x0  1    1
*/

/* Test case DEC:
CLCK D    OUT LDA   LDB OP   CIN Q    COUT ZOUT
C    0x21 1   1     0   0b11 0   0x20 x    x
C    0x21 1   1     0   0b11 1   0x20 x    x
*/
