// Digital circuit ALU.dig as structural Verilog
module ALU (
  input  [7:0] AIN,
  input  [7:0] BIN,
  input  CIN,
  input  LDA,
  input  LDB,
  input  OUT,
  input  [1:0] OP,
  input  CLCK,
  output [7:0] Q,
  output ZOUT,
  output COUT,
  output [7:0] lt_A_gt,
  output [7:0] lt_B_gt
);

  wire _7400_1_pin3, _7400_1_pin6, A__FFs_pin11, ADD_pin9, B__FFs_pin11, BADD0, BADD1, BADD2, BADD3, BADD4,
       BADD5, BADD6, BADD7, CADJ, NOTB0, NOTB1, NOTB2, NOTB3, NOTB4, NOTB5, NOTB6, NOTB7, NOTTRIOUT,
       OR_2_pin3, OR_2_pin6, OR_2_pin11, OR_pin3, OR_pin6, OR_pin8, OR_pin11, OUT0, OUT1, OUT2, OUT3, OUT4,
       OUT5, OUT6, OUT7;

  Seven_Seg_Hex seven_seg_hex_1 (.d(lt_A_gt[7:4]), .dp(1'b0));
  LED led_1 (.in(lt_A_gt[7]));
  LED led_2 (.in(lt_A_gt[6]));
  LED led_3 (.in(lt_A_gt[5]));
  Seven_Seg_Hex seven_seg_hex_2 (.d({OUT7, OUT6, OUT5, OUT4}), .dp(1'b0));
  LED led_4 (.in(OUT7));
  LED led_5 (.in(OUT6));
  LED led_6 (.in(OUT5));
  Seven_Seg_Hex seven_seg_hex_3 (.d(lt_A_gt[3:0]), .dp(1'b0));
  LED led_7 (.in(lt_A_gt[4]));
  LED led_8 (.in(lt_A_gt[3]));
  LED led_9 (.in(lt_A_gt[2]));
  LED led_10 (.in(lt_A_gt[1]));
  Seven_Seg_Hex seven_seg_hex_4 (.d({OUT3, OUT2, OUT1, OUT0}), .dp(1'b0));
  LED led_11 (.in(OUT4));
  LED led_12 (.in(OUT3));
  LED led_13 (.in(OUT2));
  LED led_14 (.in(OUT1));
  LED led_15 (.in(lt_A_gt[0]));
  LED led_16 (.in(OUT0));
  LED led_17 (.in(ZOUT));
  LED led_18 (.in(COUT));
  Seven_Seg_Hex seven_seg_hex_5 (.d(lt_B_gt[7:4]), .dp(1'b0));
  LED led_19 (.in(lt_B_gt[7]));
  LED led_20 (.in(lt_B_gt[6]));
  LED led_21 (.in(lt_B_gt[5]));
  Seven_Seg_Hex seven_seg_hex_6 (.d(lt_B_gt[3:0]), .dp(1'b0));
  LED led_22 (.in(lt_B_gt[4]));
  LED led_23 (.in(lt_B_gt[3]));
  LED led_24 (.in(lt_B_gt[2]));
  LED led_25 (.in(lt_B_gt[1]));
  LED led_26 (.in(lt_B_gt[0]));
  _74273 A__FFs (
    .pin1(1'b1), .pin2(lt_A_gt[0]), .pin3(AIN[0]), .pin4(AIN[1]), .pin5(lt_A_gt[1]), .pin6(lt_A_gt[2]),
    .pin7(AIN[2]), .pin8(AIN[3]), .pin9(lt_A_gt[3]), .pin10(1'b0), .pin11(A__FFs_pin11), .pin12(lt_A_gt[4]),
    .pin13(AIN[4]), .pin14(AIN[5]), .pin15(lt_A_gt[5]), .pin16(lt_A_gt[6]), .pin17(AIN[6]), .pin18(AIN[7]),
    .pin19(lt_A_gt[7]), .pin20(1'b1));
  _74273 B__FFs (
    .pin1(1'b1), .pin2(lt_B_gt[0]), .pin3(BIN[0]), .pin4(BIN[1]), .pin5(lt_B_gt[1]), .pin6(lt_B_gt[2]),
    .pin7(BIN[2]), .pin8(BIN[3]), .pin9(lt_B_gt[3]), .pin10(1'b0), .pin11(B__FFs_pin11), .pin12(lt_B_gt[4]),
    .pin13(BIN[4]), .pin14(BIN[5]), .pin15(lt_B_gt[5]), .pin16(lt_B_gt[6]), .pin17(BIN[6]), .pin18(BIN[7]),
    .pin19(lt_B_gt[7]), .pin20(1'b1));
  _7400 _7400_1 (
    .pin1(OP[1]), .pin2(OP[1]), .pin3(_7400_1_pin3), .pin4(_7400_1_pin3), .pin5(CIN), .pin6(_7400_1_pin6),
    .pin7(1'b0), .pin8(CADJ), .pin9(_7400_1_pin6), .pin10(_7400_1_pin6), .pin12(1'b0), .pin13(1'b0),
    .pin14(1'b1));  // open: pin11
  _7408 AND (
    .pin1(CLCK), .pin2(LDA), .pin3(A__FFs_pin11), .pin4(CLCK), .pin5(LDB), .pin6(B__FFs_pin11), .pin7(1'b0),
    .pin9(1'b0), .pin10(1'b0), .pin12(1'b0), .pin13(1'b0), .pin14(1'b1));  // open: pin8, pin11
  _7432 OR (
    .pin1(OUT0), .pin2(OUT1), .pin3(OR_pin3), .pin4(OUT2), .pin5(OUT3), .pin6(OR_pin6), .pin7(1'b0),
    .pin8(OR_pin8), .pin9(OUT4), .pin10(OUT5), .pin11(OR_pin11), .pin12(OUT6), .pin13(OUT7), .pin14(1'b1));
  _7404 NOT (
    .pin1(lt_B_gt[0]), .pin2(NOTB0), .pin3(lt_B_gt[1]), .pin4(NOTB1), .pin5(lt_B_gt[2]), .pin6(NOTB2),
    .pin7(1'b0), .pin8(NOTB3), .pin9(lt_B_gt[3]), .pin11(1'b0), .pin12(NOTTRIOUT), .pin13(OUT), .pin14(1'b1));  // open: pin10
  _7404 NOT_2 (
    .pin1(lt_B_gt[4]), .pin2(NOTB4), .pin3(lt_B_gt[5]), .pin4(NOTB5), .pin5(lt_B_gt[6]), .pin6(NOTB6),
    .pin7(1'b0), .pin8(NOTB7), .pin9(lt_B_gt[7]), .pin11(1'b0), .pin13(1'b0), .pin14(1'b1));  // open: pin10, pin12
  _7432 OR_2 (
    .pin1(OR_pin3), .pin2(OR_pin6), .pin3(OR_2_pin3), .pin4(OR_pin11), .pin5(OR_pin8), .pin6(OR_2_pin6),
    .pin7(1'b0), .pin9(1'b0), .pin10(1'b0), .pin11(OR_2_pin11), .pin12(OR_2_pin6), .pin13(OR_2_pin3),
    .pin14(1'b1));  // open: pin8
  _74153 MUX___0_1 (
    .pin1(1'b0), .pin2(OP[1]), .pin3(1'b1), .pin4(1'b1), .pin5(NOTB0), .pin6(lt_B_gt[0]), .pin7(BADD0),
    .pin8(1'b0), .pin9(BADD1), .pin10(lt_B_gt[1]), .pin11(NOTB1), .pin12(1'b0), .pin13(1'b1), .pin14(OP[0]),
    .pin15(1'b0), .pin16(1'b1));
  _74153 MUX___2_3 (
    .pin1(1'b0), .pin2(OP[1]), .pin3(1'b1), .pin4(1'b0), .pin5(NOTB2), .pin6(lt_B_gt[2]), .pin7(BADD2),
    .pin8(1'b0), .pin9(BADD3), .pin10(lt_B_gt[3]), .pin11(NOTB3), .pin12(1'b0), .pin13(1'b1), .pin14(OP[0]),
    .pin15(1'b0), .pin16(1'b1));
  _7404 NOT_3 (
    .pin1(OR_2_pin11), .pin2(ZOUT), .pin3(1'b0), .pin5(1'b0), .pin7(1'b0), .pin9(1'b0), .pin11(1'b0),
    .pin13(1'b0), .pin14(1'b1));  // open: pin4, pin6, pin8, pin10, pin12
  _74153 MUX___4_5 (
    .pin1(1'b0), .pin2(OP[1]), .pin3(1'b1), .pin4(1'b0), .pin5(NOTB4), .pin6(lt_B_gt[4]), .pin7(BADD4),
    .pin8(1'b0), .pin9(BADD5), .pin10(lt_B_gt[5]), .pin11(NOTB5), .pin12(1'b0), .pin13(1'b1), .pin14(OP[0]),
    .pin15(1'b0), .pin16(1'b1));
  _74153 MUX___6_7 (
    .pin1(1'b0), .pin2(OP[1]), .pin3(1'b1), .pin4(1'b0), .pin5(NOTB6), .pin6(lt_B_gt[6]), .pin7(BADD6),
    .pin8(1'b0), .pin9(BADD7), .pin10(lt_B_gt[7]), .pin11(NOTB7), .pin12(1'b0), .pin13(1'b1), .pin14(OP[0]),
    .pin15(1'b0), .pin16(1'b1));
  _74283 ADD (
    .pin1(OUT1), .pin2(BADD1), .pin3(lt_A_gt[1]), .pin4(OUT0), .pin5(lt_A_gt[0]), .pin6(BADD0), .pin7(CADJ),
    .pin8(1'b0), .pin9(ADD_pin9), .pin10(OUT3), .pin11(BADD3), .pin12(lt_A_gt[3]), .pin13(OUT2),
    .pin14(lt_A_gt[2]), .pin15(BADD2), .pin16(1'b1));
  _74283 ADD_2 (
    .pin1(OUT5), .pin2(BADD5), .pin3(lt_A_gt[5]), .pin4(OUT4), .pin5(lt_A_gt[4]), .pin6(BADD4),
    .pin7(ADD_pin9), .pin8(1'b0), .pin9(COUT), .pin10(OUT7), .pin11(BADD7), .pin12(lt_A_gt[7]), .pin13(OUT6),
    .pin14(lt_A_gt[6]), .pin15(BADD6), .pin16(1'b1));
  _74244 _74244_1 (
    .pin1(NOTTRIOUT), .pin2(OUT0), .pin3(Q[7]), .pin4(OUT1), .pin5(Q[6]), .pin6(OUT2), .pin7(Q[5]),
    .pin8(OUT3), .pin9(Q[4]), .pin10(1'b0), .pin11(OUT4), .pin12(Q[3]), .pin13(OUT5), .pin14(Q[2]),
    .pin15(OUT6), .pin16(Q[1]), .pin17(OUT7), .pin18(Q[0]), .pin19(NOTTRIOUT), .pin20(1'b1));

  // Other names for the same wires on the sheet: A0 = lt_A_gt[0]; A1 = lt_A_gt[1]; A2 = lt_A_gt[2]; A3 = lt_A_gt[3];
  //   A4 = lt_A_gt[4]; A5 = lt_A_gt[5]; A6 = lt_A_gt[6]; A7 = lt_A_gt[7]; B0 = lt_B_gt[0]; B1 = lt_B_gt[1];
  //   B2 = lt_B_gt[2]; B3 = lt_B_gt[3]; B4 = lt_B_gt[4]; B5 = lt_B_gt[5]; B6 = lt_B_gt[6]; B7 = lt_B_gt[7];
  //   TRIOUT = OUT; TRIOUT0 = Q[0]; TRIOUT1 = Q[1]; TRIOUT2 = Q[2]; TRIOUT3 = Q[3]; TRIOUT4 = Q[4]; TRIOUT5 = Q[5];
  //   TRIOUT6 = Q[6]; TRIOUT7 = Q[7]

  // Notes on the sheet:
  //   AIN: default 3
  //   BIN: default 3
  //   NOTES
  //   Follows the 6502 sub behaviour where CIN
  //   must be set for correct subtraction
  //   0 0 ADD
  //   0 1 SUB
  //   1 0 INC
  //   1 1 DEC
  //   A
  //   Out
  //   B
  //   Carry
  //   ADD, SUB, INC and DEC (and invert out)
  //   ZOUT
  //   Tristate out
endmodule

/* Test case ADD:
CLCK AIN  BIN    CIN OUT LDA   LDB OP   Q    ZOUT 
C    0x21 0      0   1   1     0   0b00 x    x
C    0    0x32   0   1   0     1   0b00 0x53 0
C    0    0      0   1   1     0   0b00 x    x
C    0    0      0   1   0     1   0b00 0x0  1
C    0xDD 0      0   1   1     0   0b00 x    x
C    0    0xEE   0   1   0     1   0b00 x    0
*/

/* Test case INC:
CLCK AIN  OUT  LDA   LDB OP   Q    ZOUT CIN
C    0x21 1    1     0   0b10 0x22 x    1
C    0x21 1    1     0   0b10 0x22 x    0
*/

/* Test case SUB:
CLCK AIN  BIN  OUT CIN LDA   LDB OP    Q    ZOUT COUT
C    0x63 0x32 1   1   1     1   0b01  0x31 x    1
C    0    0    1   1   1     1   0b01  0    x    1
*/

/* Test case DEC:
CLCK AIN  OUT LDA   LDB OP   Q    ZOUT CIN
C    0x21 1   1     0   0b11 0x20 x    1
C    0x21 1   1     0   0b11 0x20 x    0
*/
