// Digital circuit Address Decoder.dig as structural Verilog
module Address_Decoder (
  input  [7:0] A,
  input  CS,
  output CS0,
  output CS1,
  output CS2
);

  wire AND_2_pin3, AND_2_pin6, AND_3_pin10, AND_pin3, AND_pin6, NOT_pin2, NOT_pin3, NOT_pin4, NOT_pin5,
       NOT_pin6;

  _7404 NOT (
    .pin1(A[4]), .pin2(NOT_pin2), .pin3(NOT_pin3), .pin4(NOT_pin4), .pin5(NOT_pin5), .pin6(NOT_pin6),
    .pin7(1'b0), .pin9(1'b0), .pin11(1'b0), .pin13(1'b0), .pin14(1'b1));  // open: pin8, pin10, pin12
  _7408 AND (
    .pin1(NOT_pin2), .pin2(A[5]), .pin3(AND_pin3), .pin4(A[7]), .pin5(A[6]), .pin6(AND_pin6), .pin7(1'b0),
    .pin9(1'b0), .pin10(1'b0), .pin11(NOT_pin3), .pin12(AND_pin6), .pin13(AND_pin3), .pin14(1'b1));  // open: pin8
  _7408 AND_2 (
    .pin1(A[4]), .pin2(A[5]), .pin3(AND_2_pin3), .pin4(A[7]), .pin5(A[6]), .pin6(AND_2_pin6), .pin7(1'b0),
    .pin9(1'b0), .pin10(1'b0), .pin11(NOT_pin5), .pin12(AND_2_pin6), .pin13(AND_2_pin3), .pin14(1'b1));  // open: pin8
  _7408 AND_3 (
    .pin1(CS), .pin2(NOT_pin5), .pin3(CS2), .pin4(CS), .pin5(NOT_pin3), .pin6(CS1), .pin7(1'b0), .pin8(CS0),
    .pin9(CS), .pin10(AND_3_pin10), .pin11(AND_3_pin10), .pin12(NOT_pin6), .pin13(NOT_pin4), .pin14(1'b1));

  // Notes on the sheet:
  //   Banks
  //   0xF0...0xFF - I/O
  //   0xE0...0xEF - RAM
  //   0x00...0xDF - ROM
endmodule

/* Test case:
CS A    CS0 CS1 CS2 
1  0xFF 0   0   1   
1  0xE1 0   1   0
1  0xCF 1   0   0  
0  0xFF 0   0   0   
0  0xE1 0   0   0
0  0xCF 0   0   0  
*/
