// Digital circuit Fake carry.dig as structural Verilog
module Fake_carry (
  input  [1:0] OP,
  output COUT
);

  wire _7400_1_pin3, _7400_1_pin6;

  LED OP1 (.in(OP[1]));
  LED OP0 (.in(OP[0]));
  LED u_COUT (.in(COUT));
  _7400 _7400_1 (
    .pin1(OP[1]), .pin2(OP[1]), .pin3(_7400_1_pin3), .pin4(_7400_1_pin3), .pin5(OP[0]), .pin6(_7400_1_pin6),
    .pin7(1'b0), .pin8(COUT), .pin9(_7400_1_pin6), .pin10(_7400_1_pin6), .pin12(1'b0), .pin13(1'b0),
    .pin14(1'b1));  // open: pin11
endmodule
