// Digital circuit MBR Layout.dig as structural Verilog
module MBR_Layout (
);

  wire _74377_1_pin1, CLOCK, FROMCDATA0, FROMCDATA1, FROMCDATA2, FROMCDATA3, FROMCDATA4, FROMCDATA5,
       FROMCDATA6, FROMCDATA7, FROMMBR0, FROMMBR1, FROMMBR2, FROMMBR3, FROMMBR4, FROMMBR5, FROMMBR6,
       FROMMBR7, FROMXCDATA0, FROMXCDATA1, FROMXCDATA2, FROMXCDATA3, FROMXCDATA4, FROMXCDATA5, FROMXCDATA6,
       FROMXCDATA7, FROMXDATA0, FROMXDATA1, FROMXDATA2, FROMXDATA3, FROMXDATA4, FROMXDATA5, FROMXDATA6,
       FROMXDATA7, MBR_LD_CDATA, MBR_LD_XDATA, MBR_OUT_CDATA, MBR_OUT_XDATA, Not_pin9, Not_pin10,
       Route_to_CDATA__Tristate_pin1, TOCDATA0, TOCDATA1, TOCDATA2, TOCDATA3, TOCDATA4, TOCDATA5, TOCDATA6,
       TOCDATA7, TOXDATA0, TOXDATA1, TOXDATA2, TOXDATA3, TOXDATA4, TOXDATA5, TOXDATA6, TOXDATA7;
  wire [7:0] XDATA_CDATA;

  _74157 Load_from_XDATA_CDATA_high__MUX (
    .pin1(MBR_LD_CDATA), .pin2(FROMXDATA4), .pin3(FROMCDATA4), .pin4(XDATA_CDATA[4]), .pin5(FROMXDATA5),
    .pin6(FROMCDATA5), .pin7(XDATA_CDATA[5]), .pin8(1'b0), .pin9(XDATA_CDATA[6]), .pin10(FROMCDATA6),
    .pin11(FROMXDATA6), .pin12(XDATA_CDATA[7]), .pin13(FROMCDATA7), .pin14(FROMXDATA7), .pin15(1'b0),
    .pin16(1'b1));
  _74377 _74377_1 (
    .pin1(_74377_1_pin1), .pin2(FROMMBR0), .pin3(FROMXCDATA0), .pin4(FROMXCDATA1), .pin5(FROMMBR1),
    .pin6(FROMMBR2), .pin7(FROMXCDATA2), .pin8(FROMXCDATA3), .pin9(FROMMBR3), .pin10(1'b0), .pin11(CLOCK),
    .pin12(FROMMBR4), .pin13(FROMXCDATA4), .pin14(FROMXCDATA5), .pin15(FROMMBR5), .pin16(FROMMBR6),
    .pin17(FROMXCDATA6), .pin18(FROMXCDATA7), .pin19(FROMMBR7), .pin20(1'b1));
  _74157 Load_from_XDATA_CDATA_low__MUX (
    .pin1(MBR_LD_CDATA), .pin2(FROMXDATA0), .pin3(FROMCDATA0), .pin4(XDATA_CDATA[0]), .pin5(FROMXDATA1),
    .pin6(FROMCDATA1), .pin7(XDATA_CDATA[1]), .pin8(1'b0), .pin9(XDATA_CDATA[2]), .pin10(FROMCDATA2),
    .pin11(FROMXDATA2), .pin12(XDATA_CDATA[3]), .pin13(FROMCDATA3), .pin14(FROMXDATA3), .pin15(1'b0),
    .pin16(1'b1));
  _74244 Route_to_CDATA__Tristate (
    .pin1(Route_to_CDATA__Tristate_pin1), .pin2(FROMMBR0), .pin3(TOCDATA7), .pin4(FROMMBR1), .pin5(TOCDATA6),
    .pin6(FROMMBR2), .pin7(TOCDATA5), .pin8(FROMMBR3), .pin9(TOCDATA4), .pin10(1'b0), .pin11(FROMMBR4),
    .pin12(TOCDATA3), .pin13(FROMMBR5), .pin14(TOCDATA2), .pin15(FROMMBR6), .pin16(TOCDATA1),
    .pin17(FROMMBR7), .pin18(TOCDATA0), .pin19(Route_to_CDATA__Tristate_pin1), .pin20(1'b1));
  _7404 Not (
    .pin8(_74377_1_pin1), .pin9(Not_pin9), .pin10(Not_pin10), .pin11(MBR_OUT_XDATA),
    .pin12(Route_to_CDATA__Tristate_pin1), .pin13(MBR_OUT_CDATA), .pin14(1'b1));  // open: pin1, pin2, pin3, pin4, pin5, pin6, pin7
  _7432 Load_control__Or (
    .pin1(MBR_LD_CDATA), .pin2(MBR_LD_XDATA), .pin3(Not_pin9), .pin7(1'b0), .pin14(1'b1));  // open: pin4, pin5, pin6, pin8, pin9, pin10, pin11, pin12, pin13
  _74244 Route_to_XDATA__Tristate (
    .pin1(Not_pin10), .pin2(FROMMBR0), .pin3(TOXDATA7), .pin4(FROMMBR1), .pin5(TOXDATA6), .pin6(FROMMBR2),
    .pin7(TOXDATA5), .pin8(FROMMBR3), .pin9(TOXDATA4), .pin10(1'b0), .pin11(FROMMBR4), .pin12(TOXDATA3),
    .pin13(FROMMBR5), .pin14(TOXDATA2), .pin15(FROMMBR6), .pin16(TOXDATA1), .pin17(FROMMBR7),
    .pin18(TOXDATA0), .pin19(Not_pin10), .pin20(1'b1));
endmodule
