// Digital circuit P.dig as structural Verilog
module P (
  input  LDZ,
  input  ZIN,
  input  CLCK,
  input  LDC,
  input  CIN,
  output C,
  output Z
);

  wire AND_pin3, AND_pin6, AND_pin8, AND_pin11, D_Flip_Flops_pin3, D_Flip_Flops_pin4, NOT_pin2, NOT_pin4;

  LED led_1 (.in(Z));
  LED led_2 (.in(C));
  _7404 NOT (
    .pin1(LDZ), .pin2(NOT_pin2), .pin3(LDC), .pin4(NOT_pin4), .pin5(1'b0), .pin7(1'b0), .pin9(1'b0),
    .pin11(1'b0), .pin13(1'b0), .pin14(1'b1));  // open: pin6, pin8, pin10, pin12
  _7408 AND (
    .pin1(ZIN), .pin2(LDZ), .pin3(AND_pin3), .pin4(Z), .pin5(NOT_pin2), .pin6(AND_pin6), .pin7(1'b0),
    .pin8(AND_pin8), .pin9(NOT_pin4), .pin10(C), .pin11(AND_pin11), .pin12(LDC), .pin13(CIN), .pin14(1'b1));
  _74273 D_Flip_Flops (
    .pin1(1'b1), .pin2(Z), .pin3(D_Flip_Flops_pin3), .pin4(D_Flip_Flops_pin4), .pin5(C), .pin7(1'b0),
    .pin8(1'b0), .pin10(1'b0), .pin11(CLCK), .pin13(1'b0), .pin14(1'b0), .pin17(1'b0), .pin18(1'b0),
    .pin20(1'b1));  // open: pin6, pin9, pin12, pin15, pin16, pin19
  _7432 OR (
    .pin1(AND_pin3), .pin2(AND_pin6), .pin3(D_Flip_Flops_pin3), .pin4(AND_pin11), .pin5(AND_pin8),
    .pin6(D_Flip_Flops_pin4), .pin7(1'b0), .pin9(1'b0), .pin10(1'b0), .pin12(1'b0), .pin13(1'b0), .pin14(1'b1));  // open: pin8, pin11

  // Notes on the sheet:
  //   Logic fronting the D-Flip flops
  //   multiplexes each flag between the input value 
  //   and its  current value.  So then provides
  //   a load enable line for each flag.
endmodule
