// Digital circuit PC-gen.dig as structural Verilog
module PC_gen (
  input  LD,
  input  INC,
  input  REL,
  input  [7:0] D,
  input  C,
  output [7:0] Q
);

  wire or_1_out;
  wire [7:0] multiplexer_1_out, multiplexer_2_out, PCADD_s;

  Seven_Seg_Hex seven_seg_hex_1 (.d(Q[3:0]), .dp(1'b0));
  Seven_Seg_Hex seven_seg_hex_2 (.d(Q[7:4]), .dp(1'b0));
  LED led_1 (.in(LD));
  LED led_2 (.in(INC));
  LED led_3 (.in(REL));
  Multiplexer #(.Bits(8)) multiplexer_1 (.sel(INC), .in_0(D), .in_1(8'h1), .out(multiplexer_1_out));
  Multiplexer #(.Bits(8)) multiplexer_2 (.sel(LD), .in_0(PCADD_s), .in_1(D), .out(multiplexer_2_out));
  or or_1 (or_1_out, INC, REL, LD);
  Add #(.Bits(8)) PCADD (.a(Q), .b(multiplexer_1_out), .c_i(1'b0), .s(PCADD_s));  // open: c_o
  Register #(.Bits(8)) PC (.D(multiplexer_2_out), .C(C), .en(or_1_out), .Q(Q));

  // Notes on the sheet:
  //   Q
endmodule
