// Digital circuit PC.dig as structural Verilog
module PC (
  input  LD,
  input  INC,
  input  REL,
  input  [7:0] D,
  input  C,
  output [7:0] Q
);

  wire ADD_IN_LOW_MUX_2_pin2, ADD_IN_LOW_MUX_2_pin6, ADD_IN_LOW_MUX_2_pin11, ADD_IN_LOW_MUX_2_pin15,
       ADD_IN_LOW_MUX_pin2, ADD_IN_LOW_MUX_pin6, ADD_IN_LOW_MUX_pin9, ADD_IN_LOW_MUX_pin11,
       ADD_IN_LOW_MUX_pin15, OR_pin3, OR_pin6, PC_IN_HIGH_MUX_pin4, PC_IN_HIGH_MUX_pin7, PC_IN_HIGH_MUX_pin9,
       PC_IN_HIGH_MUX_pin12, PC_IN_LOW_MUX_pin4, PC_IN_LOW_MUX_pin7, PC_IN_LOW_MUX_pin9, PC_IN_LOW_MUX_pin12,
       PC_pin11, S0, S1, S2, S3, S4, S5, S6, S7;

  Seven_Seg_Hex seven_seg_hex_1 (.d(Q[3:0]), .dp(1'b0));
  Seven_Seg_Hex seven_seg_hex_2 (.d(Q[7:4]), .dp(1'b0));
  LED led_1 (.in(LD));
  LED led_2 (.in(INC));
  LED led_3 (.in(REL));
  _74157 PC_IN_LOW_MUX (
    .pin1(LD), .pin2(S0), .pin3(D[0]), .pin4(PC_IN_LOW_MUX_pin4), .pin5(S1), .pin6(D[1]),
    .pin7(PC_IN_LOW_MUX_pin7), .pin8(1'b0), .pin9(PC_IN_LOW_MUX_pin9), .pin10(D[2]), .pin11(S2),
    .pin12(PC_IN_LOW_MUX_pin12), .pin13(D[3]), .pin14(S3), .pin15(1'b0), .pin16(1'b1));
  _74157 PC_IN_HIGH_MUX (
    .pin1(LD), .pin2(S4), .pin3(D[4]), .pin4(PC_IN_HIGH_MUX_pin4), .pin5(S5), .pin6(D[5]),
    .pin7(PC_IN_HIGH_MUX_pin7), .pin8(1'b0), .pin9(PC_IN_HIGH_MUX_pin9), .pin10(D[6]), .pin11(S6),
    .pin12(PC_IN_HIGH_MUX_pin12), .pin13(D[7]), .pin14(S7), .pin15(1'b0), .pin16(1'b1));
  _7432 OR (
    .pin1(REL), .pin2(LD), .pin3(OR_pin3), .pin4(OR_pin3), .pin5(INC), .pin6(OR_pin6), .pin7(1'b0),
    .pin9(1'b0), .pin10(1'b0), .pin12(1'b0), .pin13(1'b0), .pin14(1'b1));  // open: pin8, pin11
  _74273 PC (
    .pin1(1'b1), .pin2(Q[0]), .pin3(PC_IN_LOW_MUX_pin4), .pin4(PC_IN_LOW_MUX_pin7), .pin5(Q[1]), .pin6(Q[2]),
    .pin7(PC_IN_LOW_MUX_pin9), .pin8(PC_IN_LOW_MUX_pin12), .pin9(Q[3]), .pin10(1'b0), .pin11(PC_pin11),
    .pin12(Q[4]), .pin13(PC_IN_HIGH_MUX_pin4), .pin14(PC_IN_HIGH_MUX_pin7), .pin15(Q[5]), .pin16(Q[6]),
    .pin17(PC_IN_HIGH_MUX_pin9), .pin18(PC_IN_HIGH_MUX_pin12), .pin19(Q[7]), .pin20(1'b1));
  _7408 AND (
    .pin1(C), .pin2(OR_pin6), .pin3(PC_pin11), .pin4(1'b0), .pin5(1'b0), .pin7(1'b0), .pin8(1'b0),
    .pin9(1'b0), .pin10(1'b0), .pin12(1'b0), .pin13(1'b0), .pin14(1'b1));  // open: pin6, pin11
  _74283 ADD_IN_LOW_MUX (
    .pin1(S1), .pin2(ADD_IN_LOW_MUX_pin2), .pin3(Q[1]), .pin4(S0), .pin5(Q[0]), .pin6(ADD_IN_LOW_MUX_pin6),
    .pin7(1'b0), .pin8(1'b0), .pin9(ADD_IN_LOW_MUX_pin9), .pin10(S3), .pin11(ADD_IN_LOW_MUX_pin11),
    .pin12(Q[3]), .pin13(S2), .pin14(Q[2]), .pin15(ADD_IN_LOW_MUX_pin15), .pin16(1'b1));
  _74283 ADD_IN_LOW_MUX_2 (
    .pin1(S5), .pin2(ADD_IN_LOW_MUX_2_pin2), .pin3(Q[5]), .pin4(S4), .pin5(Q[4]),
    .pin6(ADD_IN_LOW_MUX_2_pin6), .pin7(ADD_IN_LOW_MUX_pin9), .pin8(1'b0), .pin10(S6),
    .pin11(ADD_IN_LOW_MUX_2_pin11), .pin12(Q[7]), .pin13(S7), .pin14(Q[6]), .pin15(ADD_IN_LOW_MUX_2_pin15),
    .pin16(1'b1));  // open: pin9
  _74157 ADD_IN_LOW (
    .pin1(INC), .pin2(D[0]), .pin3(1'b1), .pin4(ADD_IN_LOW_MUX_pin6), .pin5(D[1]), .pin6(1'b0),
    .pin7(ADD_IN_LOW_MUX_pin2), .pin8(1'b0), .pin9(ADD_IN_LOW_MUX_pin15), .pin10(1'b0), .pin11(D[2]),
    .pin12(ADD_IN_LOW_MUX_pin11), .pin13(1'b0), .pin14(D[3]), .pin15(1'b0), .pin16(1'b1));
  _74157 ADD_IN_HIGH (
    .pin1(INC), .pin2(D[4]), .pin3(1'b0), .pin4(ADD_IN_LOW_MUX_2_pin6), .pin5(D[5]), .pin6(1'b0),
    .pin7(ADD_IN_LOW_MUX_2_pin2), .pin8(1'b0), .pin9(ADD_IN_LOW_MUX_2_pin15), .pin10(1'b0), .pin11(D[6]),
    .pin12(ADD_IN_LOW_MUX_2_pin11), .pin13(1'b0), .pin14(D[7]), .pin15(1'b0), .pin16(1'b1));
endmodule
