// Digital circuit RegisterWithEdgeTrigger.dig as structural Verilog
module RegisterWithEdgeTrigger (
  input  C,
  input  [7:0] D,
  input  OUT,
  input  LD,
  output [7:0] Q,
  output [7:0] lt_Q_gt
);

  wire AND_pin2, AND_pin3, D_Flip_Flops_pin11, NOT_pin4, NOT_pin6, NOT_pin11, Tri_State_pin1;

  Seven_Seg_Hex seven_seg_hex_1 (.d(Q[7:4]), .dp(1'b0));
  Seven_Seg_Hex seven_seg_hex_2 (.d(Q[3:0]), .dp(1'b0));
  Seven_Seg_Hex seven_seg_hex_3 (.d(lt_Q_gt[7:4]), .dp(1'b0));
  Seven_Seg_Hex seven_seg_hex_4 (.d(lt_Q_gt[3:0]), .dp(1'b0));
  _74273 D_Flip_Flops (
    .pin1(1'b1), .pin2(lt_Q_gt[0]), .pin3(D[0]), .pin4(D[1]), .pin5(lt_Q_gt[1]), .pin6(lt_Q_gt[2]),
    .pin7(D[2]), .pin8(D[3]), .pin9(lt_Q_gt[3]), .pin10(1'b0), .pin11(D_Flip_Flops_pin11),
    .pin12(lt_Q_gt[4]), .pin13(D[4]), .pin14(D[5]), .pin15(lt_Q_gt[5]), .pin16(lt_Q_gt[6]), .pin17(D[6]),
    .pin18(D[7]), .pin19(lt_Q_gt[7]), .pin20(1'b1));
  _7408 AND (
    .pin1(C), .pin2(AND_pin2), .pin3(AND_pin3), .pin4(AND_pin3), .pin5(LD), .pin6(D_Flip_Flops_pin11),
    .pin7(1'b0), .pin9(1'b0), .pin10(1'b0), .pin12(1'b0), .pin13(1'b0), .pin14(1'b1));  // open: pin8, pin11
  _74244 Tri_State (
    .pin1(Tri_State_pin1), .pin2(lt_Q_gt[0]), .pin3(Q[7]), .pin4(lt_Q_gt[1]), .pin5(Q[6]), .pin6(lt_Q_gt[2]),
    .pin7(Q[5]), .pin8(lt_Q_gt[3]), .pin9(Q[4]), .pin10(1'b0), .pin11(lt_Q_gt[4]), .pin12(Q[3]),
    .pin13(lt_Q_gt[5]), .pin14(Q[2]), .pin15(lt_Q_gt[6]), .pin16(Q[1]), .pin17(lt_Q_gt[7]), .pin18(Q[0]),
    .pin19(Tri_State_pin1), .pin20(1'b1));
  _7404 NOT (
    .pin1(OUT), .pin2(Tri_State_pin1), .pin3(C), .pin4(NOT_pin4), .pin5(NOT_pin4), .pin6(NOT_pin6),
    .pin7(1'b0), .pin9(1'b0), .pin10(AND_pin2), .pin11(NOT_pin11), .pin12(NOT_pin11), .pin13(NOT_pin6),
    .pin14(1'b1));  // open: pin8

  // Other names for the same wires on the sheet: lt_Q0_gt = lt_Q_gt[0]; lt_Q1_gt = lt_Q_gt[1]; lt_Q2_gt = lt_Q_gt[2];
  //   lt_Q3_gt = lt_Q_gt[3]; lt_Q4_gt = lt_Q_gt[4]; lt_Q5_gt = lt_Q_gt[5]; lt_Q6_gt = lt_Q_gt[6];
  //   lt_Q7_gt = lt_Q_gt[7]

  // Notes on the sheet:
  //   Q
  //   <Q>
endmodule
