// Digital circuit Zero.dig as structural Verilog
module Zero (
  input  [7:0] D,
  output ZOUT
);

  wire OR_2_pin3, OR_2_pin6, OR_2_pin11, OR_pin3, OR_pin6, OR_pin8, OR_pin11;

  Seven_Seg_Hex seven_seg_hex_1 (.d(D[7:4]), .dp(1'b0));
  Seven_Seg_Hex seven_seg_hex_2 (.d(D[3:0]), .dp(1'b0));
  LED led_1 (.in(D[7]));
  LED led_2 (.in(D[6]));
  LED led_3 (.in(D[5]));
  LED led_4 (.in(D[4]));
  LED led_5 (.in(D[3]));
  LED led_6 (.in(D[2]));
  LED led_7 (.in(ZOUT));
  LED led_8 (.in(D[1]));
  LED led_9 (.in(D[0]));
  _7432 OR (
    .pin1(D[0]), .pin2(D[1]), .pin3(OR_pin3), .pin4(D[2]), .pin5(D[3]), .pin6(OR_pin6), .pin7(1'b0),
    .pin8(OR_pin8), .pin9(D[4]), .pin10(D[5]), .pin11(OR_pin11), .pin12(D[6]), .pin13(D[7]), .pin14(1'b1));
  _7432 OR_2 (
    .pin1(OR_pin3), .pin2(OR_pin6), .pin3(OR_2_pin3), .pin4(OR_pin11), .pin5(OR_pin8), .pin6(OR_2_pin6),
    .pin7(1'b0), .pin9(1'b0), .pin10(1'b0), .pin11(OR_2_pin11), .pin12(OR_2_pin6), .pin13(OR_2_pin3),
    .pin14(1'b1));  // open: pin8
  _7404 NOT (
    .pin1(OR_2_pin11), .pin2(ZOUT), .pin3(1'b0), .pin5(1'b0), .pin7(1'b0), .pin9(1'b0), .pin11(1'b0),
    .pin13(1'b0), .pin14(1'b1));  // open: pin4, pin6, pin8, pin10, pin12

  // Other names for the same wires on the sheet: FROMD0 = D[0]; FROMD1 = D[1]; FROMD2 = D[2]; FROMD3 = D[3];
  //   FROMD4 = D[4]; FROMD5 = D[5]; FROMD6 = D[6]; FROMD7 = D[7]

  // Notes on the sheet:
  //   D: default 3
  //   D
  //   Out
  //   ZOUT
endmodule
