// Digital circuit Control-Unit-rel-addr.dig as structural Verilog
module Control_Unit_rel_addr (
  input  [7:0] MODEADDR,
  input  [7:0] OPCODEADDR,
  input  Z,
  input  RESET,
  input  CLOCK,
  output CDATA_LD_0,
  output CDATA_TO_CADDR,
  output MEM_LD_XDATA,
  output MEM_OUT_XDATA,
  output IR_LD_XDATA,
  output MBR_LD_XDATA,
  output MBR_OUT_XDATA,
  output MBR_LD_CDATA,
  output MBR_OUT_CDATA,
  output MAR_LD_CADDR,
  output PC_INC,
  output PC_REL_CDATA,
  output PC_LD_CDATA,
  output PCL_OUT_CDATA,
  output PC_OUT_CADDR,
  output A_LD_CDATA,
  output A_OUT_CDATA,
  output X_LD_CDATA,
  output X_OUT_CDATA,
  output PZ_LD,
  output ALUA_LD_CDATA,
  output ALUB_LD_CDATA,
  output ALUR_OUT_CDATA,
  output ALUOP_0,
  output ALUOP_1,
  output Z_SRC_CDATA,
  output CPU_ERR,
  output [7:0] lt_CAR_gt,
  output [7:0] lt_UPARAM_gt,
  output [7:0] lt_CARNEXT_gt,
  output [2:0] lt_CARNEXTSRC_gt
);

  wire And_2_pin3, And_2_pin6, And_3_pin2, And_3_pin5, And_3_pin11, And_pin3, And_pin6, And_pin8, And_pin10,
       BIT2_pin7, BIT2_pin9, BIT3_pin7, BIT3_pin9, BIT6_pin7, BIT6_pin9, BIT7_pin7, BIT7_pin9,
       CAR_plus_1_low_nibble_pin9, CAR_plus_offset_low_nibble_pin9, decoder_1_out_0, decoder_1_out_1,
       decoder_1_out_2, decoder_1_out_3, decoder_1_out_4, decoder_1_out_5, decoder_1_out_6, decoder_1_out_7,
       FROMOFFSET0, FROMOFFSET1, FROMOFFSET2, FROMOFFSET3, FROMOFFSET4, FROMOFFSET5, FROMOFFSET6,
       FROMOFFSET7, FROMPLUSONE0, FROMPLUSONE1, FROMPLUSONE2, FROMPLUSONE3, FROMPLUSONE4, FROMPLUSONE5,
       FROMPLUSONE6, FROMPLUSONE7, FROMuP0ADDR0, FROMuP0ADDR1, FROMuP0ADDR2, FROMuP0ADDR3, FROMuP0ADDR4,
       FROMuP0ADDR5, FROMuP0ADDR6, High_Nibble_pin10, High_Nibble_pin11, High_Nibble_pin13,
       High_Nibble_pin14, Low_Nibble_pin10, Low_Nibble_pin11, Low_Nibble_pin13, Low_Nibble_pin14, OR_2_pin3,
       OR_2_pin5, OR_2_pin11, OR_pin3, uJMP, uJMPINV, uP0, uP1, uP2, uZJMP;

  Seven_Seg_Hex seven_seg_hex_1 (.d(lt_CAR_gt[3:0]), .dp(1'b0));
  Seven_Seg_Hex seven_seg_hex_2 (.d(lt_CAR_gt[7:4]), .dp(1'b0));
  Seven_Seg_Hex seven_seg_hex_3 (.d(lt_CARNEXT_gt[7:4]), .dp(1'b0));
  Seven_Seg_Hex seven_seg_hex_4 (.d(lt_CARNEXT_gt[3:0]), .dp(1'b0));
  Seven_Seg_Hex seven_seg_hex_5 (.d(lt_UPARAM_gt[3:0]), .dp(1'b0));
  Seven_Seg_Hex seven_seg_hex_6 (.d(lt_UPARAM_gt[7:4]), .dp(1'b0));
  Decoder #(.Selector_Bits(3)) decoder_1 (
    .sel(lt_CARNEXTSRC_gt), .out_0(decoder_1_out_0), .out_1(decoder_1_out_1), .out_2(decoder_1_out_2),
    .out_3(decoder_1_out_3), .out_4(decoder_1_out_4), .out_5(decoder_1_out_5), .out_6(decoder_1_out_6),
    .out_7(decoder_1_out_7));
  LED plus_1 (.in(decoder_1_out_0));
  LED p0 (.in(decoder_1_out_1));
  LED p1 (.in(decoder_1_out_2));
  LED p2 (.in(decoder_1_out_3));
  LED uJMPs (.in(decoder_1_out_4));
  LED u_Reset (.in(decoder_1_out_5));
  LED N_A (.in(decoder_1_out_6));
  LED N_A_2 (.in(decoder_1_out_7));
  _7408 And (
    .pin1(lt_CAR_gt[0]), .pin2(lt_CAR_gt[1]), .pin3(And_pin3), .pin4(And_pin3), .pin5(lt_CAR_gt[2]),
    .pin6(And_pin6), .pin7(1'b0), .pin8(And_pin8), .pin9(lt_CAR_gt[4]), .pin10(And_pin10), .pin11(And_pin10),
    .pin12(lt_CAR_gt[3]), .pin13(And_pin6), .pin14(1'b1));
  _74153 BIT3 (
    .pin1(1'b0), .pin2(lt_CARNEXTSRC_gt[1]), .pin3(OPCODEADDR[3]), .pin4(MODEADDR[3]), .pin5(FROMuP0ADDR3),
    .pin6(FROMPLUSONE3), .pin7(BIT3_pin7), .pin8(1'b0), .pin9(BIT3_pin9), .pin10(FROMOFFSET3), .pin11(1'b0),
    .pin12(1'b0), .pin13(1'b0), .pin14(lt_CARNEXTSRC_gt[0]), .pin15(1'b0), .pin16(1'b1));
  _74153 BIT7 (
    .pin1(1'b0), .pin2(lt_CARNEXTSRC_gt[1]), .pin3(OPCODEADDR[7]), .pin4(MODEADDR[7]), .pin5(FROMuP0ADDR6),
    .pin6(FROMPLUSONE7), .pin7(BIT7_pin7), .pin8(1'b0), .pin9(BIT7_pin9), .pin10(FROMOFFSET7), .pin11(1'b0),
    .pin12(1'b0), .pin13(1'b0), .pin14(lt_CARNEXTSRC_gt[0]), .pin15(1'b0), .pin16(1'b1));
  _7408 And_2 (
    .pin1(And_pin8), .pin2(lt_CAR_gt[5]), .pin3(And_2_pin3), .pin4(And_2_pin3), .pin5(lt_CAR_gt[6]),
    .pin6(And_2_pin6), .pin7(1'b0), .pin9(1'b0), .pin10(1'b0), .pin11(CPU_ERR), .pin12(lt_CAR_gt[7]),
    .pin13(And_2_pin6), .pin14(1'b1));  // open: pin8
  _74153 BIT2 (
    .pin1(1'b0), .pin2(lt_CARNEXTSRC_gt[1]), .pin3(OPCODEADDR[2]), .pin4(MODEADDR[2]), .pin5(FROMuP0ADDR2),
    .pin6(FROMPLUSONE2), .pin7(BIT2_pin7), .pin8(1'b0), .pin9(BIT2_pin9), .pin10(FROMOFFSET2), .pin11(1'b0),
    .pin12(1'b0), .pin13(1'b0), .pin14(lt_CARNEXTSRC_gt[0]), .pin15(1'b0), .pin16(1'b1));
  _74153 BIT6 (
    .pin1(1'b0), .pin2(lt_CARNEXTSRC_gt[1]), .pin3(OPCODEADDR[6]), .pin4(MODEADDR[6]), .pin5(FROMuP0ADDR6),
    .pin6(FROMPLUSONE6), .pin7(BIT6_pin7), .pin8(1'b0), .pin9(BIT6_pin9), .pin10(FROMOFFSET6), .pin11(1'b0),
    .pin12(1'b0), .pin13(1'b0), .pin14(lt_CARNEXTSRC_gt[0]), .pin15(1'b0), .pin16(1'b1));
  ROM #(.AddrBits(8), .Bits(8)) uCode0 (.A(lt_CAR_gt), .sel(1'b1), .D(lt_UPARAM_gt));
  ROM #(.AddrBits(8), .Bits(8)) uCode1 (
    .A(lt_CAR_gt), .sel(1'b1),
    .D({MBR_LD_CDATA, MBR_OUT_XDATA, MBR_LD_XDATA, IR_LD_XDATA, MEM_OUT_XDATA, MEM_LD_XDATA, CDATA_TO_CADDR, CDATA_LD_0}));
  ROM #(.AddrBits(8), .Bits(8)) uCode2 (
    .A(lt_CAR_gt), .sel(1'b1),
    .D({A_LD_CDATA, PC_OUT_CADDR, PCL_OUT_CDATA, PC_LD_CDATA, PC_REL_CDATA, PC_INC, MAR_LD_CADDR, MBR_OUT_CDATA}));
  ROM #(.AddrBits(8), .Bits(8)) uCode3 (
    .A(lt_CAR_gt), .sel(1'b1),
    .D({ALUOP_0, ALUR_OUT_CDATA, ALUB_LD_CDATA, ALUA_LD_CDATA, PZ_LD, X_OUT_CDATA, X_LD_CDATA, A_OUT_CDATA}));
  ROM #(.AddrBits(8), .Bits(8)) uCode4 (
    .A(lt_CAR_gt), .sel(1'b1), .D({uZJMP, uP2, uP1, uP0, uJMPINV, uJMP, Z_SRC_CDATA, ALUOP_1}));
  _74157 Low_Nibble (
    .pin1(lt_CARNEXTSRC_gt[2]), .pin2(BIT3_pin7), .pin3(BIT3_pin9), .pin4(lt_CARNEXT_gt[3]),
    .pin5(BIT2_pin7), .pin6(BIT2_pin9), .pin7(lt_CARNEXT_gt[2]), .pin8(1'b0), .pin9(lt_CARNEXT_gt[1]),
    .pin10(Low_Nibble_pin10), .pin11(Low_Nibble_pin11), .pin12(lt_CARNEXT_gt[0]), .pin13(Low_Nibble_pin13),
    .pin14(Low_Nibble_pin14), .pin15(1'b0), .pin16(1'b1));
  _74157 High_Nibble (
    .pin1(lt_CARNEXTSRC_gt[2]), .pin2(BIT7_pin7), .pin3(BIT7_pin9), .pin4(lt_CARNEXT_gt[7]),
    .pin5(BIT6_pin7), .pin6(BIT6_pin9), .pin7(lt_CARNEXT_gt[6]), .pin8(1'b0), .pin9(lt_CARNEXT_gt[5]),
    .pin10(High_Nibble_pin10), .pin11(High_Nibble_pin11), .pin12(lt_CARNEXT_gt[4]),
    .pin13(High_Nibble_pin13), .pin14(High_Nibble_pin14), .pin15(1'b0), .pin16(1'b1));
  _74153 BIT1 (
    .pin1(1'b0), .pin2(lt_CARNEXTSRC_gt[1]), .pin3(OPCODEADDR[1]), .pin4(MODEADDR[1]), .pin5(FROMuP0ADDR1),
    .pin6(FROMPLUSONE1), .pin7(Low_Nibble_pin11), .pin8(1'b0), .pin9(Low_Nibble_pin10), .pin10(FROMOFFSET1),
    .pin11(1'b0), .pin12(1'b0), .pin13(1'b0), .pin14(lt_CARNEXTSRC_gt[0]), .pin15(1'b0), .pin16(1'b1));
  _74153 BIT5 (
    .pin1(1'b0), .pin2(lt_CARNEXTSRC_gt[1]), .pin3(OPCODEADDR[5]), .pin4(MODEADDR[5]), .pin5(FROMuP0ADDR5),
    .pin6(FROMPLUSONE5), .pin7(High_Nibble_pin11), .pin8(1'b0), .pin9(High_Nibble_pin10),
    .pin10(FROMOFFSET5), .pin11(1'b0), .pin12(1'b0), .pin13(1'b0), .pin14(lt_CARNEXTSRC_gt[0]), .pin15(1'b0),
    .pin16(1'b1));
  _74273 CAR (
    .pin1(1'b1), .pin2(lt_CAR_gt[0]), .pin3(lt_CARNEXT_gt[0]), .pin4(lt_CARNEXT_gt[1]), .pin5(lt_CAR_gt[1]),
    .pin6(lt_CAR_gt[2]), .pin7(lt_CARNEXT_gt[2]), .pin8(lt_CARNEXT_gt[3]), .pin9(lt_CAR_gt[3]), .pin10(1'b0),
    .pin11(CLOCK), .pin12(lt_CAR_gt[4]), .pin13(lt_CARNEXT_gt[4]), .pin14(lt_CARNEXT_gt[5]),
    .pin15(lt_CAR_gt[5]), .pin16(lt_CAR_gt[6]), .pin17(lt_CARNEXT_gt[6]), .pin18(lt_CARNEXT_gt[7]),
    .pin19(lt_CAR_gt[7]), .pin20(1'b1));
  _74283 CAR_plus_1_low_nibble (
    .pin1(FROMPLUSONE1), .pin2(1'b0), .pin3(lt_CAR_gt[1]), .pin4(FROMPLUSONE0), .pin5(lt_CAR_gt[0]),
    .pin6(1'b1), .pin7(1'b0), .pin8(1'b0), .pin9(CAR_plus_1_low_nibble_pin9), .pin10(FROMPLUSONE3),
    .pin11(1'b0), .pin12(lt_CAR_gt[3]), .pin13(FROMPLUSONE2), .pin14(lt_CAR_gt[2]), .pin15(1'b0), .pin16(1'b1));
  _7432 OR (
    .pin1(uP0), .pin2(uP2), .pin3(OR_pin3), .pin4(OR_pin3), .pin5(RESET), .pin6(lt_CARNEXTSRC_gt[0]),
    .pin7(1'b0), .pin9(1'b0), .pin10(1'b0), .pin11(lt_CARNEXTSRC_gt[1]), .pin12(uP1), .pin13(uP2),
    .pin14(1'b1));  // open: pin8
  _7432 OR_2 (
    .pin1(RESET), .pin2(uJMP), .pin3(OR_2_pin3), .pin4(OR_2_pin3), .pin5(OR_2_pin5),
    .pin6(lt_CARNEXTSRC_gt[2]), .pin7(1'b0), .pin9(1'b0), .pin10(1'b0), .pin11(OR_2_pin11), .pin12(uJMPINV),
    .pin13(Z), .pin14(1'b1));  // open: pin8
  _74153 BIT0 (
    .pin1(1'b0), .pin2(lt_CARNEXTSRC_gt[1]), .pin3(OPCODEADDR[0]), .pin4(MODEADDR[0]), .pin5(FROMuP0ADDR0),
    .pin6(FROMPLUSONE0), .pin7(Low_Nibble_pin14), .pin8(1'b0), .pin9(Low_Nibble_pin13), .pin10(FROMOFFSET0),
    .pin11(1'b0), .pin12(1'b0), .pin13(1'b0), .pin14(lt_CARNEXTSRC_gt[0]), .pin15(1'b0), .pin16(1'b1));
  _74153 BIT4 (
    .pin1(1'b0), .pin2(lt_CARNEXTSRC_gt[1]), .pin3(OPCODEADDR[4]), .pin4(MODEADDR[4]), .pin5(FROMuP0ADDR4),
    .pin6(FROMPLUSONE4), .pin7(High_Nibble_pin14), .pin8(1'b0), .pin9(High_Nibble_pin13),
    .pin10(FROMOFFSET4), .pin11(1'b0), .pin12(1'b0), .pin13(1'b0), .pin14(lt_CARNEXTSRC_gt[0]), .pin15(1'b0),
    .pin16(1'b1));
  _74283 CAR_plus_1_high_nibble (
    .pin1(FROMPLUSONE5), .pin2(1'b0), .pin3(lt_CAR_gt[5]), .pin4(FROMPLUSONE4), .pin5(lt_CAR_gt[4]),
    .pin6(1'b0), .pin7(CAR_plus_1_low_nibble_pin9), .pin8(1'b0), .pin10(FROMPLUSONE7), .pin11(1'b0),
    .pin12(lt_CAR_gt[7]), .pin13(FROMPLUSONE6), .pin14(lt_CAR_gt[6]), .pin15(1'b0), .pin16(1'b1));  // open: pin9
  _7408 And_3 (
    .pin1(uZJMP), .pin2(And_3_pin2), .pin3(OR_2_pin5), .pin4(OR_2_pin11), .pin5(And_3_pin5),
    .pin6(And_3_pin2), .pin7(1'b0), .pin9(1'b0), .pin10(1'b0), .pin11(And_3_pin11), .pin12(uJMPINV),
    .pin13(Z), .pin14(1'b1));  // open: pin8
  DipSwitch uP0ADDR7 (.out(FROMuP0ADDR6));
  DipSwitch uP0ADDR6 (.out(FROMuP0ADDR6));
  DipSwitch uP0ADDR5 (.out(FROMuP0ADDR5));
  DipSwitch uP0ADDR4 (.out(FROMuP0ADDR4));
  DipSwitch uP0ADDR3 (.out(FROMuP0ADDR3));
  DipSwitch uP0ADDR2 (.out(FROMuP0ADDR2));
  DipSwitch #(.dipDefault("true")) uP0ADDR1 (.out(FROMuP0ADDR1));
  DipSwitch uP0ADDR0 (.out(FROMuP0ADDR0));
  _7404 Not (
    .pin1(And_3_pin11), .pin2(And_3_pin5), .pin3(1'b0), .pin5(1'b0), .pin7(1'b0), .pin9(1'b0), .pin11(1'b0),
    .pin13(1'b0), .pin14(1'b1));  // open: pin4, pin6, pin8, pin10, pin12
  _74283 CAR_plus_offset_low_nibble (
    .pin1(FROMOFFSET1), .pin2(lt_UPARAM_gt[1]), .pin3(lt_CAR_gt[1]), .pin4(FROMOFFSET0), .pin5(lt_CAR_gt[0]),
    .pin6(lt_UPARAM_gt[0]), .pin7(1'b0), .pin8(1'b0), .pin9(CAR_plus_offset_low_nibble_pin9),
    .pin10(FROMOFFSET3), .pin11(lt_UPARAM_gt[3]), .pin12(lt_CAR_gt[3]), .pin13(FROMOFFSET2),
    .pin14(lt_CAR_gt[2]), .pin15(lt_UPARAM_gt[2]), .pin16(1'b1));
  _74283 CAR_plus_offset_high_nibble (
    .pin1(FROMOFFSET5), .pin2(lt_UPARAM_gt[3]), .pin3(lt_CAR_gt[5]), .pin4(FROMOFFSET4), .pin5(lt_CAR_gt[4]),
    .pin6(lt_UPARAM_gt[3]), .pin7(CAR_plus_offset_low_nibble_pin9), .pin8(1'b0), .pin10(FROMOFFSET7),
    .pin11(lt_UPARAM_gt[3]), .pin12(lt_CAR_gt[7]), .pin13(FROMOFFSET6), .pin14(lt_CAR_gt[6]),
    .pin15(lt_UPARAM_gt[3]), .pin16(1'b1));  // open: pin9

  // Other names for the same wires on the sheet: PC_OUT_CDATA = PCL_OUT_CDATA; CARNEXTSRC[2:0] = lt_CARNEXTSRC_gt;
  //   FROMCARNEXTSRC2 = lt_CARNEXTSRC_gt[2]; FROMCARNEXTSRC0 = lt_CARNEXTSRC_gt[0];
  //   FROMCARNEXTSRC1 = lt_CARNEXTSRC_gt[1]; CDATA_TO_CADDRL = CDATA_TO_CADDR; FROMMODEADDR0 = MODEADDR[0];
  //   FROMMODEADDR1 = MODEADDR[1]; FROMMODEADDR2 = MODEADDR[2]; FROMMODEADDR3 = MODEADDR[3];
  //   FROMMODEADDR4 = MODEADDR[4]; FROMMODEADDR5 = MODEADDR[5]; FROMMODEADDR6 = MODEADDR[6];
  //   FROMMODEADDR7 = MODEADDR[7]; FROMOPCODEADDR0 = OPCODEADDR[0]; FROMOPCODEADDR1 = OPCODEADDR[1];
  //   FROMOPCODEADDR2 = OPCODEADDR[2]; FROMOPCODEADDR3 = OPCODEADDR[3]; FROMOPCODEADDR4 = OPCODEADDR[4];
  //   FROMOPCODEADDR5 = OPCODEADDR[5]; FROMOPCODEADDR6 = OPCODEADDR[6]; FROMOPCODEADDR7 = OPCODEADDR[7];
  //   CAR[7:0] = lt_CAR_gt; FROMCAR0 = lt_CAR_gt[0]; TOCAR0 = lt_CAR_gt[0]; FROMCAR1 = lt_CAR_gt[1];
  //   TOCAR1 = lt_CAR_gt[1]; FROMCAR2 = lt_CAR_gt[2]; TOCAR2 = lt_CAR_gt[2]; FROMCAR3 = lt_CAR_gt[3];
  //   TOCAR3 = lt_CAR_gt[3]; FROMCAR4 = lt_CAR_gt[4]; TOCAR4 = lt_CAR_gt[4]; FROMCAR5 = lt_CAR_gt[5];
  //   TOCAR5 = lt_CAR_gt[5]; FROMCAR6 = lt_CAR_gt[6]; TOCAR6 = lt_CAR_gt[6]; FROMCAR7 = lt_CAR_gt[7];
  //   TOCAR7 = lt_CAR_gt[7]; CARNEXT[7:0] = lt_CARNEXT_gt; FROMCARNEXT0 = lt_CARNEXT_gt[0];
  //   TOCARNEXT0 = lt_CARNEXT_gt[0]; FROMCARNEXT1 = lt_CARNEXT_gt[1]; TOCARNEXT1 = lt_CARNEXT_gt[1];
  //   FROMCARNEXT2 = lt_CARNEXT_gt[2]; TOCARNEXT2 = lt_CARNEXT_gt[2]; FROMCARNEXT3 = lt_CARNEXT_gt[3];
  //   TOCARNEXT3 = lt_CARNEXT_gt[3]; FROMCARNEXT4 = lt_CARNEXT_gt[4]; TOCARNEXT4 = lt_CARNEXT_gt[4];
  //   FROMCARNEXT5 = lt_CARNEXT_gt[5]; TOCARNEXT5 = lt_CARNEXT_gt[5]; FROMCARNEXT6 = lt_CARNEXT_gt[6];
  //   TOCARNEXT6 = lt_CARNEXT_gt[6]; FROMCARNEXT7 = lt_CARNEXT_gt[7]; TOCARNEXT7 = lt_CARNEXT_gt[7];
  //   OFFSET[7:0] = {FROMOFFSET7, FROMOFFSET6, FROMOFFSET5, FROMOFFSET4, FROMOFFSET3, FROMOFFSET2, FROMOFFSET1, FROMOFFSET0};
  //   TOOFFSET0 = FROMOFFSET0; TOOFFSET1 = FROMOFFSET1; TOOFFSET2 = FROMOFFSET2; TOOFFSET3 = FROMOFFSET3;
  //   TOOFFSET4 = FROMOFFSET4; TOOFFSET5 = FROMOFFSET5; TOOFFSET6 = FROMOFFSET6; TOOFFSET7 = FROMOFFSET7;
  //   PLUSONE[7:0] = {FROMPLUSONE7, FROMPLUSONE6, FROMPLUSONE5, FROMPLUSONE4, FROMPLUSONE3, FROMPLUSONE2, FROMPLUSONE1, FROMPLUSONE0};
  //   TOPLUSONE0 = FROMPLUSONE0; TOPLUSONE1 = FROMPLUSONE1; TOPLUSONE2 = FROMPLUSONE2; TOPLUSONE3 = FROMPLUSONE3;
  //   TOPLUSONE4 = FROMPLUSONE4; TOPLUSONE5 = FROMPLUSONE5; TOPLUSONE6 = FROMPLUSONE6; TOPLUSONE7 = FROMPLUSONE7;
  //   FROMUPARAM0 = lt_UPARAM_gt[0]; UPARAM[7:0] = lt_UPARAM_gt; FROMUPARAM1 = lt_UPARAM_gt[1];
  //   FROMUPARAM2 = lt_UPARAM_gt[2]; FROMUPARAM3 = lt_UPARAM_gt[3]; FROMUPARAM4 = lt_UPARAM_gt[4];
  //   FROMUPARAM5 = lt_UPARAM_gt[5]; FROMUPARAM6 = lt_UPARAM_gt[6]; FROMUPARAM7 = lt_UPARAM_gt[7]

  // Notes on the sheet:
  //   MODEADDR: default 169
  //   OPCODEADDR: default 169
  //   This alternate version makes all
  //   uJmps releative.   
  //   Advantages:
  //   * Smaller ROM footprint
  //   * Works without extension for any ROM size
  //   Disadvantages
  //   * Jumps can only +7/-8 bytes
  //   * Can't hold absolute main memory addresses
  //   * Extra circuitry
  //   CAR
  //   CARNEXT
  //   UPARAM
  //   CARNEXTSRC
  //   Debug
  //   Error
  //   uCode ROMS
  //   "Next CAR" Multiplexer
  //   uCode - each address holds the
  //   settings for control lines + 
  //   a parameter which is the target 
  //   for jump uCode instructions.
  //   Unused uCODE ROM locations
  //   are set to FF - so running into an 
  //   FF implies an error.
  //   contents of uCode0 (hex, n*v repeats v):
  //   6000000,18000000,6000000,30000000,c0000000
  //   contents of uCode1 (hex, n*v repeats v):
  //   6000000,18000000,6000000,30000000,c0000000
  //   contents of uCode2 (hex, n*v repeats v):
  //   6000000,18000000,6000000,30000000,c0000000
  //   contents of uCode3 (hex, n*v repeats v):
  //   6000000,18000000,6000000,30000000,c0000000
  //   contents of uCode4 (hex, n*v repeats v):
  //   6000000,18000000,6000000,30000000,c0000000
  //   uCode Address Register
  //   CAR + 1
  //   Current CAR + 1 to move to
  //   the next uCode instruction.
  //   Sequencing Logic
  //   The address of the current
  //   uCode instruction in the 
  //   uCode ROMs.
  //   P0 uCode Address
  //   Applies the ouput of the 
  //   sequencing logic to select
  //   the next var of the CAR.
  //   CAR + Offset
  //   Current CAR + offset  for branches in uCode
  //   Bit 3 of the uCode param is the sign and so copied 
  //   into all higher bits
  //   The address of the P0 uCode.
  //   At the cost of an extra control line
  //   and register this could be 
  //   done automatically via init uCode.
  //   Calculates the selector for the 
  //   "Next CAR" multiplexer to
  //   choose between the possible 
  //   options for the address of the 
  //   next uCode instruction,
  //   2 1 0 Meaning
  //   ------------------
  //   0 0 0 +1
  //   0 0 1 p0
  //   0 1 0 p1
  //   0 1 1 p2
  //   1 0 0 uJMPs
  //   1 x 1 Reset
  //   1 1 0 N/A
endmodule
