// Digital circuit Instruction-Decoder-rom-scanning.dig as structural Verilog
module Instruction_Decoder_rom_scanning (
  input  [7:0] OPCODE,
  input  clk,
  output [7:0] MODEADDR,
  output [7:0] OPCODEADDR
);

  wire _74162_1_pin1, A, B, C, D, D0, D1, D2, D3, D4, D5, D6, D7, nand_2_out, nand_3_out, not_1_out,
       not_2_out, not_3_out, not_4_out, P0_0, P0_1, P0_2, P0_3, P0_4, P0_5, P0_6, P0_7, P1_0, P1_1, P1_2,
       P1_3, P1_4, P1_5, P1_6, P1_7, u0, u1;

  Seven_Seg_Hex seven_seg_hex_1 (.d({D, C, B, A}), .dp(1'b0));
  Seven_Seg_Hex seven_seg_hex_2 (.d({P1_7, P1_6, P1_5, P1_4}), .dp(1'b0));
  Seven_Seg_Hex seven_seg_hex_3 (.d({P1_3, P1_2, P1_1, P1_0}), .dp(1'b0));
  Seven_Seg_Hex seven_seg_hex_4 (.d({P0_7, P0_6, P0_5, P0_4}), .dp(1'b0));
  Seven_Seg_Hex seven_seg_hex_5 (.d({2'b00, u1, u0}), .dp(1'b0));
  Seven_Seg_Hex seven_seg_hex_6 (.d({P0_3, P0_2, P0_1, P0_0}), .dp(1'b0));
  _74162 _74162_1 (
    .pin1(_74162_1_pin1), .pin2(clk), .pin3(1'b0), .pin4(1'b0), .pin5(1'b0), .pin6(1'b0), .pin7(1'b1),
    .pin8(1'b0), .pin9(1'b1), .pin10(1'b1), .pin11(D), .pin12(C), .pin13(B), .pin14(A), .pin16(1'b1));  // open: pin15
  nand nand_1 (_74162_1_pin1, not_1_out, A);
  not not_1 (not_1_out, B);
  not not_2 (not_2_out, A);
  not not_3 (not_3_out, B);
  not not_4 (not_4_out, B);
  nand nand_2 (nand_2_out, not_2_out, not_3_out);
  nand nand_3 (nand_3_out, A, not_4_out);
  _74377 Page_0 (
    .pin1(nand_2_out), .pin2(OPCODEADDR[0]), .pin3(OPCODE[0]), .pin4(OPCODE[1]), .pin5(OPCODEADDR[1]),
    .pin6(OPCODEADDR[2]), .pin7(OPCODE[2]), .pin8(OPCODE[3]), .pin9(OPCODEADDR[3]), .pin10(1'b0),
    .pin11(clk), .pin12(OPCODEADDR[4]), .pin13(OPCODE[4]), .pin14(OPCODE[5]), .pin15(OPCODEADDR[5]),
    .pin16(OPCODEADDR[6]), .pin17(OPCODE[6]), .pin18(OPCODE[7]), .pin19(OPCODEADDR[7]), .pin20(1'b1));
  _74377 Page_1 (
    .pin1(nand_3_out), .pin2(P1_0), .pin3(OPCODE[0]), .pin4(OPCODE[1]), .pin5(P1_1), .pin6(P1_2),
    .pin7(OPCODE[2]), .pin8(OPCODE[3]), .pin9(P1_3), .pin10(1'b0), .pin11(clk), .pin12(P1_4),
    .pin13(OPCODE[4]), .pin14(OPCODE[5]), .pin15(P1_5), .pin16(P1_6), .pin17(OPCODE[6]), .pin18(OPCODE[7]),
    .pin19(P1_7), .pin20(1'b1));
  ROM #(.AddrBits(9), .Bits(8)) Decoder (.A({A, OPCODE}), .sel(1'b1), .D({D7, D6, D5, D4, D3, D2, D1, D0}));

  assign MODEADDR = OPCODE;

  // Other names for the same wires on the sheet: CLCK = clk; OA0 = OPCODEADDR[0]; OA1 = OPCODEADDR[1];
  //   OA2 = OPCODEADDR[2]; OA3 = OPCODEADDR[3]; OA4 = OPCODEADDR[4]; OA5 = OPCODEADDR[5]; OA6 = OPCODEADDR[6];
  //   OA7 = OPCODEADDR[7]; OP0 = OPCODE[0]; OP1 = OPCODE[1]; OP2 = OPCODE[2]; OP3 = OPCODE[3]; OP4 = OPCODE[4];
  //   OP5 = OPCODE[5]; OP6 = OPCODE[6]; OP7 = OPCODE[7]

  // Notes on the sheet:
  //   contents of Decoder (hex, n*v repeats v):
  //   1,2,3,4,252*0,11,12,13,14
endmodule
