// Digital circuit alt-decoder.dig as structural Verilog
module alt_decoder (
  input  clk
);

  wire _74162_1_pin1, A, and_1_out, B, C, D, D0, D1, D2, D3, D4, D5, D6, D7, nand_2_out, nand_3_out,
       nand_4_out, nand_5_out, nand_6_out, not_1_out, not_2_out, not_3_out, not_4_out, not_5_out, not_6_out,
       not_7_out, not_8_out, not_9_out, not_10_out, not_11_out, not_12_out, P0_0, P0_1, P0_2, P0_3, P0_4,
       P0_5, P0_6, P0_7, P1_0, P1_1, P1_2, P1_3, P1_4, P1_5, P1_6, P1_7, P2_0, P2_1, P2_2, P2_3, P2_4, P2_5,
       P2_6, P2_7, P3_0, P3_1, P3_2, P3_3, P3_4, P3_5, P3_6, P3_7, P4_0, P4_1, P4_2, P4_3, P4_4, P4_5, P4_6,
       P4_7, u0, u1;

  Seven_Seg_Hex seven_seg_hex_1 (.d({D, C, B, A}), .dp(1'b0));
  Seven_Seg_Hex seven_seg_hex_2 (.d({P1_7, P1_6, P1_5, P1_4}), .dp(1'b0));
  Seven_Seg_Hex seven_seg_hex_3 (.d({P1_3, P1_2, P1_1, P1_0}), .dp(1'b0));
  Seven_Seg_Hex seven_seg_hex_4 (.d({P0_7, P0_6, P0_5, P0_4}), .dp(1'b0));
  Seven_Seg_Hex seven_seg_hex_5 (.d({2'b00, u1, u0}), .dp(1'b0));
  Seven_Seg_Hex seven_seg_hex_6 (.d({P0_3, P0_2, P0_1, P0_0}), .dp(1'b0));
  _74162 _74162_1 (
    .pin1(_74162_1_pin1), .pin2(clk), .pin3(1'b0), .pin4(1'b0), .pin5(1'b0), .pin6(1'b0), .pin7(1'b1),
    .pin8(1'b0), .pin9(1'b1), .pin10(1'b1), .pin11(D), .pin12(C), .pin13(B), .pin14(A), .pin16(1'b1));  // open: pin15
  not not_1 (not_1_out, B);
  nand nand_1 (_74162_1_pin1, C, not_1_out, A);
  not not_2 (not_2_out, A);
  not not_3 (not_3_out, B);
  not not_4 (not_4_out, C);
  not not_5 (not_5_out, B);
  not not_6 (not_6_out, C);
  not not_7 (not_7_out, A);
  not not_8 (not_8_out, C);
  not not_9 (not_9_out, C);
  not not_10 (not_10_out, A);
  not not_11 (not_11_out, B);
  nand nand_2 (nand_2_out, not_2_out, not_3_out, not_4_out);
  nand nand_3 (nand_3_out, A, not_5_out, not_6_out);
  nand nand_4 (nand_4_out, not_7_out, B, not_8_out);
  nand nand_5 (nand_5_out, A, B, not_9_out);
  nand nand_6 (nand_6_out, not_10_out, not_11_out, C);
  _74377 Page_0 (
    .pin1(nand_2_out), .pin2(P0_0), .pin3(D0), .pin4(D1), .pin5(P0_1), .pin6(P0_2), .pin7(D2), .pin8(D3),
    .pin9(P0_3), .pin10(1'b0), .pin11(clk), .pin12(P0_4), .pin13(D4), .pin14(D5), .pin15(P0_5), .pin16(P0_6),
    .pin17(D6), .pin18(D7), .pin19(P0_7), .pin20(1'b1));
  _74377 Page_1 (
    .pin1(nand_3_out), .pin2(P1_0), .pin3(D0), .pin4(D1), .pin5(P1_1), .pin6(P1_2), .pin7(D2), .pin8(D3),
    .pin9(P1_3), .pin10(1'b0), .pin11(clk), .pin12(P1_4), .pin13(D4), .pin14(D5), .pin15(P1_5), .pin16(P1_6),
    .pin17(D6), .pin18(D7), .pin19(P1_7), .pin20(1'b1));
  _74377 Page_2 (
    .pin1(nand_4_out), .pin2(P2_0), .pin3(D0), .pin4(D1), .pin5(P2_1), .pin6(P2_2), .pin7(D2), .pin8(D3),
    .pin9(P2_3), .pin10(1'b0), .pin11(clk), .pin12(P2_4), .pin13(D4), .pin14(D5), .pin15(P2_5), .pin16(P2_6),
    .pin17(D6), .pin18(D7), .pin19(P2_7), .pin20(1'b1));
  _74377 Page_3 (
    .pin1(nand_5_out), .pin2(P3_0), .pin3(D0), .pin4(D1), .pin5(P3_1), .pin6(P3_2), .pin7(D2), .pin8(D3),
    .pin9(P3_3), .pin10(1'b0), .pin11(clk), .pin12(P3_4), .pin13(D4), .pin14(D5), .pin15(P3_5), .pin16(P3_6),
    .pin17(D6), .pin18(D7), .pin19(P3_7), .pin20(1'b1));
  _74377 Page_4 (
    .pin1(nand_6_out), .pin2(P4_0), .pin3(D0), .pin4(D1), .pin5(P4_1), .pin6(P4_2), .pin7(D2), .pin8(D3),
    .pin9(P4_3), .pin10(1'b0), .pin11(clk), .pin12(P4_4), .pin13(D4), .pin14(D5), .pin15(P4_5), .pin16(P4_6),
    .pin17(D6), .pin18(D7), .pin19(P4_7), .pin20(1'b1));
  not not_12 (not_12_out, B);
  and and_1 (and_1_out, A, not_12_out, C);
  ROM #(.AddrBits(11), .Bits(8)) uCode (
    .A({C, B, A, {6{1'b0}}, u1, u0}), .sel(1'b1), .D({D7, D6, D5, D4, D3, D2, D1, D0}));
  _74161 uCodeAddr (
    .pin1(1'b1), .pin2(clk), .pin3(1'b0), .pin4(1'b0), .pin5(1'b0), .pin6(1'b0), .pin7(and_1_out),
    .pin8(1'b0), .pin9(1'b1), .pin10(1'b1), .pin13(u1), .pin14(u0), .pin16(1'b1));  // open: pin11, pin12, pin15

  // Other names for the same wires on the sheet: CLCK = clk

  // Notes on the sheet:
  //   contents of uCode (hex, n*v repeats v):
  //   1,2,3,4,252*0,11,12,13,14
endmodule
