// Digital circuit ALU.dig as structural Verilog
module ALU (
  input  [7:0] D,
  input  [1:0] OP,
  input  LDA,
  input  LDB,
  input  CLOCK,
  output [7:0] Q,
  output ZOUT,
  output [7:0] lt_ALUA_gt,
  output [7:0] lt_ALUB_gt
);

  wire and_1_out, not_1_out;
  wire [7:0] multiplexer_1_out, not_2_out;

  Seven_Seg_Hex seven_seg_hex_1 (.d(lt_ALUA_gt[7:4]), .dp(1'b0));
  Seven_Seg_Hex seven_seg_hex_2 (.d(lt_ALUA_gt[3:0]), .dp(1'b0));
  Seven_Seg_Hex seven_seg_hex_3 (.d(lt_ALUB_gt[7:4]), .dp(1'b0));
  Seven_Seg_Hex seven_seg_hex_4 (.d(lt_ALUB_gt[3:0]), .dp(1'b0));
  Seven_Seg_Hex seven_seg_hex_5 (.d(Q[3:0]), .dp(1'b0));
  Seven_Seg_Hex seven_seg_hex_6 (.d(Q[7:4]), .dp(1'b0));
  LED led_1 (.in(ZOUT));
  Register #(.Bits(8)) register_1 (.D(D), .C(CLOCK), .en(LDA), .Q(lt_ALUA_gt));
  Register #(.Bits(8)) register_2 (.D(D), .C(CLOCK), .en(LDB), .Q(lt_ALUB_gt));
  not not_1 (not_1_out, OP[1]);
  nor nor_1 (ZOUT, Q[0], Q[1], Q[2], Q[3], Q[4], Q[5], Q[6], Q[7]);
  assign not_2_out = ~lt_ALUB_gt;  // Not not_2, 8 bits wide
  and and_1 (and_1_out, OP[0], not_1_out);
  Multiplexer #(.Selector_Bits(2), .Bits(8)) multiplexer_1 (
    .sel(OP), .in_0(lt_ALUB_gt), .in_1(not_2_out), .in_2(8'h1), .in_3({8{1'b1}}), .out(multiplexer_1_out));
  Add #(.Bits(8)) add_1 (.a(lt_ALUA_gt), .b(multiplexer_1_out), .c_i(and_1_out), .s(Q));  // open: c_o

  // Other names for the same wires on the sheet: A[7:0] = lt_ALUA_gt; B[7:0] = lt_ALUB_gt

  // Notes on the sheet:
  //   D: default 80
  //   A
  //   B
  //   Out
  //   Operations
  //   0 0 ADD
  //   0 1 SUB
  //   1 0 INC
  //   1 1 DEC
  //   ZOUT
  //   Arithmetic/Logical Operations
endmodule
