// Digital circuit Address Decoder.dig as structural Verilog
module Address_Decoder (
  input  [7:0] A,
  input  CS,
  output CS0,
  output CS1,
  output CS2
);

  wire and_1_out, and_2_out, nor_1_out, not_1_out;

  not not_1 (not_1_out, A[4]);
  and and_1 (and_1_out, A[7], A[6], A[5], A[4]);
  and and_2 (and_2_out, not_1_out, A[5], A[6], A[7]);
  nor nor_1 (nor_1_out, and_1_out, and_2_out);
  and and_3 (CS2, and_1_out, CS);
  and and_4 (CS1, and_2_out, CS);
  and and_5 (CS0, CS, nor_1_out);

  // Notes on the sheet:
  //   Banks
  //   0xF0...0xFF - I/O
  //   0xE0...0xEF - RAM
  //   0x00...0xDF - ROM
endmodule

/* Test case:
CS A    CS0 CS1 CS2 
1  0xFF 0   0   1   
1  0xE1 0   1   0
1  0xCF 1   0   0  
*/
