// Digital circuit CPU.dig as structural Verilog
module CPU (
  input  RUN,
  input  [7:0] MCBREAKPOINT,
  input  [7:0] UCBREAKPOINT,
  input  FAST,
  input  SLOW,
  input  MCBSET,
  input  UCBSET
);

  wire A_LD_CDATA, A_OUT_CDATA, ALUA_LD_CDATA, ALUB_LD_CDATA, ALUOP_0, ALUOP_1, ALUR_OUT_CDATA, ALUZ_OUT,
       and_1_out, and_2_out, and_3_out, and_4_out, and_5_out, and_6_out, and_7_out, and_8_out, and_9_out,
       BREAK, CDATA_LD_0, CDATA_TO_CADDR, CLOCK, clock_1_cout, comparator_1_gt, comparator_2_eq,
       comparator_3_eq, comparator_4_eq, comparator_5_eq, CPU_ERR, CS0, CS1, CS2, decoder_1_out_0,
       decoder_1_out_1, decoder_1_out_2, decoder_1_out_3, decoder_2_out_0, decoder_2_out_1, decoder_2_out_2,
       decoder_2_out_3, decoder_2_out_4, decoder_2_out_5, decoder_2_out_6, decoder_2_out_7, ERROR, HALTED,
       IR_LD_XDATA, MAR_LD_CADDR, MBR_LD_CDATA, MBR_LD_XDATA, MBR_OUT_CDATA, MBR_OUT_XDATA, MEM_LD_XDATA,
       MEM_OUT_XDATA, multiplexer_1_out, nor_1_out, or_1_out, or_5_out, or_6_out, PC_INC, PC_LD_CDATA,
       PC_OUT_CADDR, PC_OUT_CDATA, PC_REL_CDATA, PZ_LD, RESET, STEP_out, switchdt_1_p3, X_LD_CDATA,
       X_OUT_CDATA, Z, Z_SRC_CDATA;
  wire [2:0] lt_CARNEXTSRC_gt;
  wire [3:0] register_1_q, register_1_q_2, register_2_q, register_2_q_2;
  wire [7:0] A, ALUR, CADDR, CDATA, IR, lt_ALUA_gt, lt_ALUB_gt, lt_CAR_gt, lt_CARNEXT_gt, lt_UPARAM_gt, MAR,
       MBR, MODEADDR, multiplexer_2_out, OPCODEADDR, PC, X, XDATA;

  Button STEP (.out(STEP_out));
  Button u_RESET (.out(RESET));
  Seven_Seg_Hex seven_seg_hex_1 (.d(MAR[3:0]), .dp(1'b0));
  Seven_Seg_Hex seven_seg_hex_2 (.d(MAR[7:4]), .dp(1'b0));
  Seven_Seg_Hex seven_seg_hex_3 (.d(A[3:0]), .dp(1'b0));
  Seven_Seg_Hex seven_seg_hex_4 (.d(A[7:4]), .dp(1'b0));
  and and_1 (and_1_out, CS0, MEM_LD_XDATA);
  Comparator #(.Bits(8)) comparator_1 (.a(MAR), .b(8'hf2), .gt(comparator_1_gt));  // open: eq, lt
  or or_1 (or_1_out, ERROR, BREAK);
  // SwitchDT switchdt_1: pin names not known; wires that end beside it: FAST, SLOW, switchdt_1_p3
  Seven_Seg_Hex seven_seg_hex_5 (.d(MBR[7:4]), .dp(1'b0));
  Seven_Seg_Hex seven_seg_hex_6 (.d(X[7:4]), .dp(1'b0));
  Comparator #(.Bits(8)) comparator_2 (.a(MCBREAKPOINT), .b(PC), .eq(comparator_2_eq));  // open: gt, lt
  Comparator #(.Bits(8)) comparator_3 (.a(UCBREAKPOINT), .b(lt_CAR_gt), .eq(comparator_3_eq));  // open: gt, lt
  and and_2 (and_2_out, CS2, comparator_1_gt);
  Seven_Seg_Hex seven_seg_hex_7 (.d(MBR[3:0]), .dp(1'b0));
  Seven_Seg_Hex seven_seg_hex_8 (.d(X[3:0]), .dp(1'b0));
  and and_3 (and_3_out, MCBSET, comparator_2_eq);
  and and_4 (and_4_out, UCBSET, comparator_3_eq);
  or or_2 (ERROR, CPU_ERR, and_1_out, and_2_out);
  Clock clock_1 (
    .RUN(RUN), .STEP(STEP_out), .HALT(or_1_out), .Cin(switchdt_1_p3), .HALTED(HALTED), .Cout(clock_1_cout));
  Seven_Seg_Hex seven_seg_hex_9 (.d(PC[3:0]), .dp(1'b0));
  Seven_Seg_Hex seven_seg_hex_10 (.d(PC[7:4]), .dp(1'b0));
  and and_5 (and_5_out, HALTED, RESET);
  Seven_Seg_Hex seven_seg_hex_11 (.d(IR[7:4]), .dp(1'b0));
  LED led_1 (.in(Z));
  or or_3 (BREAK, and_3_out, and_4_out);
  or or_4 (CLOCK, clock_1_cout, and_5_out);
  Seven_Seg_Hex seven_seg_hex_12 (.d(IR[3:0]), .dp(1'b0));
  nor nor_1 (nor_1_out, CDATA[0], CDATA[1], CDATA[2], CDATA[3], CDATA[4], CDATA[5], CDATA[6], CDATA[7]);
  Multiplexer multiplexer_1 (.sel(Z_SRC_CDATA), .in_0(ALUZ_OUT), .in_1(nor_1_out), .out(multiplexer_1_out));
  Instruction_Decoder Instruction_Decoder (.OPCODE(IR), .MODEADDR(MODEADDR), .OPCODEADDR(OPCODEADDR));
  Register u_Z (.D(multiplexer_1_out), .C(CLOCK), .en(PZ_LD), .Q(Z));
  Seven_Seg_Hex seven_seg_hex_13 (.d(lt_ALUA_gt[7:4]), .dp(1'b0));
  Seven_Seg_Hex seven_seg_hex_14 (.d(MODEADDR[7:4]), .dp(1'b0));
  Seven_Seg_Hex seven_seg_hex_15 (.d(lt_ALUA_gt[3:0]), .dp(1'b0));
  or or_5 (or_5_out, MEM_LD_XDATA, MEM_OUT_XDATA);
  Seven_Seg_Hex seven_seg_hex_16 (.d(MODEADDR[3:0]), .dp(1'b0));
  Seven_Seg_Hex seven_seg_hex_17 (.d(lt_ALUB_gt[3:0]), .dp(1'b0));
  Seven_Seg_Hex seven_seg_hex_18 (.d(lt_ALUB_gt[7:4]), .dp(1'b0));
  io io_1 (.ADDR(MAR), .IN(XDATA), .WR(MEM_LD_XDATA), .CLK(CLOCK));
  Address_Decoder address_decoder_1 (.A(MAR), .CS(or_5_out), .CS0(CS0), .CS1(CS1), .CS2(CS2));
  Seven_Seg_Hex seven_seg_hex_19 (.d(ALUR[3:0]), .dp(1'b0));
  Seven_Seg_Hex seven_seg_hex_20 (.d(ALUR[7:4]), .dp(1'b0));
  Register #(.Bits(8)) u_MAR (.D(CADDR), .C(CLOCK), .en(MAR_LD_CADDR), .Q(MAR));
  Control_Unit Control_Unit (
    .MODEADDR(MODEADDR), .OPCODEADDR(OPCODEADDR), .Z(Z), .RESET(RESET), .CLOCK(CLOCK),
    .CDATA_LD_0(CDATA_LD_0), .CDATA_TO_CADDR(CDATA_TO_CADDR), .MEM_LD_XDATA(MEM_LD_XDATA),
    .MEM_OUT_XDATA(MEM_OUT_XDATA), .IR_LD_XDATA(IR_LD_XDATA), .MBR_LD_XDATA(MBR_LD_XDATA),
    .MBR_OUT_XDATA(MBR_OUT_XDATA), .MBR_LD_CDATA(MBR_LD_CDATA), .MBR_OUT_CDATA(MBR_OUT_CDATA),
    .MAR_LD_CADDR(MAR_LD_CADDR), .PC_INC(PC_INC), .PC_REL_CDATA(PC_REL_CDATA), .PC_LD_CDATA(PC_LD_CDATA),
    .PCL_OUT_CDATA(PC_OUT_CDATA), .PC_OUT_CADDR(PC_OUT_CADDR), .A_LD_CDATA(A_LD_CDATA),
    .A_OUT_CDATA(A_OUT_CDATA), .X_LD_CDATA(X_LD_CDATA), .X_OUT_CDATA(X_OUT_CDATA), .PZ_LD(PZ_LD),
    .ALUA_LD_CDATA(ALUA_LD_CDATA), .ALUB_LD_CDATA(ALUB_LD_CDATA), .ALUR_OUT_CDATA(ALUR_OUT_CDATA),
    .ALUOP_0(ALUOP_0), .ALUOP_1(ALUOP_1), .Z_SRC_CDATA(Z_SRC_CDATA), .CPU_ERR(CPU_ERR),
    .lt_CAR_gt(lt_CAR_gt), .lt_UPARAM_gt(lt_UPARAM_gt), .lt_CARNEXT_gt(lt_CARNEXT_gt),
    .lt_CARNEXTSRC_gt(lt_CARNEXTSRC_gt));
  Seven_Seg_Hex seven_seg_hex_21 (.d(OPCODEADDR[3:0]), .dp(1'b0));
  Seven_Seg_Hex seven_seg_hex_22 (.d(OPCODEADDR[7:4]), .dp(1'b0));
  LED led_2 (.in(ALUZ_OUT));
  assign CADDR = CDATA_TO_CADDR ? CDATA : 8'bz;  // Driver driver_1
  Decoder #(.Selector_Bits(2)) decoder_1 (
    .sel({ALUOP_1, ALUOP_0}), .out_0(decoder_1_out_0), .out_1(decoder_1_out_1), .out_2(decoder_1_out_2),
    .out_3(decoder_1_out_3));
  LED ADD (.in(decoder_1_out_0));
  LED SUB (.in(decoder_1_out_1));
  LED INC (.in(decoder_1_out_2));
  LED DEC (.in(decoder_1_out_3));
  and and_6 (and_6_out, MEM_LD_XDATA, CLOCK);
  and and_7 (and_7_out, CS0, MEM_OUT_XDATA);
  Seven_Seg_Hex seven_seg_hex_23 (.d(lt_CAR_gt[3:0]), .dp(1'b0));
  Seven_Seg_Hex seven_seg_hex_24 (.d(lt_CAR_gt[7:4]), .dp(1'b0));
  RAMSinglePortSel #(.AddrBits(4), .isProgramMemory("true"), .Bits(8)) RAM (
    .A(MAR[3:0]), .CS(CS1), .WE(and_6_out), .OE(MEM_OUT_XDATA), .D(XDATA));
  ROM #(.AddrBits(8), .Bits(8)) ROM (.A(MAR), .sel(and_7_out), .D(XDATA));
  Multiplexer #(.Bits(8)) multiplexer_2 (.sel(MBR_LD_CDATA), .in_0(XDATA), .in_1(CDATA), .out(multiplexer_2_out));
  Seven_Seg_Hex seven_seg_hex_25 (.d(lt_CARNEXT_gt[7:4]), .dp(1'b0));
  Register #(.Bits(8)) u_MBR (.D(multiplexer_2_out), .C(CLOCK), .en(or_6_out), .Q(MBR));
  or or_6 (or_6_out, MBR_LD_CDATA, MBR_LD_XDATA);
  Seven_Seg_Hex seven_seg_hex_26 (.d(lt_CARNEXT_gt[3:0]), .dp(1'b0));
  Seven_Seg_Hex seven_seg_hex_27 (.d(lt_UPARAM_gt[7:4]), .dp(1'b0));
  assign XDATA = MBR_OUT_XDATA ? MBR : 8'bz;  // Driver driver_2
  assign CDATA = MBR_OUT_CDATA ? MBR : 8'bz;  // Driver driver_3
  Seven_Seg_Hex seven_seg_hex_28 (.d(lt_UPARAM_gt[3:0]), .dp(1'b0));
  Comparator #(.Bits(8)) comparator_4 (.a(MAR), .b(8'hf0), .eq(comparator_4_eq));  // open: gt, lt
  Decoder #(.Selector_Bits(3)) decoder_2 (
    .sel(lt_CARNEXTSRC_gt), .out_0(decoder_2_out_0), .out_1(decoder_2_out_1), .out_2(decoder_2_out_2),
    .out_3(decoder_2_out_3), .out_4(decoder_2_out_4), .out_5(decoder_2_out_5), .out_6(decoder_2_out_6),
    .out_7(decoder_2_out_7));
  Seven_Seg_Hex seven_seg_hex_29 (.d(register_1_q_2), .dp(1'b0));
  LED plus_1 (.in(decoder_2_out_0));
  LED p0 (.in(decoder_2_out_1));
  LED p1 (.in(decoder_2_out_2));
  LED p2 (.in(decoder_2_out_3));
  LED uJMPs (.in(decoder_2_out_4));
  LED N_A (.in(decoder_2_out_5));
  LED N_A_2 (.in(decoder_2_out_6));
  LED N_A_3 (.in(decoder_2_out_7));
  Seven_Seg_Hex seven_seg_hex_30 (.d(register_1_q), .dp(1'b0));
  Register #(.Bits(8)) register_1 (.D(XDATA), .C(CLOCK), .en(and_8_out), .Q({register_1_q_2, register_1_q}));
  and and_8 (and_8_out, comparator_4_eq, CS2);
  Comparator #(.Bits(8)) comparator_5 (.a(MAR), .b(8'hf1), .eq(comparator_5_eq));  // open: gt, lt
  ALU alu_1 (
    .D(CDATA), .OP({ALUOP_1, ALUOP_0}), .LDA(ALUA_LD_CDATA), .LDB(ALUB_LD_CDATA), .CLOCK(CLOCK), .Q(ALUR),
    .ZOUT(ALUZ_OUT), .lt_ALUA_gt(lt_ALUA_gt), .lt_ALUB_gt(lt_ALUB_gt));
  Seven_Seg_Hex seven_seg_hex_31 (.d(register_2_q), .dp(1'b0));
  Seven_Seg_Hex seven_seg_hex_32 (.d(register_2_q_2), .dp(1'b0));
  and and_9 (and_9_out, comparator_5_eq, CS2);
  Register #(.Bits(8)) u_IR (.D(XDATA), .C(CLOCK), .en(IR_LD_XDATA), .Q(IR));
  Register #(.Bits(8)) register_2 (.D(XDATA), .C(CLOCK), .en(and_9_out), .Q({register_2_q_2, register_2_q}));
  LED led_3 (.in(HALTED));
  LED led_4 (.in(ERROR));
  LED led_5 (.in(BREAK));
  assign CDATA = ALUR_OUT_CDATA ? ALUR : 8'bz;  // Driver driver_4
  PC u_PC (.LD(PC_LD_CDATA), .INC(PC_INC), .REL(PC_REL_CDATA), .D(CDATA), .C(CLOCK));  // open: Q
  Register u_A (.C(CLOCK), .D(CDATA), .OUT(A_OUT_CDATA), .LD(A_LD_CDATA));  // open: Q, lt_Q_gt
  Seven_Seg_Hex seven_seg_hex_33 (.d(MCBREAKPOINT[3:0]), .dp(1'b0));
  Seven_Seg_Hex seven_seg_hex_34 (.d(MCBREAKPOINT[7:4]), .dp(1'b0));
  Seven_Seg_Hex seven_seg_hex_35 (.d(UCBREAKPOINT[3:0]), .dp(1'b0));
  Seven_Seg_Hex seven_seg_hex_36 (.d(UCBREAKPOINT[7:4]), .dp(1'b0));
  assign CADDR = PC_OUT_CADDR ? PC : 8'bz;  // Driver driver_5
  assign CDATA = PC_OUT_CDATA ? PC : 8'bz;  // Driver driver_6
  Register u_X (.C(CLOCK), .D(CDATA), .OUT(X_OUT_CDATA), .LD(X_LD_CDATA));  // open: Q, lt_Q_gt
  assign CDATA = CDATA_LD_0 ? {8{1'b0}} : 8'bz;  // Driver driver_7

  // Other names for the same wires on the sheet: XADDR[7:0] = MAR

  // Notes on the sheet:
  //   MCBREAKPOINT: default 65535
  //   UCBREAKPOINT: default 65535
  //   FAST: Hz: 500
  //   SLOW: Hz: 50
  //   Clock
  //   Breakpoints
  //   Error Conditions
  //   CPU
  //   MAR
  //   A
  //   X
  //   MBR
  //   PC
  //   P
  //   Z
  //   IR
  //   ROM/RAM Interfacing
  //   XADDR Bus
  //   CADDR Bus
  //   Bank Selection
  //   Instruction Decoder
  //   (p1) MODEADDR
  //   ALU
  //   ALUA
  //   ALUB
  //   ALUOUT
  //   (p2) OPCODEADDR
  //   ROM/RAM Banks
  //   OP
  //   XDATA Bus
  //   CDATA Bus
  //   Control Unit
  //   CAR
  //   contents of ROM (hex, n*v repeats v):
  //   a9,42,16379*0,2
  //   CARNEXT
  //   UPARAM
  //   ALU operation
  //   0 0 ADD
  //   0 1 SUB
  //   1 0 INC
  //   1 1 DEC
  //   CARNEXTSRC
  //   POST1
  //   POST0
  //   HALTED
  //   ERROR
  //   BREAKPOINT
  //   General Purpose Registers
  //   MC Breakpoint
  //   UC Breakpoint
  //   PC - In/out CDATA out CADDR
  //   Used for initialisation/reset
endmodule
