// Digital circuit Control Unit.dig as structural Verilog
module Control_Unit (
  input  [7:0] MODEADDR,
  input  [7:0] OPCODEADDR,
  input  Z,
  input  RESET,
  input  CLOCK,
  output CDATA_LD_0,
  output CDATA_TO_CADDR,
  output MEM_LD_XDATA,
  output MEM_OUT_XDATA,
  output IR_LD_XDATA,
  output MBR_LD_XDATA,
  output MBR_OUT_XDATA,
  output MBR_LD_CDATA,
  output MBR_OUT_CDATA,
  output MAR_LD_CADDR,
  output PC_INC,
  output PC_REL_CDATA,
  output PC_LD_CDATA,
  output PCL_OUT_CDATA,
  output PC_OUT_CADDR,
  output A_LD_CDATA,
  output A_OUT_CDATA,
  output X_LD_CDATA,
  output X_OUT_CDATA,
  output PZ_LD,
  output ALUA_LD_CDATA,
  output ALUB_LD_CDATA,
  output ALUR_OUT_CDATA,
  output ALUOP_0,
  output ALUOP_1,
  output Z_SRC_CDATA,
  output CPU_ERR,
  output [7:0] lt_CAR_gt,
  output [7:0] lt_UPARAM_gt,
  output [7:0] lt_CARNEXT_gt,
  output [2:0] lt_CARNEXTSRC_gt
);

  wire and_1_out, decoder_1_out_0, decoder_1_out_1, decoder_1_out_2, decoder_1_out_3, decoder_1_out_4,
       decoder_1_out_5, decoder_1_out_6, decoder_1_out_7, uJMP, uJMPINV, uP0, uP1, uP2, uZJMP, xor_1_out;
  wire [7:0] CAR_Adder_s, p0__Fetch_q;

  Seven_Seg_Hex seven_seg_hex_1 (.d(lt_CAR_gt[7:4]), .dp(1'b0));
  Seven_Seg_Hex seven_seg_hex_2 (.d(lt_CAR_gt[3:0]), .dp(1'b0));
  Seven_Seg_Hex seven_seg_hex_3 (.d(lt_CARNEXT_gt[3:0]), .dp(1'b0));
  Seven_Seg_Hex seven_seg_hex_4 (.d(lt_CARNEXT_gt[7:4]), .dp(1'b0));
  Seven_Seg_Hex seven_seg_hex_5 (.d(lt_UPARAM_gt[3:0]), .dp(1'b0));
  Seven_Seg_Hex seven_seg_hex_6 (.d(lt_UPARAM_gt[7:4]), .dp(1'b0));
  Decoder #(.Selector_Bits(3)) decoder_1 (
    .sel(lt_CARNEXTSRC_gt), .out_0(decoder_1_out_0), .out_1(decoder_1_out_1), .out_2(decoder_1_out_2),
    .out_3(decoder_1_out_3), .out_4(decoder_1_out_4), .out_5(decoder_1_out_5), .out_6(decoder_1_out_6),
    .out_7(decoder_1_out_7));
  LED plus_1 (.in(decoder_1_out_0));
  LED p0 (.in(decoder_1_out_1));
  LED p1 (.in(decoder_1_out_2));
  LED p2 (.in(decoder_1_out_3));
  LED uJMPs (.in(decoder_1_out_4));
  LED N_A (.in(decoder_1_out_5));
  LED N_A_2 (.in(decoder_1_out_6));
  LED N_A_3 (.in(decoder_1_out_7));
  Comparator #(.Bits(8)) Error_Detection (.a(lt_CAR_gt), .b({8{1'b1}}), .eq(CPU_ERR));  // open: gt, lt
  ROM #(.AddrBits(8), .Bits(8)) uCode0 (.A(lt_CAR_gt), .sel(1'b1), .D(lt_UPARAM_gt));
  ROM #(.AddrBits(8), .Bits(8)) uCode1 (
    .A(lt_CAR_gt), .sel(1'b1),
    .D({MBR_LD_CDATA, MBR_OUT_XDATA, MBR_LD_XDATA, IR_LD_XDATA, MEM_OUT_XDATA, MEM_LD_XDATA, CDATA_TO_CADDR, CDATA_LD_0}));
  ROM #(.AddrBits(8), .Bits(8)) uCode2 (
    .A(lt_CAR_gt), .sel(1'b1),
    .D({A_LD_CDATA, PC_OUT_CADDR, PCL_OUT_CDATA, PC_LD_CDATA, PC_REL_CDATA, PC_INC, MAR_LD_CADDR, MBR_OUT_CDATA}));
  ROM #(.AddrBits(8), .Bits(8)) uCode3 (
    .A(lt_CAR_gt), .sel(1'b1),
    .D({ALUOP_0, ALUR_OUT_CDATA, ALUB_LD_CDATA, ALUA_LD_CDATA, PZ_LD, X_OUT_CDATA, X_LD_CDATA, A_OUT_CDATA}));
  ROM #(.AddrBits(8), .Bits(8)) uCode4 (
    .A(lt_CAR_gt), .sel(1'b1), .D({uZJMP, uP2, uP1, uP0, uJMPINV, uJMP, Z_SRC_CDATA, ALUOP_1}));
  Register #(.Bits(8)) CAR (.D(lt_CARNEXT_gt), .C(CLOCK), .en(1'b1), .Q(lt_CAR_gt));
  Add #(.Bits(8)) CAR_Adder (.a(lt_CAR_gt), .b(8'h1), .c_i(1'b0), .s(CAR_Adder_s));  // open: c_o
  or or_1 (lt_CARNEXTSRC_gt[2], uJMP, and_1_out);
  and and_1 (and_1_out, uZJMP, xor_1_out);
  Register #(.Bits(8)) p0__Fetch (.D(lt_UPARAM_gt), .C(CLOCK), .en(1'b0), .Q(p0__Fetch_q));
  xor xor_1 (xor_1_out, Z, uJMPINV);
  or or_2 (lt_CARNEXTSRC_gt[1], uP1, uP2);
  Multiplexer #(.Selector_Bits(3), .Bits(8)) multiplexer_1 (
    .sel(lt_CARNEXTSRC_gt), .in_0(CAR_Adder_s), .in_1(p0__Fetch_q), .in_2(MODEADDR), .in_3(OPCODEADDR),
    .in_4(lt_UPARAM_gt), .in_5({8{1'b0}}), .in_6({8{1'b0}}), .in_7({8{1'b0}}), .out(lt_CARNEXT_gt));
  or or_3 (lt_CARNEXTSRC_gt[0], uP0, uP2);

  // Other names for the same wires on the sheet: PC_OUT_CDATA = PCL_OUT_CDATA; CARNEXTSRC[2:0] = lt_CARNEXTSRC_gt;
  //   CDATA_TO_CADDRL = CDATA_TO_CADDR; CAR[7:0] = lt_CAR_gt; CARNEXT[7:0] = lt_CARNEXT_gt;
  //   UPARAM[7:0] = lt_UPARAM_gt

  // Notes on the sheet:
  //   MODEADDR: default 169
  //   OPCODEADDR: default 169
  //   CAR
  //   CARNEXT
  //   UPARAM
  //   CARNEXTSRC
  //   Debug
  //   !!!!!!!!!!!!
  //   contents of uCode0 (hex, n*v repeats v):
  //   6000000,18000000,6000000,30000000,c0000000
  //   contents of uCode1 (hex, n*v repeats v):
  //   6000000,18000000,6000000,30000000,c0000000
  //   contents of uCode2 (hex, n*v repeats v):
  //   6000000,18000000,6000000,30000000,c0000000
  //   contents of uCode3 (hex, n*v repeats v):
  //   6000000,18000000,6000000,30000000,c0000000
  //   contents of uCode4 (hex, n*v repeats v):
  //   6000000,18000000,6000000,30000000,c0000000
  //   Next Mux
  //   0 0 0 +1
  //   0 0 1 p0
  //   0 1 0 p1
  //   0 1 1 p2
  //   1 0 0 uJMPs
  //   1 0 1 N/A
  //   1 1 x N/A
endmodule
