// Digital circuit Instruction Decoder.dig as structural Verilog
module Instruction_Decoder (
  input  [7:0] OPCODE,
  output [15:0] MODEADDR,
  output [15:0] OPCODEADDR
);

  ROM #(.AddrBits(8), .Bits(8)) p1__Mode (.A(OPCODE), .sel(1'b1), .D(MODEADDR[7:0]));
  ROM #(.AddrBits(8), .Bits(8)) p2__OpCode (.A(OPCODE), .sel(1'b1), .D(OPCODEADDR[7:0]));
  // Pins of 8 and 16 bits meet at MODEADDR
  // Pins of 8 and 16 bits meet at OPCODEADDR

  // Notes on the sheet:
  //   contents of p1__Mode (hex, n*v repeats v):
  //   6000000,18000000,6000000,30000000,c0000000
  //   contents of p2__OpCode (hex, n*v repeats v):
  //   6000000,18000000,6000000,30000000,c0000000
endmodule
